// Logisim project rapidroll.circ as structural Verilog: 12 circuits, main circuit MallaPersonaje
// per
module MallaPersonaje (
  input  [1:0] in_1,
  input  in_2,
  input  in_3,
  input  in_4,
  input  in_5,
  output [31:0] c1,
  output [31:0] c2,
  output [31:0] c3,
  output [31:0] c4,
  output [31:0] c5,
  output [31:0] c6,
  output [31:0] c7,
  output [31:0] c8,
  output [31:0] c9,
  output [31:0] c10,
  output [31:0] c11,
  output [31:0] c12,
  output [31:0] c13,
  output [31:0] c14,
  output [31:0] c15,
  output [31:0] c16,
  output [3:0] out_22
);

  wire clk, clock_1_out, pixelpersonaje_2_sar, pixelpersonaje_3_sar, pixelpersonaje_4_sar,
       pixelpersonaje_5_sar, pixelpersonaje_6_sar, pixelpersonaje_7_sar, pixelpersonaje_8_sar,
       pixelpersonaje_9_sar, pixelpersonaje_10_sar, pixelpersonaje_11_sar, pixelpersonaje_12_sar,
       pixelpersonaje_13_sar, pixelpersonaje_14_sar, pixelpersonaje_15_sar, pixelpersonaje_16_sar,
       pixelpersonaje_17_sar, pixelpersonaje_18_sar, pixelpersonaje_19_sar, pixelpersonaje_20_sar,
       pixelpersonaje_21_sar, pixelpersonaje_22_sar, pixelpersonaje_23_sar, pixelpersonaje_24_sar,
       pixelpersonaje_25_sar, pixelpersonaje_26_sar, pixelpersonaje_27_sar, pixelpersonaje_28_sar,
       pixelpersonaje_29_sar, pixelpersonaje_30_sar, pixelpersonaje_31_sar, pixelpersonaje_32_sar,
       pixelpersonaje_33_siz, pixelpersonaje_34_sar, pixelpersonaje_34_siz, pixelpersonaje_35_sar,
       pixelpersonaje_35_siz, pixelpersonaje_36_sar, pixelpersonaje_36_siz, pixelpersonaje_37_sar,
       pixelpersonaje_37_siz, pixelpersonaje_38_sar, pixelpersonaje_38_siz, pixelpersonaje_39_sar,
       pixelpersonaje_39_siz, pixelpersonaje_40_sar, pixelpersonaje_40_siz, pixelpersonaje_41_sar,
       pixelpersonaje_41_siz, pixelpersonaje_42_sar, pixelpersonaje_42_siz, pixelpersonaje_43_sar,
       pixelpersonaje_43_siz, pixelpersonaje_44_sar, pixelpersonaje_44_siz, pixelpersonaje_45_sar,
       pixelpersonaje_45_siz, pixelpersonaje_46_sar, pixelpersonaje_46_siz, pixelpersonaje_47_sar,
       pixelpersonaje_47_siz, pixelpersonaje_48_sar, pixelpersonaje_48_siz, pixelpersonaje_49_sar,
       pixelpersonaje_49_siz, pixelpersonaje_50_sar, pixelpersonaje_50_siz, pixelpersonaje_51_sar,
       pixelpersonaje_51_siz, pixelpersonaje_52_sar, pixelpersonaje_52_siz, pixelpersonaje_53_sar,
       pixelpersonaje_53_siz, pixelpersonaje_54_sar, pixelpersonaje_54_siz, pixelpersonaje_55_sar,
       pixelpersonaje_55_siz, pixelpersonaje_56_sar, pixelpersonaje_56_siz, pixelpersonaje_57_sar,
       pixelpersonaje_57_siz, pixelpersonaje_58_sar, pixelpersonaje_58_siz, pixelpersonaje_59_sar,
       pixelpersonaje_59_siz, pixelpersonaje_60_sar, pixelpersonaje_60_siz, pixelpersonaje_61_sar,
       pixelpersonaje_61_siz, pixelpersonaje_62_sar, pixelpersonaje_62_siz, pixelpersonaje_63_sar,
       pixelpersonaje_63_siz, pixelpersonaje_64_sar, pixelpersonaje_64_siz, pixelpersonaje_65_siz,
       pixelpersonaje_66_sar, pixelpersonaje_66_siz, pixelpersonaje_67_sar, pixelpersonaje_67_siz,
       pixelpersonaje_68_sar, pixelpersonaje_68_siz, pixelpersonaje_69_sar, pixelpersonaje_69_siz,
       pixelpersonaje_70_sar, pixelpersonaje_70_siz, pixelpersonaje_71_sar, pixelpersonaje_71_siz,
       pixelpersonaje_72_sar, pixelpersonaje_72_siz, pixelpersonaje_73_sar, pixelpersonaje_73_siz,
       pixelpersonaje_74_sar, pixelpersonaje_74_siz, pixelpersonaje_75_sar, pixelpersonaje_75_siz,
       pixelpersonaje_76_sar, pixelpersonaje_76_siz, pixelpersonaje_77_sar, pixelpersonaje_77_siz,
       pixelpersonaje_78_sar, pixelpersonaje_78_siz, pixelpersonaje_79_sar, pixelpersonaje_79_siz,
       pixelpersonaje_80_sar, pixelpersonaje_80_siz, pixelpersonaje_81_sar, pixelpersonaje_81_siz,
       pixelpersonaje_82_sar, pixelpersonaje_82_siz, pixelpersonaje_83_sar, pixelpersonaje_83_siz,
       pixelpersonaje_84_sar, pixelpersonaje_84_siz, pixelpersonaje_85_sar, pixelpersonaje_85_siz,
       pixelpersonaje_86_sar, pixelpersonaje_86_siz, pixelpersonaje_87_sar, pixelpersonaje_87_siz,
       pixelpersonaje_88_sar, pixelpersonaje_88_siz, pixelpersonaje_89_sar, pixelpersonaje_89_siz,
       pixelpersonaje_90_sar, pixelpersonaje_90_siz, pixelpersonaje_91_sar, pixelpersonaje_91_siz,
       pixelpersonaje_92_sar, pixelpersonaje_92_siz, pixelpersonaje_93_sar, pixelpersonaje_93_siz,
       pixelpersonaje_94_sar, pixelpersonaje_94_siz, pixelpersonaje_95_sar, pixelpersonaje_95_siz,
       pixelpersonaje_96_sar, pixelpersonaje_96_siz, pixelpersonaje_97_siz, pixelpersonaje_98_sar,
       pixelpersonaje_98_siz, pixelpersonaje_99_sar, pixelpersonaje_99_siz, pixelpersonaje_100_sar,
       pixelpersonaje_100_siz, pixelpersonaje_101_sar, pixelpersonaje_101_siz, pixelpersonaje_102_sar,
       pixelpersonaje_102_siz, pixelpersonaje_103_sar, pixelpersonaje_103_siz, pixelpersonaje_104_sar,
       pixelpersonaje_104_siz, pixelpersonaje_105_sar, pixelpersonaje_105_siz, pixelpersonaje_106_sar,
       pixelpersonaje_106_siz, pixelpersonaje_107_sar, pixelpersonaje_107_siz, pixelpersonaje_108_sar,
       pixelpersonaje_108_siz, pixelpersonaje_109_sar, pixelpersonaje_109_siz, pixelpersonaje_110_sar,
       pixelpersonaje_110_siz, pixelpersonaje_111_sar, pixelpersonaje_111_siz, pixelpersonaje_112_sar,
       pixelpersonaje_112_siz, pixelpersonaje_113_sar, pixelpersonaje_113_siz, pixelpersonaje_114_sar,
       pixelpersonaje_114_siz, pixelpersonaje_115_sar, pixelpersonaje_115_siz, pixelpersonaje_116_sar,
       pixelpersonaje_116_siz, pixelpersonaje_117_sar, pixelpersonaje_117_siz, pixelpersonaje_118_sar,
       pixelpersonaje_118_siz, pixelpersonaje_119_sar, pixelpersonaje_119_siz, pixelpersonaje_120_sar,
       pixelpersonaje_120_siz, pixelpersonaje_121_sar, pixelpersonaje_121_siz, pixelpersonaje_122_sar,
       pixelpersonaje_122_siz, pixelpersonaje_123_sar, pixelpersonaje_123_siz, pixelpersonaje_124_sar,
       pixelpersonaje_124_siz, pixelpersonaje_125_sar, pixelpersonaje_125_siz, pixelpersonaje_126_sar,
       pixelpersonaje_126_siz, pixelpersonaje_127_sar, pixelpersonaje_127_siz, pixelpersonaje_128_sar,
       pixelpersonaje_128_siz, pixelpersonaje_129_siz, pixelpersonaje_130_sar, pixelpersonaje_130_siz,
       pixelpersonaje_131_sar, pixelpersonaje_131_siz, pixelpersonaje_132_sar, pixelpersonaje_132_siz,
       pixelpersonaje_133_sar, pixelpersonaje_133_siz, pixelpersonaje_134_sar, pixelpersonaje_134_siz,
       pixelpersonaje_135_sar, pixelpersonaje_135_siz, pixelpersonaje_136_sar, pixelpersonaje_136_siz,
       pixelpersonaje_137_sar, pixelpersonaje_137_siz, pixelpersonaje_138_sar, pixelpersonaje_138_siz,
       pixelpersonaje_139_sar, pixelpersonaje_139_siz, pixelpersonaje_140_sar, pixelpersonaje_140_siz,
       pixelpersonaje_141_sar, pixelpersonaje_141_siz, pixelpersonaje_142_sar, pixelpersonaje_142_siz,
       pixelpersonaje_143_sar, pixelpersonaje_143_siz, pixelpersonaje_144_sar, pixelpersonaje_144_siz,
       pixelpersonaje_145_sar, pixelpersonaje_145_siz, pixelpersonaje_146_sar, pixelpersonaje_146_siz,
       pixelpersonaje_147_sar, pixelpersonaje_147_siz, pixelpersonaje_148_sar, pixelpersonaje_148_siz,
       pixelpersonaje_149_sar, pixelpersonaje_149_siz, pixelpersonaje_150_sar, pixelpersonaje_150_siz,
       pixelpersonaje_151_sar, pixelpersonaje_151_siz, pixelpersonaje_152_sar, pixelpersonaje_152_siz,
       pixelpersonaje_153_sar, pixelpersonaje_153_siz, pixelpersonaje_154_sar, pixelpersonaje_154_siz,
       pixelpersonaje_155_sar, pixelpersonaje_155_siz, pixelpersonaje_156_sar, pixelpersonaje_156_siz,
       pixelpersonaje_157_sar, pixelpersonaje_157_siz, pixelpersonaje_158_sar, pixelpersonaje_158_siz,
       pixelpersonaje_159_sar, pixelpersonaje_159_siz, pixelpersonaje_160_sar, pixelpersonaje_160_siz,
       pixelpersonaje_161_siz, pixelpersonaje_162_sar, pixelpersonaje_162_siz, pixelpersonaje_163_sar,
       pixelpersonaje_163_siz, pixelpersonaje_164_sar, pixelpersonaje_164_siz, pixelpersonaje_165_sar,
       pixelpersonaje_165_siz, pixelpersonaje_166_sar, pixelpersonaje_166_siz, pixelpersonaje_167_sar,
       pixelpersonaje_167_siz, pixelpersonaje_168_sar, pixelpersonaje_168_siz, pixelpersonaje_169_sar,
       pixelpersonaje_169_siz, pixelpersonaje_170_sar, pixelpersonaje_170_siz, pixelpersonaje_171_sar,
       pixelpersonaje_171_siz, pixelpersonaje_172_sar, pixelpersonaje_172_siz, pixelpersonaje_173_sar,
       pixelpersonaje_173_siz, pixelpersonaje_174_sar, pixelpersonaje_174_siz, pixelpersonaje_175_sar,
       pixelpersonaje_175_siz, pixelpersonaje_176_sar, pixelpersonaje_176_siz, pixelpersonaje_177_sar,
       pixelpersonaje_177_siz, pixelpersonaje_178_sar, pixelpersonaje_178_siz, pixelpersonaje_179_sar,
       pixelpersonaje_179_siz, pixelpersonaje_180_sar, pixelpersonaje_180_siz, pixelpersonaje_181_sar,
       pixelpersonaje_181_siz, pixelpersonaje_182_sar, pixelpersonaje_182_siz, pixelpersonaje_183_sar,
       pixelpersonaje_183_siz, pixelpersonaje_184_sar, pixelpersonaje_184_siz, pixelpersonaje_185_sar,
       pixelpersonaje_185_siz, pixelpersonaje_186_sar, pixelpersonaje_186_siz, pixelpersonaje_187_sar,
       pixelpersonaje_187_siz, pixelpersonaje_188_sar, pixelpersonaje_188_siz, pixelpersonaje_189_sar,
       pixelpersonaje_189_siz, pixelpersonaje_190_sar, pixelpersonaje_190_siz, pixelpersonaje_191_sar,
       pixelpersonaje_191_siz, pixelpersonaje_192_sar, pixelpersonaje_192_siz, pixelpersonaje_193_siz,
       pixelpersonaje_194_sar, pixelpersonaje_194_siz, pixelpersonaje_195_sar, pixelpersonaje_195_siz,
       pixelpersonaje_196_sar, pixelpersonaje_196_siz, pixelpersonaje_197_sar, pixelpersonaje_197_siz,
       pixelpersonaje_198_sar, pixelpersonaje_198_siz, pixelpersonaje_199_sar, pixelpersonaje_199_siz,
       pixelpersonaje_200_sar, pixelpersonaje_200_siz, pixelpersonaje_201_sar, pixelpersonaje_201_siz,
       pixelpersonaje_202_sar, pixelpersonaje_202_siz, pixelpersonaje_203_sar, pixelpersonaje_203_siz,
       pixelpersonaje_204_sar, pixelpersonaje_204_siz, pixelpersonaje_205_sar, pixelpersonaje_205_siz,
       pixelpersonaje_206_sar, pixelpersonaje_206_siz, pixelpersonaje_207_sar, pixelpersonaje_207_siz,
       pixelpersonaje_208_sar, pixelpersonaje_208_siz, pixelpersonaje_209_sar, pixelpersonaje_209_siz,
       pixelpersonaje_210_sar, pixelpersonaje_210_siz, pixelpersonaje_211_sar, pixelpersonaje_211_siz,
       pixelpersonaje_212_sar, pixelpersonaje_212_siz, pixelpersonaje_213_sar, pixelpersonaje_213_siz,
       pixelpersonaje_214_sar, pixelpersonaje_214_siz, pixelpersonaje_215_sar, pixelpersonaje_215_siz,
       pixelpersonaje_216_sar, pixelpersonaje_216_siz, pixelpersonaje_217_sar, pixelpersonaje_217_siz,
       pixelpersonaje_218_sar, pixelpersonaje_218_siz, pixelpersonaje_219_sar, pixelpersonaje_219_siz,
       pixelpersonaje_220_sar, pixelpersonaje_220_siz, pixelpersonaje_221_sar, pixelpersonaje_221_siz,
       pixelpersonaje_222_sar, pixelpersonaje_222_siz, pixelpersonaje_223_sar, pixelpersonaje_223_siz,
       pixelpersonaje_224_sar, pixelpersonaje_224_siz, pixelpersonaje_225_siz, pixelpersonaje_226_sar,
       pixelpersonaje_226_siz, pixelpersonaje_227_sar, pixelpersonaje_227_siz, pixelpersonaje_228_sar,
       pixelpersonaje_228_siz, pixelpersonaje_229_sar, pixelpersonaje_229_siz, pixelpersonaje_230_sar,
       pixelpersonaje_230_siz, pixelpersonaje_231_sar, pixelpersonaje_231_siz, pixelpersonaje_232_sar,
       pixelpersonaje_232_siz, pixelpersonaje_233_sar, pixelpersonaje_233_siz, pixelpersonaje_234_sar,
       pixelpersonaje_234_siz, pixelpersonaje_235_sar, pixelpersonaje_235_siz, pixelpersonaje_236_sar,
       pixelpersonaje_236_siz, pixelpersonaje_237_sar, pixelpersonaje_237_siz, pixelpersonaje_238_sar,
       pixelpersonaje_238_siz, pixelpersonaje_239_sar, pixelpersonaje_239_siz, pixelpersonaje_240_sar,
       pixelpersonaje_240_siz, pixelpersonaje_241_sar, pixelpersonaje_241_siz, pixelpersonaje_242_sar,
       pixelpersonaje_242_siz, pixelpersonaje_243_sar, pixelpersonaje_243_siz, pixelpersonaje_244_sar,
       pixelpersonaje_244_siz, pixelpersonaje_245_sar, pixelpersonaje_245_siz, pixelpersonaje_246_sar,
       pixelpersonaje_246_siz, pixelpersonaje_247_sar, pixelpersonaje_247_siz, pixelpersonaje_248_sar,
       pixelpersonaje_248_siz, pixelpersonaje_249_sar, pixelpersonaje_249_siz, pixelpersonaje_250_sar,
       pixelpersonaje_250_siz, pixelpersonaje_251_sar, pixelpersonaje_251_siz, pixelpersonaje_252_sar,
       pixelpersonaje_252_siz, pixelpersonaje_253_sar, pixelpersonaje_253_siz, pixelpersonaje_254_sar,
       pixelpersonaje_254_siz, pixelpersonaje_255_sar, pixelpersonaje_255_siz, pixelpersonaje_256_sar,
       pixelpersonaje_256_siz, pixelpersonaje_257_siz, pixelpersonaje_258_sar, pixelpersonaje_258_siz,
       pixelpersonaje_259_sar, pixelpersonaje_259_siz, pixelpersonaje_260_sar, pixelpersonaje_260_siz,
       pixelpersonaje_261_sar, pixelpersonaje_261_siz, pixelpersonaje_262_sar, pixelpersonaje_262_siz,
       pixelpersonaje_263_sar, pixelpersonaje_263_siz, pixelpersonaje_264_sar, pixelpersonaje_264_siz,
       pixelpersonaje_265_sar, pixelpersonaje_265_siz, pixelpersonaje_266_sar, pixelpersonaje_266_siz,
       pixelpersonaje_267_sar, pixelpersonaje_267_siz, pixelpersonaje_268_sar, pixelpersonaje_268_siz,
       pixelpersonaje_269_sar, pixelpersonaje_269_siz, pixelpersonaje_270_sar, pixelpersonaje_270_siz,
       pixelpersonaje_271_sar, pixelpersonaje_271_siz, pixelpersonaje_272_sar, pixelpersonaje_272_siz,
       pixelpersonaje_273_sar, pixelpersonaje_273_siz, pixelpersonaje_274_sar, pixelpersonaje_274_siz,
       pixelpersonaje_275_sar, pixelpersonaje_275_siz, pixelpersonaje_276_sar, pixelpersonaje_276_siz,
       pixelpersonaje_277_sar, pixelpersonaje_277_siz, pixelpersonaje_278_sar, pixelpersonaje_278_siz,
       pixelpersonaje_279_sar, pixelpersonaje_279_siz, pixelpersonaje_280_sar, pixelpersonaje_280_siz,
       pixelpersonaje_281_sar, pixelpersonaje_281_siz, pixelpersonaje_282_sar, pixelpersonaje_282_siz,
       pixelpersonaje_283_sar, pixelpersonaje_283_siz, pixelpersonaje_284_sar, pixelpersonaje_284_siz,
       pixelpersonaje_285_sar, pixelpersonaje_285_siz, pixelpersonaje_286_sar, pixelpersonaje_286_siz,
       pixelpersonaje_287_sar, pixelpersonaje_287_siz, pixelpersonaje_288_sar, pixelpersonaje_288_siz,
       pixelpersonaje_289_siz, pixelpersonaje_290_sar, pixelpersonaje_290_siz, pixelpersonaje_291_sar,
       pixelpersonaje_291_siz, pixelpersonaje_292_sar, pixelpersonaje_292_siz, pixelpersonaje_293_sar,
       pixelpersonaje_293_siz, pixelpersonaje_294_sar, pixelpersonaje_294_siz, pixelpersonaje_295_sar,
       pixelpersonaje_295_siz, pixelpersonaje_296_sar, pixelpersonaje_296_siz, pixelpersonaje_297_sar,
       pixelpersonaje_297_siz, pixelpersonaje_298_sar, pixelpersonaje_298_siz, pixelpersonaje_299_sar,
       pixelpersonaje_299_siz, pixelpersonaje_300_sar, pixelpersonaje_300_siz, pixelpersonaje_301_sar,
       pixelpersonaje_301_siz, pixelpersonaje_302_sar, pixelpersonaje_302_siz, pixelpersonaje_303_sar,
       pixelpersonaje_303_siz, pixelpersonaje_304_sar, pixelpersonaje_304_siz, pixelpersonaje_305_sar,
       pixelpersonaje_305_siz, pixelpersonaje_306_sar, pixelpersonaje_306_siz, pixelpersonaje_307_sar,
       pixelpersonaje_307_siz, pixelpersonaje_308_sar, pixelpersonaje_308_siz, pixelpersonaje_309_sar,
       pixelpersonaje_309_siz, pixelpersonaje_310_sar, pixelpersonaje_310_siz, pixelpersonaje_311_sar,
       pixelpersonaje_311_siz, pixelpersonaje_312_sar, pixelpersonaje_312_siz, pixelpersonaje_313_sar,
       pixelpersonaje_313_siz, pixelpersonaje_314_sar, pixelpersonaje_314_siz, pixelpersonaje_315_sar,
       pixelpersonaje_315_siz, pixelpersonaje_316_sar, pixelpersonaje_316_siz, pixelpersonaje_317_sar,
       pixelpersonaje_317_siz, pixelpersonaje_318_sar, pixelpersonaje_318_siz, pixelpersonaje_319_sar,
       pixelpersonaje_319_siz, pixelpersonaje_320_sar, pixelpersonaje_320_siz, pixelpersonaje_321_siz,
       pixelpersonaje_322_sar, pixelpersonaje_322_siz, pixelpersonaje_323_sar, pixelpersonaje_323_siz,
       pixelpersonaje_324_sar, pixelpersonaje_324_siz, pixelpersonaje_325_sar, pixelpersonaje_325_siz,
       pixelpersonaje_326_sar, pixelpersonaje_326_siz, pixelpersonaje_327_sar, pixelpersonaje_327_siz,
       pixelpersonaje_328_sar, pixelpersonaje_328_siz, pixelpersonaje_329_sar, pixelpersonaje_329_siz,
       pixelpersonaje_330_sar, pixelpersonaje_330_siz, pixelpersonaje_331_sar, pixelpersonaje_331_siz,
       pixelpersonaje_332_sar, pixelpersonaje_332_siz, pixelpersonaje_333_sar, pixelpersonaje_333_siz,
       pixelpersonaje_334_sar, pixelpersonaje_334_siz, pixelpersonaje_335_sar, pixelpersonaje_335_siz,
       pixelpersonaje_336_sar, pixelpersonaje_336_siz, pixelpersonaje_337_sar, pixelpersonaje_337_siz,
       pixelpersonaje_338_sar, pixelpersonaje_338_siz, pixelpersonaje_339_sar, pixelpersonaje_339_siz,
       pixelpersonaje_340_sar, pixelpersonaje_340_siz, pixelpersonaje_341_sar, pixelpersonaje_341_siz,
       pixelpersonaje_342_sar, pixelpersonaje_342_siz, pixelpersonaje_343_sar, pixelpersonaje_343_siz,
       pixelpersonaje_344_sar, pixelpersonaje_344_siz, pixelpersonaje_345_sar, pixelpersonaje_345_siz,
       pixelpersonaje_346_sar, pixelpersonaje_346_siz, pixelpersonaje_347_sar, pixelpersonaje_347_siz,
       pixelpersonaje_348_sar, pixelpersonaje_348_siz, pixelpersonaje_349_sar, pixelpersonaje_349_siz,
       pixelpersonaje_350_sar, pixelpersonaje_350_siz, pixelpersonaje_351_sar, pixelpersonaje_351_siz,
       pixelpersonaje_352_sar, pixelpersonaje_352_siz, pixelpersonaje_353_siz, pixelpersonaje_354_sar,
       pixelpersonaje_354_siz, pixelpersonaje_355_sar, pixelpersonaje_355_siz, pixelpersonaje_356_sar,
       pixelpersonaje_356_siz, pixelpersonaje_357_sar, pixelpersonaje_357_siz, pixelpersonaje_358_sar,
       pixelpersonaje_358_siz, pixelpersonaje_359_sar, pixelpersonaje_359_siz, pixelpersonaje_360_sar,
       pixelpersonaje_360_siz, pixelpersonaje_361_sar, pixelpersonaje_361_siz, pixelpersonaje_362_sar,
       pixelpersonaje_362_siz, pixelpersonaje_363_sar, pixelpersonaje_363_siz, pixelpersonaje_364_sar,
       pixelpersonaje_364_siz, pixelpersonaje_365_sar, pixelpersonaje_365_siz, pixelpersonaje_366_sar,
       pixelpersonaje_366_siz, pixelpersonaje_367_sar, pixelpersonaje_367_siz, pixelpersonaje_368_sar,
       pixelpersonaje_368_siz, pixelpersonaje_369_sar, pixelpersonaje_369_siz, pixelpersonaje_370_sar,
       pixelpersonaje_370_siz, pixelpersonaje_371_sar, pixelpersonaje_371_siz, pixelpersonaje_372_sar,
       pixelpersonaje_372_siz, pixelpersonaje_373_sar, pixelpersonaje_373_siz, pixelpersonaje_374_sar,
       pixelpersonaje_374_siz, pixelpersonaje_375_sar, pixelpersonaje_375_siz, pixelpersonaje_376_sar,
       pixelpersonaje_376_siz, pixelpersonaje_377_sar, pixelpersonaje_377_siz, pixelpersonaje_378_sar,
       pixelpersonaje_378_siz, pixelpersonaje_379_sar, pixelpersonaje_379_siz, pixelpersonaje_380_sar,
       pixelpersonaje_380_siz, pixelpersonaje_381_sar, pixelpersonaje_381_siz, pixelpersonaje_382_sar,
       pixelpersonaje_382_siz, pixelpersonaje_383_sar, pixelpersonaje_383_siz, pixelpersonaje_384_sar,
       pixelpersonaje_384_siz, pixelpersonaje_385_siz, pixelpersonaje_386_sar, pixelpersonaje_386_siz,
       pixelpersonaje_387_sar, pixelpersonaje_387_siz, pixelpersonaje_388_sar, pixelpersonaje_388_siz,
       pixelpersonaje_389_sar, pixelpersonaje_389_siz, pixelpersonaje_390_sar, pixelpersonaje_390_siz,
       pixelpersonaje_391_sar, pixelpersonaje_391_siz, pixelpersonaje_392_sar, pixelpersonaje_392_siz,
       pixelpersonaje_393_sar, pixelpersonaje_393_siz, pixelpersonaje_394_sar, pixelpersonaje_394_siz,
       pixelpersonaje_395_sar, pixelpersonaje_395_siz, pixelpersonaje_396_sar, pixelpersonaje_396_siz,
       pixelpersonaje_397_sar, pixelpersonaje_397_siz, pixelpersonaje_398_sar, pixelpersonaje_398_siz,
       pixelpersonaje_399_sar, pixelpersonaje_399_siz, pixelpersonaje_400_sar, pixelpersonaje_400_siz,
       pixelpersonaje_401_sar, pixelpersonaje_401_siz, pixelpersonaje_402_sar, pixelpersonaje_402_siz,
       pixelpersonaje_403_sar, pixelpersonaje_403_siz, pixelpersonaje_404_sar, pixelpersonaje_404_siz,
       pixelpersonaje_405_sar, pixelpersonaje_405_siz, pixelpersonaje_406_sar, pixelpersonaje_406_siz,
       pixelpersonaje_407_sar, pixelpersonaje_407_siz, pixelpersonaje_408_sar, pixelpersonaje_408_siz,
       pixelpersonaje_409_sar, pixelpersonaje_409_siz, pixelpersonaje_410_sar, pixelpersonaje_410_siz,
       pixelpersonaje_411_sar, pixelpersonaje_411_siz, pixelpersonaje_412_sar, pixelpersonaje_412_siz,
       pixelpersonaje_413_sar, pixelpersonaje_413_siz, pixelpersonaje_414_sar, pixelpersonaje_414_siz,
       pixelpersonaje_415_sar, pixelpersonaje_415_siz, pixelpersonaje_416_sar, pixelpersonaje_416_siz,
       pixelpersonaje_417_siz, pixelpersonaje_418_sar, pixelpersonaje_418_siz, pixelpersonaje_419_sar,
       pixelpersonaje_419_siz, pixelpersonaje_420_sar, pixelpersonaje_420_siz, pixelpersonaje_421_sar,
       pixelpersonaje_421_siz, pixelpersonaje_422_sar, pixelpersonaje_422_siz, pixelpersonaje_423_sar,
       pixelpersonaje_423_siz, pixelpersonaje_424_sar, pixelpersonaje_424_siz, pixelpersonaje_425_sar,
       pixelpersonaje_425_siz, pixelpersonaje_426_sar, pixelpersonaje_426_siz, pixelpersonaje_427_sar,
       pixelpersonaje_427_siz, pixelpersonaje_428_sar, pixelpersonaje_428_siz, pixelpersonaje_429_sar,
       pixelpersonaje_429_siz, pixelpersonaje_430_sar, pixelpersonaje_430_siz, pixelpersonaje_431_sar,
       pixelpersonaje_431_siz, pixelpersonaje_432_sar, pixelpersonaje_432_siz, pixelpersonaje_433_sar,
       pixelpersonaje_433_siz, pixelpersonaje_434_sar, pixelpersonaje_434_siz, pixelpersonaje_435_sar,
       pixelpersonaje_435_siz, pixelpersonaje_436_sar, pixelpersonaje_436_siz, pixelpersonaje_437_sar,
       pixelpersonaje_437_siz, pixelpersonaje_438_sar, pixelpersonaje_438_siz, pixelpersonaje_439_sar,
       pixelpersonaje_439_siz, pixelpersonaje_440_sar, pixelpersonaje_440_siz, pixelpersonaje_441_sar,
       pixelpersonaje_441_siz, pixelpersonaje_442_sar, pixelpersonaje_442_siz, pixelpersonaje_443_sar,
       pixelpersonaje_443_siz, pixelpersonaje_444_sar, pixelpersonaje_444_siz, pixelpersonaje_445_sar,
       pixelpersonaje_445_siz, pixelpersonaje_446_sar, pixelpersonaje_446_siz, pixelpersonaje_447_sar,
       pixelpersonaje_447_siz, pixelpersonaje_448_sar, pixelpersonaje_448_siz, pixelpersonaje_449_siz,
       pixelpersonaje_450_sar, pixelpersonaje_450_siz, pixelpersonaje_451_sar, pixelpersonaje_451_siz,
       pixelpersonaje_452_sar, pixelpersonaje_452_siz, pixelpersonaje_453_sar, pixelpersonaje_453_siz,
       pixelpersonaje_454_sar, pixelpersonaje_454_siz, pixelpersonaje_455_sar, pixelpersonaje_455_siz,
       pixelpersonaje_456_sar, pixelpersonaje_456_siz, pixelpersonaje_457_sar, pixelpersonaje_457_siz,
       pixelpersonaje_458_sar, pixelpersonaje_458_siz, pixelpersonaje_459_sar, pixelpersonaje_459_siz,
       pixelpersonaje_460_sar, pixelpersonaje_460_siz, pixelpersonaje_461_sar, pixelpersonaje_461_siz,
       pixelpersonaje_462_sar, pixelpersonaje_462_siz, pixelpersonaje_463_sar, pixelpersonaje_463_siz,
       pixelpersonaje_464_sar, pixelpersonaje_464_siz, pixelpersonaje_465_sar, pixelpersonaje_465_siz,
       pixelpersonaje_466_sar, pixelpersonaje_466_siz, pixelpersonaje_467_sar, pixelpersonaje_467_siz,
       pixelpersonaje_468_sar, pixelpersonaje_468_siz, pixelpersonaje_469_sar, pixelpersonaje_469_siz,
       pixelpersonaje_470_sar, pixelpersonaje_470_siz, pixelpersonaje_471_sar, pixelpersonaje_471_siz,
       pixelpersonaje_472_sar, pixelpersonaje_472_siz, pixelpersonaje_473_sar, pixelpersonaje_473_siz,
       pixelpersonaje_474_sar, pixelpersonaje_474_siz, pixelpersonaje_475_sar, pixelpersonaje_475_siz,
       pixelpersonaje_476_sar, pixelpersonaje_476_siz, pixelpersonaje_477_sar, pixelpersonaje_477_siz,
       pixelpersonaje_478_sar, pixelpersonaje_478_siz, pixelpersonaje_479_sar, pixelpersonaje_479_siz,
       pixelpersonaje_480_sar, pixelpersonaje_480_siz, pixelpersonaje_481_siz, pixelpersonaje_482_sar,
       pixelpersonaje_482_siz, pixelpersonaje_483_sar, pixelpersonaje_483_siz, pixelpersonaje_484_sar,
       pixelpersonaje_484_siz, pixelpersonaje_485_sar, pixelpersonaje_485_siz, pixelpersonaje_486_sar,
       pixelpersonaje_486_siz, pixelpersonaje_487_sar, pixelpersonaje_487_siz, pixelpersonaje_488_sar,
       pixelpersonaje_488_siz, pixelpersonaje_489_sar, pixelpersonaje_489_siz, pixelpersonaje_490_sar,
       pixelpersonaje_490_siz, pixelpersonaje_491_sar, pixelpersonaje_491_siz, pixelpersonaje_492_sar,
       pixelpersonaje_492_siz, pixelpersonaje_493_sar, pixelpersonaje_493_siz, pixelpersonaje_494_sar,
       pixelpersonaje_494_siz, pixelpersonaje_495_sar, pixelpersonaje_495_siz, pixelpersonaje_496_sar,
       pixelpersonaje_496_siz, pixelpersonaje_497_sar, pixelpersonaje_497_siz, pixelpersonaje_498_sar,
       pixelpersonaje_498_siz, pixelpersonaje_499_sar, pixelpersonaje_499_siz, pixelpersonaje_500_sar,
       pixelpersonaje_500_siz, pixelpersonaje_501_sar, pixelpersonaje_501_siz, pixelpersonaje_502_sar,
       pixelpersonaje_502_siz, pixelpersonaje_503_sar, pixelpersonaje_503_siz, pixelpersonaje_504_sar,
       pixelpersonaje_504_siz, pixelpersonaje_505_sar, pixelpersonaje_505_siz, pixelpersonaje_506_sar,
       pixelpersonaje_506_siz, pixelpersonaje_507_sar, pixelpersonaje_507_siz, pixelpersonaje_508_sar,
       pixelpersonaje_508_siz, pixelpersonaje_509_sar, pixelpersonaje_509_siz, pixelpersonaje_510_sar,
       pixelpersonaje_510_siz, pixelpersonaje_511_sar, pixelpersonaje_511_siz, pixelpersonaje_512_sar,
       pixelpersonaje_512_siz, s1, s1os2, s2, s2os3, s3, s3os4, s4, s4os5, s5os6, s6, s6os7, s7, s7os8, s8,
       s8os9, s9, s9os10, s10, s10os11, s11, s11os12, s12, s12os13, s13, s13os14, s14, s14os15, s15, s16,
       undriven;
  wire [3:0] random_2_out;

  PixelPersonaje pixelpersonaje_1 (
    .clk(clk), .abajo(pixelpersonaje_2_sar), .izq(c16[31]), .der(pixelpersonaje_33_siz), .dir(in_1),
    .sde(c1[31]), .in_7(in_2), .in_5(in_3));  // open: sar, siz, in_8
  PixelPersonaje pixelpersonaje_2 (
    .clk(clk), .abajo(pixelpersonaje_3_sar), .izq(c16[30]), .der(pixelpersonaje_34_siz), .dir(in_1),
    .sar(pixelpersonaje_2_sar), .sde(c1[30]), .in_7(in_2), .in_5(in_3));  // open: siz, in_8
  PixelPersonaje pixelpersonaje_3 (
    .clk(clk), .abajo(pixelpersonaje_4_sar), .izq(c16[29]), .der(pixelpersonaje_35_siz), .dir(in_1),
    .sar(pixelpersonaje_3_sar), .sde(c1[29]), .in_7(in_2), .in_5(in_3));  // open: siz, in_8
  PixelPersonaje pixelpersonaje_4 (
    .clk(clk), .abajo(pixelpersonaje_5_sar), .izq(c16[28]), .der(pixelpersonaje_36_siz), .dir(in_1),
    .sar(pixelpersonaje_4_sar), .sde(c1[28]), .in_7(in_2), .in_5(in_3));  // open: siz, in_8
  PixelPersonaje pixelpersonaje_5 (
    .clk(clk), .abajo(pixelpersonaje_6_sar), .izq(c16[27]), .der(pixelpersonaje_37_siz), .dir(in_1),
    .sar(pixelpersonaje_5_sar), .sde(c1[27]), .in_7(in_2), .in_5(in_3));  // open: siz, in_8
  PixelPersonaje pixelpersonaje_6 (
    .clk(clk), .abajo(pixelpersonaje_7_sar), .izq(c16[26]), .der(pixelpersonaje_38_siz), .dir(in_1),
    .sar(pixelpersonaje_6_sar), .sde(c1[26]), .in_7(in_2), .in_5(in_3));  // open: siz, in_8
  PixelPersonaje pixelpersonaje_7 (
    .clk(clk), .abajo(pixelpersonaje_8_sar), .izq(c16[25]), .der(pixelpersonaje_39_siz), .dir(in_1),
    .sar(pixelpersonaje_7_sar), .sde(c1[25]), .in_7(in_2), .in_5(in_3));  // open: siz, in_8
  PixelPersonaje pixelpersonaje_8 (
    .clk(clk), .abajo(pixelpersonaje_9_sar), .izq(c16[24]), .der(pixelpersonaje_40_siz), .dir(in_1),
    .sar(pixelpersonaje_8_sar), .sde(c1[24]), .in_7(in_2), .in_5(in_3));  // open: siz, in_8
  PixelPersonaje pixelpersonaje_9 (
    .clk(clk), .abajo(pixelpersonaje_10_sar), .izq(c16[23]), .der(pixelpersonaje_41_siz), .dir(in_1),
    .sar(pixelpersonaje_9_sar), .sde(c1[23]), .in_7(in_2), .in_5(in_3));  // open: siz, in_8
  PixelPersonaje pixelpersonaje_10 (
    .clk(clk), .abajo(pixelpersonaje_11_sar), .izq(c16[22]), .der(pixelpersonaje_42_siz), .dir(in_1),
    .sar(pixelpersonaje_10_sar), .sde(c1[22]), .in_7(in_2), .in_5(in_3));  // open: siz, in_8
  PixelPersonaje pixelpersonaje_11 (
    .clk(clk), .abajo(pixelpersonaje_12_sar), .izq(c16[21]), .der(pixelpersonaje_43_siz), .dir(in_1),
    .sar(pixelpersonaje_11_sar), .sde(c1[21]), .in_7(in_2), .in_5(in_3));  // open: siz, in_8
  PixelPersonaje pixelpersonaje_12 (
    .clk(clk), .abajo(pixelpersonaje_13_sar), .izq(c16[20]), .der(pixelpersonaje_44_siz), .dir(in_1),
    .sar(pixelpersonaje_12_sar), .sde(c1[20]), .in_7(in_2), .in_5(in_3));  // open: siz, in_8
  PixelPersonaje pixelpersonaje_13 (
    .clk(clk), .abajo(pixelpersonaje_14_sar), .izq(c16[19]), .der(pixelpersonaje_45_siz), .dir(in_1),
    .sar(pixelpersonaje_13_sar), .sde(c1[19]), .in_7(in_2), .in_5(in_3));  // open: siz, in_8
  PixelPersonaje pixelpersonaje_14 (
    .clk(clk), .abajo(pixelpersonaje_15_sar), .izq(c16[18]), .der(pixelpersonaje_46_siz), .dir(in_1),
    .sar(pixelpersonaje_14_sar), .sde(c1[18]), .in_7(in_2), .in_5(in_3));  // open: siz, in_8
  PixelPersonaje pixelpersonaje_15 (
    .clk(clk), .abajo(pixelpersonaje_16_sar), .izq(c16[17]), .der(pixelpersonaje_47_siz), .dir(in_1),
    .sar(pixelpersonaje_15_sar), .sde(c1[17]), .in_7(in_2), .in_5(in_3));  // open: siz, in_8
  PixelPersonaje pixelpersonaje_16 (
    .clk(clk), .abajo(pixelpersonaje_17_sar), .izq(c16[16]), .der(pixelpersonaje_48_siz), .dir(in_1),
    .sar(pixelpersonaje_16_sar), .sde(c1[16]), .in_7(in_2), .in_5(in_3));  // open: siz, in_8
  PixelPersonaje pixelpersonaje_17 (
    .clk(clk), .abajo(pixelpersonaje_18_sar), .izq(c16[15]), .der(pixelpersonaje_49_siz), .dir(in_1),
    .sar(pixelpersonaje_17_sar), .sde(c1[15]), .in_7(in_2), .in_5(in_3));  // open: siz, in_8
  PixelPersonaje pixelpersonaje_18 (
    .clk(clk), .abajo(pixelpersonaje_19_sar), .izq(c16[14]), .der(pixelpersonaje_50_siz), .dir(in_1),
    .sar(pixelpersonaje_18_sar), .sde(c1[14]), .in_7(in_2), .in_5(in_3));  // open: siz, in_8
  PixelPersonaje pixelpersonaje_19 (
    .clk(clk), .abajo(pixelpersonaje_20_sar), .izq(c16[13]), .der(pixelpersonaje_51_siz), .dir(in_1),
    .sar(pixelpersonaje_19_sar), .sde(c1[13]), .in_7(in_2), .in_5(in_3));  // open: siz, in_8
  PixelPersonaje pixelpersonaje_20 (
    .clk(clk), .abajo(pixelpersonaje_21_sar), .izq(c16[12]), .der(pixelpersonaje_52_siz), .dir(in_1),
    .sar(pixelpersonaje_20_sar), .sde(c1[12]), .in_7(in_2), .in_5(in_3));  // open: siz, in_8
  PixelPersonaje pixelpersonaje_21 (
    .clk(clk), .abajo(pixelpersonaje_22_sar), .izq(c16[11]), .der(pixelpersonaje_53_siz), .dir(in_1),
    .sar(pixelpersonaje_21_sar), .sde(c1[11]), .in_7(in_2), .in_5(in_3));  // open: siz, in_8
  PixelPersonaje pixelpersonaje_22 (
    .clk(clk), .abajo(pixelpersonaje_23_sar), .izq(c16[10]), .der(pixelpersonaje_54_siz), .dir(in_1),
    .sar(pixelpersonaje_22_sar), .sde(c1[10]), .in_7(in_2), .in_5(in_3));  // open: siz, in_8
  PixelPersonaje pixelpersonaje_23 (
    .clk(clk), .abajo(pixelpersonaje_24_sar), .izq(c16[9]), .der(pixelpersonaje_55_siz), .dir(in_1),
    .sar(pixelpersonaje_23_sar), .sde(c1[9]), .in_7(in_2), .in_5(in_3));  // open: siz, in_8
  PixelPersonaje pixelpersonaje_24 (
    .clk(clk), .abajo(pixelpersonaje_25_sar), .izq(c16[8]), .der(pixelpersonaje_56_siz), .dir(in_1),
    .sar(pixelpersonaje_24_sar), .sde(c1[8]), .in_7(in_2), .in_5(in_3));  // open: siz, in_8
  PixelPersonaje pixelpersonaje_25 (
    .clk(clk), .abajo(pixelpersonaje_26_sar), .izq(c16[7]), .der(pixelpersonaje_57_siz), .dir(in_1),
    .sar(pixelpersonaje_25_sar), .sde(c1[7]), .in_7(in_2), .in_5(in_3));  // open: siz, in_8
  PixelPersonaje pixelpersonaje_26 (
    .clk(clk), .abajo(pixelpersonaje_27_sar), .izq(c16[6]), .der(pixelpersonaje_58_siz), .dir(in_1),
    .sar(pixelpersonaje_26_sar), .sde(c1[6]), .in_7(in_2), .in_5(in_3));  // open: siz, in_8
  PixelPersonaje pixelpersonaje_27 (
    .clk(clk), .abajo(pixelpersonaje_28_sar), .izq(c16[5]), .der(pixelpersonaje_59_siz), .dir(in_1),
    .sar(pixelpersonaje_27_sar), .sde(c1[5]), .in_7(in_2), .in_5(in_3));  // open: siz, in_8
  PixelPersonaje pixelpersonaje_28 (
    .clk(clk), .abajo(pixelpersonaje_29_sar), .izq(c16[4]), .der(pixelpersonaje_60_siz), .dir(in_1),
    .sar(pixelpersonaje_28_sar), .sde(c1[4]), .in_7(in_2), .in_5(in_3));  // open: siz, in_8
  PixelPersonaje pixelpersonaje_29 (
    .clk(clk), .abajo(pixelpersonaje_30_sar), .izq(c16[3]), .der(pixelpersonaje_61_siz), .dir(in_1),
    .sar(pixelpersonaje_29_sar), .sde(c1[3]), .in_7(in_2), .in_5(in_3));  // open: siz, in_8
  PixelPersonaje pixelpersonaje_30 (
    .clk(clk), .abajo(pixelpersonaje_31_sar), .izq(c16[2]), .der(pixelpersonaje_62_siz), .dir(in_1),
    .sar(pixelpersonaje_30_sar), .sde(c1[2]), .in_8(s1os2), .in_7(in_2), .in_5(in_3));  // open: siz
  PixelPersonaje pixelpersonaje_31 (
    .clk(clk), .abajo(pixelpersonaje_32_sar), .izq(c16[1]), .der(pixelpersonaje_63_siz), .dir(in_1),
    .sar(pixelpersonaje_31_sar), .sde(c1[1]), .in_8(s1os2), .in_7(in_2), .in_5(in_3));  // open: siz
  PixelPersonaje pixelpersonaje_32 (
    .clk(clk), .abajo(c1[31]), .izq(c16[0]), .der(pixelpersonaje_64_siz), .dir(in_1),
    .sar(pixelpersonaje_32_sar), .sde(c1[0]), .in_7(in_2), .in_5(in_3));  // open: siz, in_8
  PixelPersonaje pixelpersonaje_33 (
    .clk(clk), .abajo(pixelpersonaje_34_sar), .izq(c1[31]), .der(pixelpersonaje_65_siz), .dir(in_1),
    .siz(pixelpersonaje_33_siz), .sde(c2[31]), .in_7(in_2), .in_5(in_3));  // open: sar, in_8
  PixelPersonaje pixelpersonaje_34 (
    .clk(clk), .abajo(pixelpersonaje_35_sar), .izq(c1[30]), .der(pixelpersonaje_66_siz), .dir(in_1),
    .sar(pixelpersonaje_34_sar), .siz(pixelpersonaje_34_siz), .sde(c2[30]), .in_7(in_2), .in_5(in_3));  // open: in_8
  PixelPersonaje pixelpersonaje_35 (
    .clk(clk), .abajo(pixelpersonaje_36_sar), .izq(c1[29]), .der(pixelpersonaje_67_siz), .dir(in_1),
    .sar(pixelpersonaje_35_sar), .siz(pixelpersonaje_35_siz), .sde(c2[29]), .in_7(in_2), .in_5(in_3));  // open: in_8
  PixelPersonaje pixelpersonaje_36 (
    .clk(clk), .abajo(pixelpersonaje_37_sar), .izq(c1[28]), .der(pixelpersonaje_68_siz), .dir(in_1),
    .sar(pixelpersonaje_36_sar), .siz(pixelpersonaje_36_siz), .sde(c2[28]), .in_7(in_2), .in_5(in_3));  // open: in_8
  PixelPersonaje pixelpersonaje_37 (
    .clk(clk), .abajo(pixelpersonaje_38_sar), .izq(c1[27]), .der(pixelpersonaje_69_siz), .dir(in_1),
    .sar(pixelpersonaje_37_sar), .siz(pixelpersonaje_37_siz), .sde(c2[27]), .in_7(in_2), .in_5(in_3));  // open: in_8
  PixelPersonaje pixelpersonaje_38 (
    .clk(clk), .abajo(pixelpersonaje_39_sar), .izq(c1[26]), .der(pixelpersonaje_70_siz), .dir(in_1),
    .sar(pixelpersonaje_38_sar), .siz(pixelpersonaje_38_siz), .sde(c2[26]), .in_7(in_2), .in_5(in_3));  // open: in_8
  PixelPersonaje pixelpersonaje_39 (
    .clk(clk), .abajo(pixelpersonaje_40_sar), .izq(c1[25]), .der(pixelpersonaje_71_siz), .dir(in_1),
    .sar(pixelpersonaje_39_sar), .siz(pixelpersonaje_39_siz), .sde(c2[25]), .in_7(in_2), .in_5(in_3));  // open: in_8
  PixelPersonaje pixelpersonaje_40 (
    .clk(clk), .abajo(pixelpersonaje_41_sar), .izq(c1[24]), .der(pixelpersonaje_72_siz), .dir(in_1),
    .sar(pixelpersonaje_40_sar), .siz(pixelpersonaje_40_siz), .sde(c2[24]), .in_7(in_2), .in_5(in_3));  // open: in_8
  PixelPersonaje pixelpersonaje_41 (
    .clk(clk), .abajo(pixelpersonaje_42_sar), .izq(c1[23]), .der(pixelpersonaje_73_siz), .dir(in_1),
    .sar(pixelpersonaje_41_sar), .siz(pixelpersonaje_41_siz), .sde(c2[23]), .in_7(in_2), .in_5(in_3));  // open: in_8
  PixelPersonaje pixelpersonaje_42 (
    .clk(clk), .abajo(pixelpersonaje_43_sar), .izq(c1[22]), .der(pixelpersonaje_74_siz), .dir(in_1),
    .sar(pixelpersonaje_42_sar), .siz(pixelpersonaje_42_siz), .sde(c2[22]), .in_7(in_2), .in_5(in_3));  // open: in_8
  PixelPersonaje pixelpersonaje_43 (
    .clk(clk), .abajo(pixelpersonaje_44_sar), .izq(c1[21]), .der(pixelpersonaje_75_siz), .dir(in_1),
    .sar(pixelpersonaje_43_sar), .siz(pixelpersonaje_43_siz), .sde(c2[21]), .in_7(in_2), .in_5(in_3));  // open: in_8
  PixelPersonaje pixelpersonaje_44 (
    .clk(clk), .abajo(pixelpersonaje_45_sar), .izq(c1[20]), .der(pixelpersonaje_76_siz), .dir(in_1),
    .sar(pixelpersonaje_44_sar), .siz(pixelpersonaje_44_siz), .sde(c2[20]), .in_7(in_2), .in_5(in_3));  // open: in_8
  PixelPersonaje pixelpersonaje_45 (
    .clk(clk), .abajo(pixelpersonaje_46_sar), .izq(c1[19]), .der(pixelpersonaje_77_siz), .dir(in_1),
    .sar(pixelpersonaje_45_sar), .siz(pixelpersonaje_45_siz), .sde(c2[19]), .in_7(in_2), .in_5(in_3));  // open: in_8
  PixelPersonaje pixelpersonaje_46 (
    .clk(clk), .abajo(pixelpersonaje_47_sar), .izq(c1[18]), .der(pixelpersonaje_78_siz), .dir(in_1),
    .sar(pixelpersonaje_46_sar), .siz(pixelpersonaje_46_siz), .sde(c2[18]), .in_7(in_2), .in_5(in_3));  // open: in_8
  PixelPersonaje pixelpersonaje_47 (
    .clk(clk), .abajo(pixelpersonaje_48_sar), .izq(c1[17]), .der(pixelpersonaje_79_siz), .dir(in_1),
    .sar(pixelpersonaje_47_sar), .siz(pixelpersonaje_47_siz), .sde(c2[17]), .in_7(in_2), .in_5(in_3));  // open: in_8
  PixelPersonaje pixelpersonaje_48 (
    .clk(clk), .abajo(pixelpersonaje_49_sar), .izq(c1[16]), .der(pixelpersonaje_80_siz), .dir(in_1),
    .sar(pixelpersonaje_48_sar), .siz(pixelpersonaje_48_siz), .sde(c2[16]), .in_7(in_2), .in_5(in_3));  // open: in_8
  PixelPersonaje pixelpersonaje_49 (
    .clk(clk), .abajo(pixelpersonaje_50_sar), .izq(c1[15]), .der(pixelpersonaje_81_siz), .dir(in_1),
    .sar(pixelpersonaje_49_sar), .siz(pixelpersonaje_49_siz), .sde(c2[15]), .in_7(in_2), .in_5(in_3));  // open: in_8
  PixelPersonaje pixelpersonaje_50 (
    .clk(clk), .abajo(pixelpersonaje_51_sar), .izq(c1[14]), .der(pixelpersonaje_82_siz), .dir(in_1),
    .sar(pixelpersonaje_50_sar), .siz(pixelpersonaje_50_siz), .sde(c2[14]), .in_7(in_2), .in_5(in_3));  // open: in_8
  PixelPersonaje pixelpersonaje_51 (
    .clk(clk), .abajo(pixelpersonaje_52_sar), .izq(c1[13]), .der(pixelpersonaje_83_siz), .dir(in_1),
    .sar(pixelpersonaje_51_sar), .siz(pixelpersonaje_51_siz), .sde(c2[13]), .in_7(in_2), .in_5(in_3));  // open: in_8
  PixelPersonaje pixelpersonaje_52 (
    .clk(clk), .abajo(pixelpersonaje_53_sar), .izq(c1[12]), .der(pixelpersonaje_84_siz), .dir(in_1),
    .sar(pixelpersonaje_52_sar), .siz(pixelpersonaje_52_siz), .sde(c2[12]), .in_7(in_2), .in_5(in_3));  // open: in_8
  PixelPersonaje pixelpersonaje_53 (
    .clk(clk), .abajo(pixelpersonaje_54_sar), .izq(c1[11]), .der(pixelpersonaje_85_siz), .dir(in_1),
    .sar(pixelpersonaje_53_sar), .siz(pixelpersonaje_53_siz), .sde(c2[11]), .in_7(in_2), .in_5(in_3));  // open: in_8
  PixelPersonaje pixelpersonaje_54 (
    .clk(clk), .abajo(pixelpersonaje_55_sar), .izq(c1[10]), .der(pixelpersonaje_86_siz), .dir(in_1),
    .sar(pixelpersonaje_54_sar), .siz(pixelpersonaje_54_siz), .sde(c2[10]), .in_7(in_2), .in_5(in_3));  // open: in_8
  PixelPersonaje pixelpersonaje_55 (
    .clk(clk), .abajo(pixelpersonaje_56_sar), .izq(c1[9]), .der(pixelpersonaje_87_siz), .dir(in_1),
    .sar(pixelpersonaje_55_sar), .siz(pixelpersonaje_55_siz), .sde(c2[9]), .in_7(in_2), .in_5(in_3));  // open: in_8
  PixelPersonaje pixelpersonaje_56 (
    .clk(clk), .abajo(pixelpersonaje_57_sar), .izq(c1[8]), .der(pixelpersonaje_88_siz), .dir(in_1),
    .sar(pixelpersonaje_56_sar), .siz(pixelpersonaje_56_siz), .sde(c2[8]), .in_7(in_2), .in_5(in_3));  // open: in_8
  PixelPersonaje pixelpersonaje_57 (
    .clk(clk), .abajo(pixelpersonaje_58_sar), .izq(c1[7]), .der(pixelpersonaje_89_siz), .dir(in_1),
    .sar(pixelpersonaje_57_sar), .siz(pixelpersonaje_57_siz), .sde(c2[7]), .in_7(in_2), .in_5(in_3));  // open: in_8
  PixelPersonaje pixelpersonaje_58 (
    .clk(clk), .abajo(pixelpersonaje_59_sar), .izq(c1[6]), .der(pixelpersonaje_90_siz), .dir(in_1),
    .sar(pixelpersonaje_58_sar), .siz(pixelpersonaje_58_siz), .sde(c2[6]), .in_7(in_2), .in_5(in_3));  // open: in_8
  PixelPersonaje pixelpersonaje_59 (
    .clk(clk), .abajo(pixelpersonaje_60_sar), .izq(c1[5]), .der(pixelpersonaje_91_siz), .dir(in_1),
    .sar(pixelpersonaje_59_sar), .siz(pixelpersonaje_59_siz), .sde(c2[5]), .in_7(in_2), .in_5(in_3));  // open: in_8
  PixelPersonaje pixelpersonaje_60 (
    .clk(clk), .abajo(pixelpersonaje_61_sar), .izq(c1[4]), .der(pixelpersonaje_92_siz), .dir(in_1),
    .sar(pixelpersonaje_60_sar), .siz(pixelpersonaje_60_siz), .sde(c2[4]), .in_7(in_2), .in_5(in_3));  // open: in_8
  PixelPersonaje pixelpersonaje_61 (
    .clk(clk), .abajo(pixelpersonaje_62_sar), .izq(c1[3]), .der(pixelpersonaje_93_siz), .dir(in_1),
    .sar(pixelpersonaje_61_sar), .siz(pixelpersonaje_61_siz), .sde(c2[3]), .in_7(in_2), .in_5(in_3));  // open: in_8
  PixelPersonaje pixelpersonaje_62 (
    .clk(clk), .abajo(pixelpersonaje_63_sar), .izq(c1[2]), .der(pixelpersonaje_94_siz), .dir(in_1),
    .sar(pixelpersonaje_62_sar), .siz(pixelpersonaje_62_siz), .sde(c2[2]), .in_8(s1os2), .in_7(in_2),
    .in_5(in_3));
  PixelPersonaje pixelpersonaje_63 (
    .clk(clk), .abajo(pixelpersonaje_64_sar), .izq(c1[1]), .der(pixelpersonaje_95_siz), .dir(in_1),
    .sar(pixelpersonaje_63_sar), .siz(pixelpersonaje_63_siz), .sde(c2[1]), .in_8(s1os2), .in_7(in_2),
    .in_5(in_3));
  PixelPersonaje pixelpersonaje_64 (
    .clk(clk), .abajo(c2[31]), .izq(c1[0]), .der(pixelpersonaje_96_siz), .dir(in_1),
    .sar(pixelpersonaje_64_sar), .siz(pixelpersonaje_64_siz), .sde(c2[0]), .in_7(in_2), .in_5(in_3));  // open: in_8
  PixelPersonaje pixelpersonaje_65 (
    .clk(clk), .abajo(pixelpersonaje_66_sar), .izq(c2[31]), .der(pixelpersonaje_97_siz), .dir(in_1),
    .siz(pixelpersonaje_65_siz), .sde(c3[31]), .in_7(in_2), .in_5(in_3));  // open: sar, in_8
  PixelPersonaje pixelpersonaje_66 (
    .clk(clk), .abajo(pixelpersonaje_67_sar), .izq(c2[30]), .der(pixelpersonaje_98_siz), .dir(in_1),
    .sar(pixelpersonaje_66_sar), .siz(pixelpersonaje_66_siz), .sde(c3[30]), .in_7(in_2), .in_5(in_3));  // open: in_8
  PixelPersonaje pixelpersonaje_67 (
    .clk(clk), .abajo(pixelpersonaje_68_sar), .izq(c2[29]), .der(pixelpersonaje_99_siz), .dir(in_1),
    .sar(pixelpersonaje_67_sar), .siz(pixelpersonaje_67_siz), .sde(c3[29]), .in_7(in_2), .in_5(in_3));  // open: in_8
  PixelPersonaje pixelpersonaje_68 (
    .clk(clk), .abajo(pixelpersonaje_69_sar), .izq(c2[28]), .der(pixelpersonaje_100_siz), .dir(in_1),
    .sar(pixelpersonaje_68_sar), .siz(pixelpersonaje_68_siz), .sde(c3[28]), .in_7(in_2), .in_5(in_3));  // open: in_8
  PixelPersonaje pixelpersonaje_69 (
    .clk(clk), .abajo(pixelpersonaje_70_sar), .izq(c2[27]), .der(pixelpersonaje_101_siz), .dir(in_1),
    .sar(pixelpersonaje_69_sar), .siz(pixelpersonaje_69_siz), .sde(c3[27]), .in_7(in_2), .in_5(in_3));  // open: in_8
  PixelPersonaje pixelpersonaje_70 (
    .clk(clk), .abajo(pixelpersonaje_71_sar), .izq(c2[26]), .der(pixelpersonaje_102_siz), .dir(in_1),
    .sar(pixelpersonaje_70_sar), .siz(pixelpersonaje_70_siz), .sde(c3[26]), .in_7(in_2), .in_5(in_3));  // open: in_8
  PixelPersonaje pixelpersonaje_71 (
    .clk(clk), .abajo(pixelpersonaje_72_sar), .izq(c2[25]), .der(pixelpersonaje_103_siz), .dir(in_1),
    .sar(pixelpersonaje_71_sar), .siz(pixelpersonaje_71_siz), .sde(c3[25]), .in_7(in_2), .in_5(in_3));  // open: in_8
  PixelPersonaje pixelpersonaje_72 (
    .clk(clk), .abajo(pixelpersonaje_73_sar), .izq(c2[24]), .der(pixelpersonaje_104_siz), .dir(in_1),
    .sar(pixelpersonaje_72_sar), .siz(pixelpersonaje_72_siz), .sde(c3[24]), .in_7(in_2), .in_5(in_3));  // open: in_8
  PixelPersonaje pixelpersonaje_73 (
    .clk(clk), .abajo(pixelpersonaje_74_sar), .izq(c2[23]), .der(pixelpersonaje_105_siz), .dir(in_1),
    .sar(pixelpersonaje_73_sar), .siz(pixelpersonaje_73_siz), .sde(c3[23]), .in_7(in_2), .in_5(in_3));  // open: in_8
  PixelPersonaje pixelpersonaje_74 (
    .clk(clk), .abajo(pixelpersonaje_75_sar), .izq(c2[22]), .der(pixelpersonaje_106_siz), .dir(in_1),
    .sar(pixelpersonaje_74_sar), .siz(pixelpersonaje_74_siz), .sde(c3[22]), .in_7(in_2), .in_5(in_3));  // open: in_8
  PixelPersonaje pixelpersonaje_75 (
    .clk(clk), .abajo(pixelpersonaje_76_sar), .izq(c2[21]), .der(pixelpersonaje_107_siz), .dir(in_1),
    .sar(pixelpersonaje_75_sar), .siz(pixelpersonaje_75_siz), .sde(c3[21]), .in_7(in_2), .in_5(in_3));  // open: in_8
  PixelPersonaje pixelpersonaje_76 (
    .clk(clk), .abajo(pixelpersonaje_77_sar), .izq(c2[20]), .der(pixelpersonaje_108_siz), .dir(in_1),
    .sar(pixelpersonaje_76_sar), .siz(pixelpersonaje_76_siz), .sde(c3[20]), .in_7(in_2), .in_5(in_3));  // open: in_8
  PixelPersonaje pixelpersonaje_77 (
    .clk(clk), .abajo(pixelpersonaje_78_sar), .izq(c2[19]), .der(pixelpersonaje_109_siz), .dir(in_1),
    .sar(pixelpersonaje_77_sar), .siz(pixelpersonaje_77_siz), .sde(c3[19]), .in_7(in_2), .in_5(in_3));  // open: in_8
  PixelPersonaje pixelpersonaje_78 (
    .clk(clk), .abajo(pixelpersonaje_79_sar), .izq(c2[18]), .der(pixelpersonaje_110_siz), .dir(in_1),
    .sar(pixelpersonaje_78_sar), .siz(pixelpersonaje_78_siz), .sde(c3[18]), .in_7(in_2), .in_5(in_3));  // open: in_8
  PixelPersonaje pixelpersonaje_79 (
    .clk(clk), .abajo(pixelpersonaje_80_sar), .izq(c2[17]), .der(pixelpersonaje_111_siz), .dir(in_1),
    .sar(pixelpersonaje_79_sar), .siz(pixelpersonaje_79_siz), .sde(c3[17]), .in_7(in_2), .in_5(in_3));  // open: in_8
  PixelPersonaje pixelpersonaje_80 (
    .clk(clk), .abajo(pixelpersonaje_81_sar), .izq(c2[16]), .der(pixelpersonaje_112_siz), .dir(in_1),
    .sar(pixelpersonaje_80_sar), .siz(pixelpersonaje_80_siz), .sde(c3[16]), .in_7(in_2), .in_5(in_3));  // open: in_8
  PixelPersonaje pixelpersonaje_81 (
    .clk(clk), .abajo(pixelpersonaje_82_sar), .izq(c2[15]), .der(pixelpersonaje_113_siz), .dir(in_1),
    .sar(pixelpersonaje_81_sar), .siz(pixelpersonaje_81_siz), .sde(c3[15]), .in_7(in_2), .in_5(in_3));  // open: in_8
  PixelPersonaje pixelpersonaje_82 (
    .clk(clk), .abajo(pixelpersonaje_83_sar), .izq(c2[14]), .der(pixelpersonaje_114_siz), .dir(in_1),
    .sar(pixelpersonaje_82_sar), .siz(pixelpersonaje_82_siz), .sde(c3[14]), .in_7(in_2), .in_5(in_3));  // open: in_8
  PixelPersonaje pixelpersonaje_83 (
    .clk(clk), .abajo(pixelpersonaje_84_sar), .izq(c2[13]), .der(pixelpersonaje_115_siz), .dir(in_1),
    .sar(pixelpersonaje_83_sar), .siz(pixelpersonaje_83_siz), .sde(c3[13]), .in_7(in_2), .in_5(in_3));  // open: in_8
  PixelPersonaje pixelpersonaje_84 (
    .clk(clk), .abajo(pixelpersonaje_85_sar), .izq(c2[12]), .der(pixelpersonaje_116_siz), .dir(in_1),
    .sar(pixelpersonaje_84_sar), .siz(pixelpersonaje_84_siz), .sde(c3[12]), .in_7(in_2), .in_5(in_3));  // open: in_8
  PixelPersonaje pixelpersonaje_85 (
    .clk(clk), .abajo(pixelpersonaje_86_sar), .izq(c2[11]), .der(pixelpersonaje_117_siz), .dir(in_1),
    .sar(pixelpersonaje_85_sar), .siz(pixelpersonaje_85_siz), .sde(c3[11]), .in_7(in_2), .in_5(in_3));  // open: in_8
  PixelPersonaje pixelpersonaje_86 (
    .clk(clk), .abajo(pixelpersonaje_87_sar), .izq(c2[10]), .der(pixelpersonaje_118_siz), .dir(in_1),
    .sar(pixelpersonaje_86_sar), .siz(pixelpersonaje_86_siz), .sde(c3[10]), .in_7(in_2), .in_5(in_3));  // open: in_8
  PixelPersonaje pixelpersonaje_87 (
    .clk(clk), .abajo(pixelpersonaje_88_sar), .izq(c2[9]), .der(pixelpersonaje_119_siz), .dir(in_1),
    .sar(pixelpersonaje_87_sar), .siz(pixelpersonaje_87_siz), .sde(c3[9]), .in_7(in_2), .in_5(in_3));  // open: in_8
  PixelPersonaje pixelpersonaje_88 (
    .clk(clk), .abajo(pixelpersonaje_89_sar), .izq(c2[8]), .der(pixelpersonaje_120_siz), .dir(in_1),
    .sar(pixelpersonaje_88_sar), .siz(pixelpersonaje_88_siz), .sde(c3[8]), .in_7(in_2), .in_5(in_3));  // open: in_8
  PixelPersonaje pixelpersonaje_89 (
    .clk(clk), .abajo(pixelpersonaje_90_sar), .izq(c2[7]), .der(pixelpersonaje_121_siz), .dir(in_1),
    .sar(pixelpersonaje_89_sar), .siz(pixelpersonaje_89_siz), .sde(c3[7]), .in_7(in_2), .in_5(in_3));  // open: in_8
  PixelPersonaje pixelpersonaje_90 (
    .clk(clk), .abajo(pixelpersonaje_91_sar), .izq(c2[6]), .der(pixelpersonaje_122_siz), .dir(in_1),
    .sar(pixelpersonaje_90_sar), .siz(pixelpersonaje_90_siz), .sde(c3[6]), .in_7(in_2), .in_5(in_3));  // open: in_8
  PixelPersonaje pixelpersonaje_91 (
    .clk(clk), .abajo(pixelpersonaje_92_sar), .izq(c2[5]), .der(pixelpersonaje_123_siz), .dir(in_1),
    .sar(pixelpersonaje_91_sar), .siz(pixelpersonaje_91_siz), .sde(c3[5]), .in_7(in_2), .in_5(in_3));  // open: in_8
  PixelPersonaje pixelpersonaje_92 (
    .clk(clk), .abajo(pixelpersonaje_93_sar), .izq(c2[4]), .der(pixelpersonaje_124_siz), .dir(in_1),
    .sar(pixelpersonaje_92_sar), .siz(pixelpersonaje_92_siz), .sde(c3[4]), .in_7(in_2), .in_5(in_3));  // open: in_8
  PixelPersonaje pixelpersonaje_93 (
    .clk(clk), .abajo(pixelpersonaje_94_sar), .izq(c2[3]), .der(pixelpersonaje_125_siz), .dir(in_1),
    .sar(pixelpersonaje_93_sar), .siz(pixelpersonaje_93_siz), .sde(c3[3]), .in_7(in_2), .in_5(in_3));  // open: in_8
  PixelPersonaje pixelpersonaje_94 (
    .clk(clk), .abajo(pixelpersonaje_95_sar), .izq(c2[2]), .der(pixelpersonaje_126_siz), .dir(in_1),
    .sar(pixelpersonaje_94_sar), .siz(pixelpersonaje_94_siz), .sde(c3[2]), .in_8(s2os3), .in_7(in_2),
    .in_5(in_3));
  PixelPersonaje pixelpersonaje_95 (
    .clk(clk), .abajo(pixelpersonaje_96_sar), .izq(c2[1]), .der(pixelpersonaje_127_siz), .dir(in_1),
    .sar(pixelpersonaje_95_sar), .siz(pixelpersonaje_95_siz), .sde(c3[1]), .in_8(s2os3), .in_7(in_2),
    .in_5(in_3));
  PixelPersonaje pixelpersonaje_96 (
    .clk(clk), .abajo(c3[31]), .izq(c2[0]), .der(pixelpersonaje_128_siz), .dir(in_1),
    .sar(pixelpersonaje_96_sar), .siz(pixelpersonaje_96_siz), .sde(c3[0]), .in_7(in_2), .in_5(in_3));  // open: in_8
  PixelPersonaje pixelpersonaje_97 (
    .clk(clk), .abajo(pixelpersonaje_98_sar), .izq(c3[31]), .der(pixelpersonaje_129_siz), .dir(in_1),
    .siz(pixelpersonaje_97_siz), .sde(c4[31]), .in_7(in_2), .in_5(in_3));  // open: sar, in_8
  PixelPersonaje pixelpersonaje_98 (
    .clk(clk), .abajo(pixelpersonaje_99_sar), .izq(c3[30]), .der(pixelpersonaje_130_siz), .dir(in_1),
    .sar(pixelpersonaje_98_sar), .siz(pixelpersonaje_98_siz), .sde(c4[30]), .in_7(in_2), .in_5(in_3));  // open: in_8
  PixelPersonaje pixelpersonaje_99 (
    .clk(clk), .abajo(pixelpersonaje_100_sar), .izq(c3[29]), .der(pixelpersonaje_131_siz), .dir(in_1),
    .sar(pixelpersonaje_99_sar), .siz(pixelpersonaje_99_siz), .sde(c4[29]), .in_7(in_2), .in_5(in_3));  // open: in_8
  PixelPersonaje pixelpersonaje_100 (
    .clk(clk), .abajo(pixelpersonaje_101_sar), .izq(c3[28]), .der(pixelpersonaje_132_siz), .dir(in_1),
    .sar(pixelpersonaje_100_sar), .siz(pixelpersonaje_100_siz), .sde(c4[28]), .in_7(in_2), .in_5(in_3));  // open: in_8
  PixelPersonaje pixelpersonaje_101 (
    .clk(clk), .abajo(pixelpersonaje_102_sar), .izq(c3[27]), .der(pixelpersonaje_133_siz), .dir(in_1),
    .sar(pixelpersonaje_101_sar), .siz(pixelpersonaje_101_siz), .sde(c4[27]), .in_7(in_2), .in_5(in_3));  // open: in_8
  PixelPersonaje pixelpersonaje_102 (
    .clk(clk), .abajo(pixelpersonaje_103_sar), .izq(c3[26]), .der(pixelpersonaje_134_siz), .dir(in_1),
    .sar(pixelpersonaje_102_sar), .siz(pixelpersonaje_102_siz), .sde(c4[26]), .in_7(in_2), .in_5(in_3));  // open: in_8
  PixelPersonaje pixelpersonaje_103 (
    .clk(clk), .abajo(pixelpersonaje_104_sar), .izq(c3[25]), .der(pixelpersonaje_135_siz), .dir(in_1),
    .sar(pixelpersonaje_103_sar), .siz(pixelpersonaje_103_siz), .sde(c4[25]), .in_7(in_2), .in_5(in_3));  // open: in_8
  PixelPersonaje pixelpersonaje_104 (
    .clk(clk), .abajo(pixelpersonaje_105_sar), .izq(c3[24]), .der(pixelpersonaje_136_siz), .dir(in_1),
    .sar(pixelpersonaje_104_sar), .siz(pixelpersonaje_104_siz), .sde(c4[24]), .in_7(in_2), .in_5(in_3));  // open: in_8
  PixelPersonaje pixelpersonaje_105 (
    .clk(clk), .abajo(pixelpersonaje_106_sar), .izq(c3[23]), .der(pixelpersonaje_137_siz), .dir(in_1),
    .sar(pixelpersonaje_105_sar), .siz(pixelpersonaje_105_siz), .sde(c4[23]), .in_7(in_2), .in_5(in_3));  // open: in_8
  PixelPersonaje pixelpersonaje_106 (
    .clk(clk), .abajo(pixelpersonaje_107_sar), .izq(c3[22]), .der(pixelpersonaje_138_siz), .dir(in_1),
    .sar(pixelpersonaje_106_sar), .siz(pixelpersonaje_106_siz), .sde(c4[22]), .in_7(in_2), .in_5(in_3));  // open: in_8
  PixelPersonaje pixelpersonaje_107 (
    .clk(clk), .abajo(pixelpersonaje_108_sar), .izq(c3[21]), .der(pixelpersonaje_139_siz), .dir(in_1),
    .sar(pixelpersonaje_107_sar), .siz(pixelpersonaje_107_siz), .sde(c4[21]), .in_7(in_2), .in_5(in_3));  // open: in_8
  PixelPersonaje pixelpersonaje_108 (
    .clk(clk), .abajo(pixelpersonaje_109_sar), .izq(c3[20]), .der(pixelpersonaje_140_siz), .dir(in_1),
    .sar(pixelpersonaje_108_sar), .siz(pixelpersonaje_108_siz), .sde(c4[20]), .in_7(in_2), .in_5(in_3));  // open: in_8
  PixelPersonaje pixelpersonaje_109 (
    .clk(clk), .abajo(pixelpersonaje_110_sar), .izq(c3[19]), .der(pixelpersonaje_141_siz), .dir(in_1),
    .sar(pixelpersonaje_109_sar), .siz(pixelpersonaje_109_siz), .sde(c4[19]), .in_7(in_2), .in_5(in_3));  // open: in_8
  PixelPersonaje pixelpersonaje_110 (
    .clk(clk), .abajo(pixelpersonaje_111_sar), .izq(c3[18]), .der(pixelpersonaje_142_siz), .dir(in_1),
    .sar(pixelpersonaje_110_sar), .siz(pixelpersonaje_110_siz), .sde(c4[18]), .in_7(in_2), .in_5(in_3));  // open: in_8
  PixelPersonaje pixelpersonaje_111 (
    .clk(clk), .abajo(pixelpersonaje_112_sar), .izq(c3[17]), .der(pixelpersonaje_143_siz), .dir(in_1),
    .sar(pixelpersonaje_111_sar), .siz(pixelpersonaje_111_siz), .sde(c4[17]), .in_7(in_2), .in_5(in_3));  // open: in_8
  PixelPersonaje pixelpersonaje_112 (
    .clk(clk), .abajo(pixelpersonaje_113_sar), .izq(c3[16]), .der(pixelpersonaje_144_siz), .dir(in_1),
    .sar(pixelpersonaje_112_sar), .siz(pixelpersonaje_112_siz), .sde(c4[16]), .in_7(in_2), .in_5(in_3));  // open: in_8
  PixelPersonaje pixelpersonaje_113 (
    .clk(clk), .abajo(pixelpersonaje_114_sar), .izq(c3[15]), .der(pixelpersonaje_145_siz), .dir(in_1),
    .sar(pixelpersonaje_113_sar), .siz(pixelpersonaje_113_siz), .sde(c4[15]), .in_7(in_2), .in_5(in_3));  // open: in_8
  PixelPersonaje pixelpersonaje_114 (
    .clk(clk), .abajo(pixelpersonaje_115_sar), .izq(c3[14]), .der(pixelpersonaje_146_siz), .dir(in_1),
    .sar(pixelpersonaje_114_sar), .siz(pixelpersonaje_114_siz), .sde(c4[14]), .in_7(in_2), .in_5(in_3));  // open: in_8
  PixelPersonaje pixelpersonaje_115 (
    .clk(clk), .abajo(pixelpersonaje_116_sar), .izq(c3[13]), .der(pixelpersonaje_147_siz), .dir(in_1),
    .sar(pixelpersonaje_115_sar), .siz(pixelpersonaje_115_siz), .sde(c4[13]), .in_7(in_2), .in_5(in_3));  // open: in_8
  PixelPersonaje pixelpersonaje_116 (
    .clk(clk), .abajo(pixelpersonaje_117_sar), .izq(c3[12]), .der(pixelpersonaje_148_siz), .dir(in_1),
    .sar(pixelpersonaje_116_sar), .siz(pixelpersonaje_116_siz), .sde(c4[12]), .in_7(in_2), .in_5(in_3));  // open: in_8
  PixelPersonaje pixelpersonaje_117 (
    .clk(clk), .abajo(pixelpersonaje_118_sar), .izq(c3[11]), .der(pixelpersonaje_149_siz), .dir(in_1),
    .sar(pixelpersonaje_117_sar), .siz(pixelpersonaje_117_siz), .sde(c4[11]), .in_7(in_2), .in_5(in_3));  // open: in_8
  PixelPersonaje pixelpersonaje_118 (
    .clk(clk), .abajo(pixelpersonaje_119_sar), .izq(c3[10]), .der(pixelpersonaje_150_siz), .dir(in_1),
    .sar(pixelpersonaje_118_sar), .siz(pixelpersonaje_118_siz), .sde(c4[10]), .in_7(in_2), .in_5(in_3));  // open: in_8
  PixelPersonaje pixelpersonaje_119 (
    .clk(clk), .abajo(pixelpersonaje_120_sar), .izq(c3[9]), .der(pixelpersonaje_151_siz), .dir(in_1),
    .sar(pixelpersonaje_119_sar), .siz(pixelpersonaje_119_siz), .sde(c4[9]), .in_7(in_2), .in_5(in_3));  // open: in_8
  PixelPersonaje pixelpersonaje_120 (
    .clk(clk), .abajo(pixelpersonaje_121_sar), .izq(c3[8]), .der(pixelpersonaje_152_siz), .dir(in_1),
    .sar(pixelpersonaje_120_sar), .siz(pixelpersonaje_120_siz), .sde(c4[8]), .in_7(in_2), .in_5(in_3));  // open: in_8
  PixelPersonaje pixelpersonaje_121 (
    .clk(clk), .abajo(pixelpersonaje_122_sar), .izq(c3[7]), .der(pixelpersonaje_153_siz), .dir(in_1),
    .sar(pixelpersonaje_121_sar), .siz(pixelpersonaje_121_siz), .sde(c4[7]), .in_7(in_2), .in_5(in_3));  // open: in_8
  PixelPersonaje pixelpersonaje_122 (
    .clk(clk), .abajo(pixelpersonaje_123_sar), .izq(c3[6]), .der(pixelpersonaje_154_siz), .dir(in_1),
    .sar(pixelpersonaje_122_sar), .siz(pixelpersonaje_122_siz), .sde(c4[6]), .in_7(in_2), .in_5(in_3));  // open: in_8
  PixelPersonaje pixelpersonaje_123 (
    .clk(clk), .abajo(pixelpersonaje_124_sar), .izq(c3[5]), .der(pixelpersonaje_155_siz), .dir(in_1),
    .sar(pixelpersonaje_123_sar), .siz(pixelpersonaje_123_siz), .sde(c4[5]), .in_7(in_2), .in_5(in_3));  // open: in_8
  PixelPersonaje pixelpersonaje_124 (
    .clk(clk), .abajo(pixelpersonaje_125_sar), .izq(c3[4]), .der(pixelpersonaje_156_siz), .dir(in_1),
    .sar(pixelpersonaje_124_sar), .siz(pixelpersonaje_124_siz), .sde(c4[4]), .in_7(in_2), .in_5(in_3));  // open: in_8
  PixelPersonaje pixelpersonaje_125 (
    .clk(clk), .abajo(pixelpersonaje_126_sar), .izq(c3[3]), .der(pixelpersonaje_157_siz), .dir(in_1),
    .sar(pixelpersonaje_125_sar), .siz(pixelpersonaje_125_siz), .sde(c4[3]), .in_7(in_2), .in_5(in_3));  // open: in_8
  PixelPersonaje pixelpersonaje_126 (
    .clk(clk), .abajo(pixelpersonaje_127_sar), .izq(c3[2]), .der(pixelpersonaje_158_siz), .dir(in_1),
    .sar(pixelpersonaje_126_sar), .siz(pixelpersonaje_126_siz), .sde(c4[2]), .in_8(s3os4), .in_7(in_2),
    .in_5(in_3));
  PixelPersonaje pixelpersonaje_127 (
    .clk(clk), .abajo(pixelpersonaje_128_sar), .izq(c3[1]), .der(pixelpersonaje_159_siz), .dir(in_1),
    .sar(pixelpersonaje_127_sar), .siz(pixelpersonaje_127_siz), .sde(c4[1]), .in_8(s3os4), .in_7(in_2),
    .in_5(in_3));
  PixelPersonaje pixelpersonaje_128 (
    .clk(clk), .abajo(c4[31]), .izq(c3[0]), .der(pixelpersonaje_160_siz), .dir(in_1),
    .sar(pixelpersonaje_128_sar), .siz(pixelpersonaje_128_siz), .sde(c4[0]), .in_7(in_2), .in_5(in_3));  // open: in_8
  PixelPersonaje pixelpersonaje_129 (
    .clk(clk), .abajo(pixelpersonaje_130_sar), .izq(c4[31]), .der(pixelpersonaje_161_siz), .dir(in_1),
    .siz(pixelpersonaje_129_siz), .sde(c5[31]), .in_7(in_2), .in_5(in_3));  // open: sar, in_8
  PixelPersonaje pixelpersonaje_130 (
    .clk(clk), .abajo(pixelpersonaje_131_sar), .izq(c4[30]), .der(pixelpersonaje_162_siz), .dir(in_1),
    .sar(pixelpersonaje_130_sar), .siz(pixelpersonaje_130_siz), .sde(c5[30]), .in_7(in_2), .in_5(in_3));  // open: in_8
  PixelPersonaje pixelpersonaje_131 (
    .clk(clk), .abajo(pixelpersonaje_132_sar), .izq(c4[29]), .der(pixelpersonaje_163_siz), .dir(in_1),
    .sar(pixelpersonaje_131_sar), .siz(pixelpersonaje_131_siz), .sde(c5[29]), .in_7(in_2), .in_5(in_3));  // open: in_8
  PixelPersonaje pixelpersonaje_132 (
    .clk(clk), .abajo(pixelpersonaje_133_sar), .izq(c4[28]), .der(pixelpersonaje_164_siz), .dir(in_1),
    .sar(pixelpersonaje_132_sar), .siz(pixelpersonaje_132_siz), .sde(c5[28]), .in_7(in_2), .in_5(in_3));  // open: in_8
  PixelPersonaje pixelpersonaje_133 (
    .clk(clk), .abajo(pixelpersonaje_134_sar), .izq(c4[27]), .der(pixelpersonaje_165_siz), .dir(in_1),
    .sar(pixelpersonaje_133_sar), .siz(pixelpersonaje_133_siz), .sde(c5[27]), .in_7(in_2), .in_5(in_3));  // open: in_8
  PixelPersonaje pixelpersonaje_134 (
    .clk(clk), .abajo(pixelpersonaje_135_sar), .izq(c4[26]), .der(pixelpersonaje_166_siz), .dir(in_1),
    .sar(pixelpersonaje_134_sar), .siz(pixelpersonaje_134_siz), .sde(c5[26]), .in_7(in_2), .in_5(in_3));  // open: in_8
  PixelPersonaje pixelpersonaje_135 (
    .clk(clk), .abajo(pixelpersonaje_136_sar), .izq(c4[25]), .der(pixelpersonaje_167_siz), .dir(in_1),
    .sar(pixelpersonaje_135_sar), .siz(pixelpersonaje_135_siz), .sde(c5[25]), .in_7(in_2), .in_5(in_3));  // open: in_8
  PixelPersonaje pixelpersonaje_136 (
    .clk(clk), .abajo(pixelpersonaje_137_sar), .izq(c4[24]), .der(pixelpersonaje_168_siz), .dir(in_1),
    .sar(pixelpersonaje_136_sar), .siz(pixelpersonaje_136_siz), .sde(c5[24]), .in_7(in_2), .in_5(in_3));  // open: in_8
  PixelPersonaje pixelpersonaje_137 (
    .clk(clk), .abajo(pixelpersonaje_138_sar), .izq(c4[23]), .der(pixelpersonaje_169_siz), .dir(in_1),
    .sar(pixelpersonaje_137_sar), .siz(pixelpersonaje_137_siz), .sde(c5[23]), .in_7(in_2), .in_5(in_3));  // open: in_8
  PixelPersonaje pixelpersonaje_138 (
    .clk(clk), .abajo(pixelpersonaje_139_sar), .izq(c4[22]), .der(pixelpersonaje_170_siz), .dir(in_1),
    .sar(pixelpersonaje_138_sar), .siz(pixelpersonaje_138_siz), .sde(c5[22]), .in_7(in_2), .in_5(in_3));  // open: in_8
  PixelPersonaje pixelpersonaje_139 (
    .clk(clk), .abajo(pixelpersonaje_140_sar), .izq(c4[21]), .der(pixelpersonaje_171_siz), .dir(in_1),
    .sar(pixelpersonaje_139_sar), .siz(pixelpersonaje_139_siz), .sde(c5[21]), .in_7(in_2), .in_5(in_3));  // open: in_8
  PixelPersonaje pixelpersonaje_140 (
    .clk(clk), .abajo(pixelpersonaje_141_sar), .izq(c4[20]), .der(pixelpersonaje_172_siz), .dir(in_1),
    .sar(pixelpersonaje_140_sar), .siz(pixelpersonaje_140_siz), .sde(c5[20]), .in_7(in_2), .in_5(in_3));  // open: in_8
  PixelPersonaje pixelpersonaje_141 (
    .clk(clk), .abajo(pixelpersonaje_142_sar), .izq(c4[19]), .der(pixelpersonaje_173_siz), .dir(in_1),
    .sar(pixelpersonaje_141_sar), .siz(pixelpersonaje_141_siz), .sde(c5[19]), .in_7(in_2), .in_5(in_3));  // open: in_8
  PixelPersonaje pixelpersonaje_142 (
    .clk(clk), .abajo(pixelpersonaje_143_sar), .izq(c4[18]), .der(pixelpersonaje_174_siz), .dir(in_1),
    .sar(pixelpersonaje_142_sar), .siz(pixelpersonaje_142_siz), .sde(c5[18]), .in_7(in_2), .in_5(in_3));  // open: in_8
  PixelPersonaje pixelpersonaje_143 (
    .clk(clk), .abajo(pixelpersonaje_144_sar), .izq(c4[17]), .der(pixelpersonaje_175_siz), .dir(in_1),
    .sar(pixelpersonaje_143_sar), .siz(pixelpersonaje_143_siz), .sde(c5[17]), .in_7(in_2), .in_5(in_3));  // open: in_8
  PixelPersonaje pixelpersonaje_144 (
    .clk(clk), .abajo(pixelpersonaje_145_sar), .izq(c4[16]), .der(pixelpersonaje_176_siz), .dir(in_1),
    .sar(pixelpersonaje_144_sar), .siz(pixelpersonaje_144_siz), .sde(c5[16]), .in_7(in_2), .in_5(in_3));  // open: in_8
  PixelPersonaje pixelpersonaje_145 (
    .clk(clk), .abajo(pixelpersonaje_146_sar), .izq(c4[15]), .der(pixelpersonaje_177_siz), .dir(in_1),
    .sar(pixelpersonaje_145_sar), .siz(pixelpersonaje_145_siz), .sde(c5[15]), .in_7(in_2), .in_5(in_3));  // open: in_8
  PixelPersonaje pixelpersonaje_146 (
    .clk(clk), .abajo(pixelpersonaje_147_sar), .izq(c4[14]), .der(pixelpersonaje_178_siz), .dir(in_1),
    .sar(pixelpersonaje_146_sar), .siz(pixelpersonaje_146_siz), .sde(c5[14]), .in_7(in_2), .in_5(in_3));  // open: in_8
  PixelPersonaje pixelpersonaje_147 (
    .clk(clk), .abajo(pixelpersonaje_148_sar), .izq(c4[13]), .der(pixelpersonaje_179_siz), .dir(in_1),
    .sar(pixelpersonaje_147_sar), .siz(pixelpersonaje_147_siz), .sde(c5[13]), .in_7(in_2), .in_5(in_3));  // open: in_8
  PixelPersonaje pixelpersonaje_148 (
    .clk(clk), .abajo(pixelpersonaje_149_sar), .izq(c4[12]), .der(pixelpersonaje_180_siz), .dir(in_1),
    .sar(pixelpersonaje_148_sar), .siz(pixelpersonaje_148_siz), .sde(c5[12]), .in_7(in_2), .in_5(in_3));  // open: in_8
  PixelPersonaje pixelpersonaje_149 (
    .clk(clk), .abajo(pixelpersonaje_150_sar), .izq(c4[11]), .der(pixelpersonaje_181_siz), .dir(in_1),
    .sar(pixelpersonaje_149_sar), .siz(pixelpersonaje_149_siz), .sde(c5[11]), .in_7(in_2), .in_5(in_3));  // open: in_8
  PixelPersonaje pixelpersonaje_150 (
    .clk(clk), .abajo(pixelpersonaje_151_sar), .izq(c4[10]), .der(pixelpersonaje_182_siz), .dir(in_1),
    .sar(pixelpersonaje_150_sar), .siz(pixelpersonaje_150_siz), .sde(c5[10]), .in_7(in_2), .in_5(in_3));  // open: in_8
  PixelPersonaje pixelpersonaje_151 (
    .clk(clk), .abajo(pixelpersonaje_152_sar), .izq(c4[9]), .der(pixelpersonaje_183_siz), .dir(in_1),
    .sar(pixelpersonaje_151_sar), .siz(pixelpersonaje_151_siz), .sde(c5[9]), .in_7(in_2), .in_5(in_3));  // open: in_8
  PixelPersonaje pixelpersonaje_152 (
    .clk(clk), .abajo(pixelpersonaje_153_sar), .izq(c4[8]), .der(pixelpersonaje_184_siz), .dir(in_1),
    .sar(pixelpersonaje_152_sar), .siz(pixelpersonaje_152_siz), .sde(c5[8]), .in_7(in_2), .in_5(in_3));  // open: in_8
  PixelPersonaje pixelpersonaje_153 (
    .clk(clk), .abajo(pixelpersonaje_154_sar), .izq(c4[7]), .der(pixelpersonaje_185_siz), .dir(in_1),
    .sar(pixelpersonaje_153_sar), .siz(pixelpersonaje_153_siz), .sde(c5[7]), .in_7(in_2), .in_5(in_3));  // open: in_8
  PixelPersonaje pixelpersonaje_154 (
    .clk(clk), .abajo(pixelpersonaje_155_sar), .izq(c4[6]), .der(pixelpersonaje_186_siz), .dir(in_1),
    .sar(pixelpersonaje_154_sar), .siz(pixelpersonaje_154_siz), .sde(c5[6]), .in_7(in_2), .in_5(in_3));  // open: in_8
  PixelPersonaje pixelpersonaje_155 (
    .clk(clk), .abajo(pixelpersonaje_156_sar), .izq(c4[5]), .der(pixelpersonaje_187_siz), .dir(in_1),
    .sar(pixelpersonaje_155_sar), .siz(pixelpersonaje_155_siz), .sde(c5[5]), .in_7(in_2), .in_5(in_3));  // open: in_8
  PixelPersonaje pixelpersonaje_156 (
    .clk(clk), .abajo(pixelpersonaje_157_sar), .izq(c4[4]), .der(pixelpersonaje_188_siz), .dir(in_1),
    .sar(pixelpersonaje_156_sar), .siz(pixelpersonaje_156_siz), .sde(c5[4]), .in_7(in_2), .in_5(in_3));  // open: in_8
  PixelPersonaje pixelpersonaje_157 (
    .clk(clk), .abajo(pixelpersonaje_158_sar), .izq(c4[3]), .der(pixelpersonaje_189_siz), .dir(in_1),
    .sar(pixelpersonaje_157_sar), .siz(pixelpersonaje_157_siz), .sde(c5[3]), .in_7(in_2), .in_5(in_3));  // open: in_8
  PixelPersonaje pixelpersonaje_158 (
    .clk(clk), .abajo(pixelpersonaje_159_sar), .izq(c4[2]), .der(pixelpersonaje_190_siz), .dir(in_1),
    .sar(pixelpersonaje_158_sar), .siz(pixelpersonaje_158_siz), .sde(c5[2]), .in_8(s4os5), .in_7(in_2),
    .in_5(in_3));
  PixelPersonaje pixelpersonaje_159 (
    .clk(clk), .abajo(pixelpersonaje_160_sar), .izq(c4[1]), .der(pixelpersonaje_191_siz), .dir(in_1),
    .sar(pixelpersonaje_159_sar), .siz(pixelpersonaje_159_siz), .sde(c5[1]), .in_8(s4os5), .in_7(in_2),
    .in_5(in_3));
  PixelPersonaje pixelpersonaje_160 (
    .clk(clk), .abajo(c5[31]), .izq(c4[0]), .der(pixelpersonaje_192_siz), .dir(in_1),
    .sar(pixelpersonaje_160_sar), .siz(pixelpersonaje_160_siz), .sde(c5[0]), .in_7(in_2), .in_5(in_3));  // open: in_8
  PixelPersonaje pixelpersonaje_161 (
    .clk(clk), .abajo(pixelpersonaje_162_sar), .izq(c5[31]), .der(pixelpersonaje_193_siz), .dir(in_1),
    .siz(pixelpersonaje_161_siz), .sde(c6[31]), .in_7(in_2), .in_5(in_3));  // open: sar, in_8
  PixelPersonaje pixelpersonaje_162 (
    .clk(clk), .abajo(pixelpersonaje_163_sar), .izq(c5[30]), .der(pixelpersonaje_194_siz), .dir(in_1),
    .sar(pixelpersonaje_162_sar), .siz(pixelpersonaje_162_siz), .sde(c6[30]), .in_7(in_2), .in_5(in_3));  // open: in_8
  PixelPersonaje pixelpersonaje_163 (
    .clk(clk), .abajo(pixelpersonaje_164_sar), .izq(c5[29]), .der(pixelpersonaje_195_siz), .dir(in_1),
    .sar(pixelpersonaje_163_sar), .siz(pixelpersonaje_163_siz), .sde(c6[29]), .in_7(in_2), .in_5(in_3));  // open: in_8
  PixelPersonaje pixelpersonaje_164 (
    .clk(clk), .abajo(pixelpersonaje_165_sar), .izq(c5[28]), .der(pixelpersonaje_196_siz), .dir(in_1),
    .sar(pixelpersonaje_164_sar), .siz(pixelpersonaje_164_siz), .sde(c6[28]), .in_7(in_2), .in_5(in_3));  // open: in_8
  PixelPersonaje pixelpersonaje_165 (
    .clk(clk), .abajo(pixelpersonaje_166_sar), .izq(c5[27]), .der(pixelpersonaje_197_siz), .dir(in_1),
    .sar(pixelpersonaje_165_sar), .siz(pixelpersonaje_165_siz), .sde(c6[27]), .in_7(in_2), .in_5(in_3));  // open: in_8
  PixelPersonaje pixelpersonaje_166 (
    .clk(clk), .abajo(pixelpersonaje_167_sar), .izq(c5[26]), .der(pixelpersonaje_198_siz), .dir(in_1),
    .sar(pixelpersonaje_166_sar), .siz(pixelpersonaje_166_siz), .sde(c6[26]), .in_7(in_2), .in_5(in_3));  // open: in_8
  PixelPersonaje pixelpersonaje_167 (
    .clk(clk), .abajo(pixelpersonaje_168_sar), .izq(c5[25]), .der(pixelpersonaje_199_siz), .dir(in_1),
    .sar(pixelpersonaje_167_sar), .siz(pixelpersonaje_167_siz), .sde(c6[25]), .in_7(in_2), .in_5(in_3));  // open: in_8
  PixelPersonaje pixelpersonaje_168 (
    .clk(clk), .abajo(pixelpersonaje_169_sar), .izq(c5[24]), .der(pixelpersonaje_200_siz), .dir(in_1),
    .sar(pixelpersonaje_168_sar), .siz(pixelpersonaje_168_siz), .sde(c6[24]), .in_7(in_2), .in_5(in_3));  // open: in_8
  PixelPersonaje pixelpersonaje_169 (
    .clk(clk), .abajo(pixelpersonaje_170_sar), .izq(c5[23]), .der(pixelpersonaje_201_siz), .dir(in_1),
    .sar(pixelpersonaje_169_sar), .siz(pixelpersonaje_169_siz), .sde(c6[23]), .in_7(in_2), .in_5(in_3));  // open: in_8
  PixelPersonaje pixelpersonaje_170 (
    .clk(clk), .abajo(pixelpersonaje_171_sar), .izq(c5[22]), .der(pixelpersonaje_202_siz), .dir(in_1),
    .sar(pixelpersonaje_170_sar), .siz(pixelpersonaje_170_siz), .sde(c6[22]), .in_7(in_2), .in_5(in_3));  // open: in_8
  PixelPersonaje pixelpersonaje_171 (
    .clk(clk), .abajo(pixelpersonaje_172_sar), .izq(c5[21]), .der(pixelpersonaje_203_siz), .dir(in_1),
    .sar(pixelpersonaje_171_sar), .siz(pixelpersonaje_171_siz), .sde(c6[21]), .in_7(in_2), .in_5(in_3));  // open: in_8
  PixelPersonaje pixelpersonaje_172 (
    .clk(clk), .abajo(pixelpersonaje_173_sar), .izq(c5[20]), .der(pixelpersonaje_204_siz), .dir(in_1),
    .sar(pixelpersonaje_172_sar), .siz(pixelpersonaje_172_siz), .sde(c6[20]), .in_7(in_2), .in_5(in_3));  // open: in_8
  PixelPersonaje pixelpersonaje_173 (
    .clk(clk), .abajo(pixelpersonaje_174_sar), .izq(c5[19]), .der(pixelpersonaje_205_siz), .dir(in_1),
    .sar(pixelpersonaje_173_sar), .siz(pixelpersonaje_173_siz), .sde(c6[19]), .in_7(in_2), .in_5(in_3));  // open: in_8
  PixelPersonaje pixelpersonaje_174 (
    .clk(clk), .abajo(pixelpersonaje_175_sar), .izq(c5[18]), .der(pixelpersonaje_206_siz), .dir(in_1),
    .sar(pixelpersonaje_174_sar), .siz(pixelpersonaje_174_siz), .sde(c6[18]), .in_7(in_2), .in_5(in_3));  // open: in_8
  PixelPersonaje pixelpersonaje_175 (
    .clk(clk), .abajo(pixelpersonaje_176_sar), .izq(c5[17]), .der(pixelpersonaje_207_siz), .dir(in_1),
    .sar(pixelpersonaje_175_sar), .siz(pixelpersonaje_175_siz), .sde(c6[17]), .in_7(in_2), .in_5(in_3));  // open: in_8
  PixelPersonaje pixelpersonaje_176 (
    .clk(clk), .abajo(pixelpersonaje_177_sar), .izq(c5[16]), .der(pixelpersonaje_208_siz), .dir(in_1),
    .sar(pixelpersonaje_176_sar), .siz(pixelpersonaje_176_siz), .sde(c6[16]), .in_7(in_2), .in_5(in_3));  // open: in_8
  PixelPersonaje pixelpersonaje_177 (
    .clk(clk), .abajo(pixelpersonaje_178_sar), .izq(c5[15]), .der(pixelpersonaje_209_siz), .dir(in_1),
    .sar(pixelpersonaje_177_sar), .siz(pixelpersonaje_177_siz), .sde(c6[15]), .in_7(in_2), .in_5(in_3));  // open: in_8
  PixelPersonaje pixelpersonaje_178 (
    .clk(clk), .abajo(pixelpersonaje_179_sar), .izq(c5[14]), .der(pixelpersonaje_210_siz), .dir(in_1),
    .sar(pixelpersonaje_178_sar), .siz(pixelpersonaje_178_siz), .sde(c6[14]), .in_7(in_2), .in_5(in_3));  // open: in_8
  PixelPersonaje pixelpersonaje_179 (
    .clk(clk), .abajo(pixelpersonaje_180_sar), .izq(c5[13]), .der(pixelpersonaje_211_siz), .dir(in_1),
    .sar(pixelpersonaje_179_sar), .siz(pixelpersonaje_179_siz), .sde(c6[13]), .in_7(in_2), .in_5(in_3));  // open: in_8
  PixelPersonaje pixelpersonaje_180 (
    .clk(clk), .abajo(pixelpersonaje_181_sar), .izq(c5[12]), .der(pixelpersonaje_212_siz), .dir(in_1),
    .sar(pixelpersonaje_180_sar), .siz(pixelpersonaje_180_siz), .sde(c6[12]), .in_7(in_2), .in_5(in_3));  // open: in_8
  PixelPersonaje pixelpersonaje_181 (
    .clk(clk), .abajo(pixelpersonaje_182_sar), .izq(c5[11]), .der(pixelpersonaje_213_siz), .dir(in_1),
    .sar(pixelpersonaje_181_sar), .siz(pixelpersonaje_181_siz), .sde(c6[11]), .in_7(in_2), .in_5(in_3));  // open: in_8
  PixelPersonaje pixelpersonaje_182 (
    .clk(clk), .abajo(pixelpersonaje_183_sar), .izq(c5[10]), .der(pixelpersonaje_214_siz), .dir(in_1),
    .sar(pixelpersonaje_182_sar), .siz(pixelpersonaje_182_siz), .sde(c6[10]), .in_7(in_2), .in_5(in_3));  // open: in_8
  PixelPersonaje pixelpersonaje_183 (
    .clk(clk), .abajo(pixelpersonaje_184_sar), .izq(c5[9]), .der(pixelpersonaje_215_siz), .dir(in_1),
    .sar(pixelpersonaje_183_sar), .siz(pixelpersonaje_183_siz), .sde(c6[9]), .in_7(in_2), .in_5(in_3));  // open: in_8
  PixelPersonaje pixelpersonaje_184 (
    .clk(clk), .abajo(pixelpersonaje_185_sar), .izq(c5[8]), .der(pixelpersonaje_216_siz), .dir(in_1),
    .sar(pixelpersonaje_184_sar), .siz(pixelpersonaje_184_siz), .sde(c6[8]), .in_7(in_2), .in_5(in_3));  // open: in_8
  PixelPersonaje pixelpersonaje_185 (
    .clk(clk), .abajo(pixelpersonaje_186_sar), .izq(c5[7]), .der(pixelpersonaje_217_siz), .dir(in_1),
    .sar(pixelpersonaje_185_sar), .siz(pixelpersonaje_185_siz), .sde(c6[7]), .in_7(in_2), .in_5(in_3));  // open: in_8
  PixelPersonaje pixelpersonaje_186 (
    .clk(clk), .abajo(pixelpersonaje_187_sar), .izq(c5[6]), .der(pixelpersonaje_218_siz), .dir(in_1),
    .sar(pixelpersonaje_186_sar), .siz(pixelpersonaje_186_siz), .sde(c6[6]), .in_7(in_2), .in_5(in_3));  // open: in_8
  PixelPersonaje pixelpersonaje_187 (
    .clk(clk), .abajo(pixelpersonaje_188_sar), .izq(c5[5]), .der(pixelpersonaje_219_siz), .dir(in_1),
    .sar(pixelpersonaje_187_sar), .siz(pixelpersonaje_187_siz), .sde(c6[5]), .in_7(in_2), .in_5(in_3));  // open: in_8
  PixelPersonaje pixelpersonaje_188 (
    .clk(clk), .abajo(pixelpersonaje_189_sar), .izq(c5[4]), .der(pixelpersonaje_220_siz), .dir(in_1),
    .sar(pixelpersonaje_188_sar), .siz(pixelpersonaje_188_siz), .sde(c6[4]), .in_7(in_2), .in_5(in_3));  // open: in_8
  PixelPersonaje pixelpersonaje_189 (
    .clk(clk), .abajo(pixelpersonaje_190_sar), .izq(c5[3]), .der(pixelpersonaje_221_siz), .dir(in_1),
    .sar(pixelpersonaje_189_sar), .siz(pixelpersonaje_189_siz), .sde(c6[3]), .in_7(in_2), .in_5(in_3));  // open: in_8
  PixelPersonaje pixelpersonaje_190 (
    .clk(clk), .abajo(pixelpersonaje_191_sar), .izq(c5[2]), .der(pixelpersonaje_222_siz), .dir(in_1),
    .sar(pixelpersonaje_190_sar), .siz(pixelpersonaje_190_siz), .sde(c6[2]), .in_8(s5os6), .in_7(in_2),
    .in_5(in_3));
  PixelPersonaje pixelpersonaje_191 (
    .clk(clk), .abajo(pixelpersonaje_192_sar), .izq(c5[1]), .der(pixelpersonaje_223_siz), .dir(in_1),
    .sar(pixelpersonaje_191_sar), .siz(pixelpersonaje_191_siz), .sde(c6[1]), .in_8(s5os6), .in_7(in_2),
    .in_5(in_3));
  PixelPersonaje pixelpersonaje_192 (
    .clk(clk), .abajo(c6[31]), .izq(c5[0]), .der(pixelpersonaje_224_siz), .dir(in_1),
    .sar(pixelpersonaje_192_sar), .siz(pixelpersonaje_192_siz), .sde(c6[0]), .in_7(in_2), .in_5(in_3));  // open: in_8
  Clock clock_1 (.out(clock_1_out));
  PixelPersonaje pixelpersonaje_193 (
    .clk(clk), .abajo(pixelpersonaje_194_sar), .izq(c6[31]), .der(pixelpersonaje_225_siz), .dir(in_1),
    .siz(pixelpersonaje_193_siz), .sde(c7[31]), .in_7(in_2), .in_5(in_3));  // open: sar, in_8
  PixelPersonaje pixelpersonaje_194 (
    .clk(clk), .abajo(pixelpersonaje_195_sar), .izq(c6[30]), .der(pixelpersonaje_226_siz), .dir(in_1),
    .sar(pixelpersonaje_194_sar), .siz(pixelpersonaje_194_siz), .sde(c7[30]), .in_7(in_2), .in_5(in_3));  // open: in_8
  PixelPersonaje pixelpersonaje_195 (
    .clk(clk), .abajo(pixelpersonaje_196_sar), .izq(c6[29]), .der(pixelpersonaje_227_siz), .dir(in_1),
    .sar(pixelpersonaje_195_sar), .siz(pixelpersonaje_195_siz), .sde(c7[29]), .in_7(in_2), .in_5(in_3));  // open: in_8
  PixelPersonaje pixelpersonaje_196 (
    .clk(clk), .abajo(pixelpersonaje_197_sar), .izq(c6[28]), .der(pixelpersonaje_228_siz), .dir(in_1),
    .sar(pixelpersonaje_196_sar), .siz(pixelpersonaje_196_siz), .sde(c7[28]), .in_7(in_2), .in_5(in_3));  // open: in_8
  PixelPersonaje pixelpersonaje_197 (
    .clk(clk), .abajo(pixelpersonaje_198_sar), .izq(c6[27]), .der(pixelpersonaje_229_siz), .dir(in_1),
    .sar(pixelpersonaje_197_sar), .siz(pixelpersonaje_197_siz), .sde(c7[27]), .in_7(in_2), .in_5(in_3));  // open: in_8
  PixelPersonaje pixelpersonaje_198 (
    .clk(clk), .abajo(pixelpersonaje_199_sar), .izq(c6[26]), .der(pixelpersonaje_230_siz), .dir(in_1),
    .sar(pixelpersonaje_198_sar), .siz(pixelpersonaje_198_siz), .sde(c7[26]), .in_7(in_2), .in_5(in_3));  // open: in_8
  PixelPersonaje pixelpersonaje_199 (
    .clk(clk), .abajo(pixelpersonaje_200_sar), .izq(c6[25]), .der(pixelpersonaje_231_siz), .dir(in_1),
    .sar(pixelpersonaje_199_sar), .siz(pixelpersonaje_199_siz), .sde(c7[25]), .in_7(in_2), .in_5(in_3));  // open: in_8
  PixelPersonaje pixelpersonaje_200 (
    .clk(clk), .abajo(pixelpersonaje_201_sar), .izq(c6[24]), .der(pixelpersonaje_232_siz), .dir(in_1),
    .sar(pixelpersonaje_200_sar), .siz(pixelpersonaje_200_siz), .sde(c7[24]), .in_7(in_2), .in_5(in_3));  // open: in_8
  PixelPersonaje pixelpersonaje_201 (
    .clk(clk), .abajo(pixelpersonaje_202_sar), .izq(c6[23]), .der(pixelpersonaje_233_siz), .dir(in_1),
    .sar(pixelpersonaje_201_sar), .siz(pixelpersonaje_201_siz), .sde(c7[23]), .in_7(in_2), .in_5(in_3));  // open: in_8
  PixelPersonaje pixelpersonaje_202 (
    .clk(clk), .abajo(pixelpersonaje_203_sar), .izq(c6[22]), .der(pixelpersonaje_234_siz), .dir(in_1),
    .sar(pixelpersonaje_202_sar), .siz(pixelpersonaje_202_siz), .sde(c7[22]), .in_7(in_2), .in_5(in_3));  // open: in_8
  PixelPersonaje pixelpersonaje_203 (
    .clk(clk), .abajo(pixelpersonaje_204_sar), .izq(c6[21]), .der(pixelpersonaje_235_siz), .dir(in_1),
    .sar(pixelpersonaje_203_sar), .siz(pixelpersonaje_203_siz), .sde(c7[21]), .in_7(in_2), .in_5(in_3));  // open: in_8
  PixelPersonaje pixelpersonaje_204 (
    .clk(clk), .abajo(pixelpersonaje_205_sar), .izq(c6[20]), .der(pixelpersonaje_236_siz), .dir(in_1),
    .sar(pixelpersonaje_204_sar), .siz(pixelpersonaje_204_siz), .sde(c7[20]), .in_7(in_2), .in_5(in_3));  // open: in_8
  PixelPersonaje pixelpersonaje_205 (
    .clk(clk), .abajo(pixelpersonaje_206_sar), .izq(c6[19]), .der(pixelpersonaje_237_siz), .dir(in_1),
    .sar(pixelpersonaje_205_sar), .siz(pixelpersonaje_205_siz), .sde(c7[19]), .in_7(in_2), .in_5(in_3));  // open: in_8
  PixelPersonaje pixelpersonaje_206 (
    .clk(clk), .abajo(pixelpersonaje_207_sar), .izq(c6[18]), .der(pixelpersonaje_238_siz), .dir(in_1),
    .sar(pixelpersonaje_206_sar), .siz(pixelpersonaje_206_siz), .sde(c7[18]), .in_7(in_2), .in_5(in_3));  // open: in_8
  PixelPersonaje pixelpersonaje_207 (
    .clk(clk), .abajo(pixelpersonaje_208_sar), .izq(c6[17]), .der(pixelpersonaje_239_siz), .dir(in_1),
    .sar(pixelpersonaje_207_sar), .siz(pixelpersonaje_207_siz), .sde(c7[17]), .in_7(in_2), .in_5(in_3));  // open: in_8
  PixelPersonaje pixelpersonaje_208 (
    .clk(clk), .abajo(pixelpersonaje_209_sar), .izq(c6[16]), .der(pixelpersonaje_240_siz), .dir(in_1),
    .sar(pixelpersonaje_208_sar), .siz(pixelpersonaje_208_siz), .sde(c7[16]), .in_7(in_2), .in_5(in_3));  // open: in_8
  PixelPersonaje pixelpersonaje_209 (
    .clk(clk), .abajo(pixelpersonaje_210_sar), .izq(c6[15]), .der(pixelpersonaje_241_siz), .dir(in_1),
    .sar(pixelpersonaje_209_sar), .siz(pixelpersonaje_209_siz), .sde(c7[15]), .in_7(in_2), .in_5(in_3));  // open: in_8
  PixelPersonaje pixelpersonaje_210 (
    .clk(clk), .abajo(pixelpersonaje_211_sar), .izq(c6[14]), .der(pixelpersonaje_242_siz), .dir(in_1),
    .sar(pixelpersonaje_210_sar), .siz(pixelpersonaje_210_siz), .sde(c7[14]), .in_7(in_2), .in_5(in_3));  // open: in_8
  PixelPersonaje pixelpersonaje_211 (
    .clk(clk), .abajo(pixelpersonaje_212_sar), .izq(c6[13]), .der(pixelpersonaje_243_siz), .dir(in_1),
    .sar(pixelpersonaje_211_sar), .siz(pixelpersonaje_211_siz), .sde(c7[13]), .in_7(in_2), .in_5(in_3));  // open: in_8
  PixelPersonaje pixelpersonaje_212 (
    .clk(clk), .abajo(pixelpersonaje_213_sar), .izq(c6[12]), .der(pixelpersonaje_244_siz), .dir(in_1),
    .sar(pixelpersonaje_212_sar), .siz(pixelpersonaje_212_siz), .sde(c7[12]), .in_7(in_2), .in_5(in_3));  // open: in_8
  PixelPersonaje pixelpersonaje_213 (
    .clk(clk), .abajo(pixelpersonaje_214_sar), .izq(c6[11]), .der(pixelpersonaje_245_siz), .dir(in_1),
    .sar(pixelpersonaje_213_sar), .siz(pixelpersonaje_213_siz), .sde(c7[11]), .in_7(in_2), .in_5(in_3));  // open: in_8
  PixelPersonaje pixelpersonaje_214 (
    .clk(clk), .abajo(pixelpersonaje_215_sar), .izq(c6[10]), .der(pixelpersonaje_246_siz), .dir(in_1),
    .sar(pixelpersonaje_214_sar), .siz(pixelpersonaje_214_siz), .sde(c7[10]), .in_7(in_2), .in_5(in_3));  // open: in_8
  PixelPersonaje pixelpersonaje_215 (
    .clk(clk), .abajo(pixelpersonaje_216_sar), .izq(c6[9]), .der(pixelpersonaje_247_siz), .dir(in_1),
    .sar(pixelpersonaje_215_sar), .siz(pixelpersonaje_215_siz), .sde(c7[9]), .in_7(in_2), .in_5(in_3));  // open: in_8
  PixelPersonaje pixelpersonaje_216 (
    .clk(clk), .abajo(pixelpersonaje_217_sar), .izq(c6[8]), .der(pixelpersonaje_248_siz), .dir(in_1),
    .sar(pixelpersonaje_216_sar), .siz(pixelpersonaje_216_siz), .sde(c7[8]), .in_7(in_2), .in_5(in_3));  // open: in_8
  PixelPersonaje pixelpersonaje_217 (
    .clk(clk), .abajo(pixelpersonaje_218_sar), .izq(c6[7]), .der(pixelpersonaje_249_siz), .dir(in_1),
    .sar(pixelpersonaje_217_sar), .siz(pixelpersonaje_217_siz), .sde(c7[7]), .in_7(in_2), .in_5(in_3));  // open: in_8
  PixelPersonaje pixelpersonaje_218 (
    .clk(clk), .abajo(pixelpersonaje_219_sar), .izq(c6[6]), .der(pixelpersonaje_250_siz), .dir(in_1),
    .sar(pixelpersonaje_218_sar), .siz(pixelpersonaje_218_siz), .sde(c7[6]), .in_7(in_2), .in_5(in_3));  // open: in_8
  PixelPersonaje pixelpersonaje_219 (
    .clk(clk), .abajo(pixelpersonaje_220_sar), .izq(c6[5]), .der(pixelpersonaje_251_siz), .dir(in_1),
    .sar(pixelpersonaje_219_sar), .siz(pixelpersonaje_219_siz), .sde(c7[5]), .in_7(in_2), .in_5(in_3));  // open: in_8
  PixelPersonaje pixelpersonaje_220 (
    .clk(clk), .abajo(pixelpersonaje_221_sar), .izq(c6[4]), .der(pixelpersonaje_252_siz), .dir(in_1),
    .sar(pixelpersonaje_220_sar), .siz(pixelpersonaje_220_siz), .sde(c7[4]), .in_7(in_2), .in_5(in_3));  // open: in_8
  PixelPersonaje pixelpersonaje_221 (
    .clk(clk), .abajo(pixelpersonaje_222_sar), .izq(c6[3]), .der(pixelpersonaje_253_siz), .dir(in_1),
    .sar(pixelpersonaje_221_sar), .siz(pixelpersonaje_221_siz), .sde(c7[3]), .in_7(in_2), .in_5(in_3));  // open: in_8
  PixelPersonaje pixelpersonaje_222 (
    .clk(clk), .abajo(pixelpersonaje_223_sar), .izq(c6[2]), .der(pixelpersonaje_254_siz), .dir(in_1),
    .sar(pixelpersonaje_222_sar), .siz(pixelpersonaje_222_siz), .sde(c7[2]), .in_8(s6os7), .in_7(in_2),
    .in_5(in_3));
  PixelPersonaje pixelpersonaje_223 (
    .clk(clk), .abajo(pixelpersonaje_224_sar), .izq(c6[1]), .der(pixelpersonaje_255_siz), .dir(in_1),
    .sar(pixelpersonaje_223_sar), .siz(pixelpersonaje_223_siz), .sde(c7[1]), .in_8(s6os7), .in_7(in_2),
    .in_5(in_3));
  PixelPersonaje pixelpersonaje_224 (
    .clk(clk), .abajo(c7[31]), .izq(c6[0]), .der(pixelpersonaje_256_siz), .dir(in_1),
    .sar(pixelpersonaje_224_sar), .siz(pixelpersonaje_224_siz), .sde(c7[0]), .in_7(in_2), .in_5(in_3));  // open: in_8
  Random_part #(.width(4)) random_1 (.clk(undriven), .out(out_22));  // open: next, clr
  Random_part #(.width(4)) random_2 (.clk(clock_1_out), .next(1'b1), .out(random_2_out));  // open: clr
  Demultiplexer #(.select(4)) demultiplexer_1 (
    .out0(s1), .out1(s2), .out2(s3), .out3(s4), .out4(s4), .out5(s6), .out6(s7), .out7(s8), .out8(s9),
    .out9(s10), .out10(s11), .out11(s12), .out12(s13), .out13(s14), .out14(s15), .out15(s16), .in(in_4),
    .sel(random_2_out), .en(in_5));
  PixelPersonaje pixelpersonaje_225 (
    .clk(clk), .abajo(pixelpersonaje_226_sar), .izq(c7[31]), .der(pixelpersonaje_257_siz), .dir(in_1),
    .siz(pixelpersonaje_225_siz), .sde(c8[31]), .in_7(in_2), .in_5(in_3));  // open: sar, in_8
  PixelPersonaje pixelpersonaje_226 (
    .clk(clk), .abajo(pixelpersonaje_227_sar), .izq(c7[30]), .der(pixelpersonaje_258_siz), .dir(in_1),
    .sar(pixelpersonaje_226_sar), .siz(pixelpersonaje_226_siz), .sde(c8[30]), .in_7(in_2), .in_5(in_3));  // open: in_8
  PixelPersonaje pixelpersonaje_227 (
    .clk(clk), .abajo(pixelpersonaje_228_sar), .izq(c7[29]), .der(pixelpersonaje_259_siz), .dir(in_1),
    .sar(pixelpersonaje_227_sar), .siz(pixelpersonaje_227_siz), .sde(c8[29]), .in_7(in_2), .in_5(in_3));  // open: in_8
  PixelPersonaje pixelpersonaje_228 (
    .clk(clk), .abajo(pixelpersonaje_229_sar), .izq(c7[28]), .der(pixelpersonaje_260_siz), .dir(in_1),
    .sar(pixelpersonaje_228_sar), .siz(pixelpersonaje_228_siz), .sde(c8[28]), .in_7(in_2), .in_5(in_3));  // open: in_8
  PixelPersonaje pixelpersonaje_229 (
    .clk(clk), .abajo(pixelpersonaje_230_sar), .izq(c7[27]), .der(pixelpersonaje_261_siz), .dir(in_1),
    .sar(pixelpersonaje_229_sar), .siz(pixelpersonaje_229_siz), .sde(c8[27]), .in_7(in_2), .in_5(in_3));  // open: in_8
  PixelPersonaje pixelpersonaje_230 (
    .clk(clk), .abajo(pixelpersonaje_231_sar), .izq(c7[26]), .der(pixelpersonaje_262_siz), .dir(in_1),
    .sar(pixelpersonaje_230_sar), .siz(pixelpersonaje_230_siz), .sde(c8[26]), .in_7(in_2), .in_5(in_3));  // open: in_8
  PixelPersonaje pixelpersonaje_231 (
    .clk(clk), .abajo(pixelpersonaje_232_sar), .izq(c7[25]), .der(pixelpersonaje_263_siz), .dir(in_1),
    .sar(pixelpersonaje_231_sar), .siz(pixelpersonaje_231_siz), .sde(c8[25]), .in_7(in_2), .in_5(in_3));  // open: in_8
  PixelPersonaje pixelpersonaje_232 (
    .clk(clk), .abajo(pixelpersonaje_233_sar), .izq(c7[24]), .der(pixelpersonaje_264_siz), .dir(in_1),
    .sar(pixelpersonaje_232_sar), .siz(pixelpersonaje_232_siz), .sde(c8[24]), .in_7(in_2), .in_5(in_3));  // open: in_8
  PixelPersonaje pixelpersonaje_233 (
    .clk(clk), .abajo(pixelpersonaje_234_sar), .izq(c7[23]), .der(pixelpersonaje_265_siz), .dir(in_1),
    .sar(pixelpersonaje_233_sar), .siz(pixelpersonaje_233_siz), .sde(c8[23]), .in_7(in_2), .in_5(in_3));  // open: in_8
  PixelPersonaje pixelpersonaje_234 (
    .clk(clk), .abajo(pixelpersonaje_235_sar), .izq(c7[22]), .der(pixelpersonaje_266_siz), .dir(in_1),
    .sar(pixelpersonaje_234_sar), .siz(pixelpersonaje_234_siz), .sde(c8[22]), .in_7(in_2), .in_5(in_3));  // open: in_8
  PixelPersonaje pixelpersonaje_235 (
    .clk(clk), .abajo(pixelpersonaje_236_sar), .izq(c7[21]), .der(pixelpersonaje_267_siz), .dir(in_1),
    .sar(pixelpersonaje_235_sar), .siz(pixelpersonaje_235_siz), .sde(c8[21]), .in_7(in_2), .in_5(in_3));  // open: in_8
  PixelPersonaje pixelpersonaje_236 (
    .clk(clk), .abajo(pixelpersonaje_237_sar), .izq(c7[20]), .der(pixelpersonaje_268_siz), .dir(in_1),
    .sar(pixelpersonaje_236_sar), .siz(pixelpersonaje_236_siz), .sde(c8[20]), .in_7(in_2), .in_5(in_3));  // open: in_8
  PixelPersonaje pixelpersonaje_237 (
    .clk(clk), .abajo(pixelpersonaje_238_sar), .izq(c7[19]), .der(pixelpersonaje_269_siz), .dir(in_1),
    .sar(pixelpersonaje_237_sar), .siz(pixelpersonaje_237_siz), .sde(c8[19]), .in_7(in_2), .in_5(in_3));  // open: in_8
  PixelPersonaje pixelpersonaje_238 (
    .clk(clk), .abajo(pixelpersonaje_239_sar), .izq(c7[18]), .der(pixelpersonaje_270_siz), .dir(in_1),
    .sar(pixelpersonaje_238_sar), .siz(pixelpersonaje_238_siz), .sde(c8[18]), .in_7(in_2), .in_5(in_3));  // open: in_8
  PixelPersonaje pixelpersonaje_239 (
    .clk(clk), .abajo(pixelpersonaje_240_sar), .izq(c7[17]), .der(pixelpersonaje_271_siz), .dir(in_1),
    .sar(pixelpersonaje_239_sar), .siz(pixelpersonaje_239_siz), .sde(c8[17]), .in_7(in_2), .in_5(in_3));  // open: in_8
  PixelPersonaje pixelpersonaje_240 (
    .clk(clk), .abajo(pixelpersonaje_241_sar), .izq(c7[16]), .der(pixelpersonaje_272_siz), .dir(in_1),
    .sar(pixelpersonaje_240_sar), .siz(pixelpersonaje_240_siz), .sde(c8[16]), .in_7(in_2), .in_5(in_3));  // open: in_8
  PixelPersonaje pixelpersonaje_241 (
    .clk(clk), .abajo(pixelpersonaje_242_sar), .izq(c7[15]), .der(pixelpersonaje_273_siz), .dir(in_1),
    .sar(pixelpersonaje_241_sar), .siz(pixelpersonaje_241_siz), .sde(c8[15]), .in_7(in_2), .in_5(in_3));  // open: in_8
  PixelPersonaje pixelpersonaje_242 (
    .clk(clk), .abajo(pixelpersonaje_243_sar), .izq(c7[14]), .der(pixelpersonaje_274_siz), .dir(in_1),
    .sar(pixelpersonaje_242_sar), .siz(pixelpersonaje_242_siz), .sde(c8[14]), .in_7(in_2), .in_5(in_3));  // open: in_8
  PixelPersonaje pixelpersonaje_243 (
    .clk(clk), .abajo(pixelpersonaje_244_sar), .izq(c7[13]), .der(pixelpersonaje_275_siz), .dir(in_1),
    .sar(pixelpersonaje_243_sar), .siz(pixelpersonaje_243_siz), .sde(c8[13]), .in_7(in_2), .in_5(in_3));  // open: in_8
  PixelPersonaje pixelpersonaje_244 (
    .clk(clk), .abajo(pixelpersonaje_245_sar), .izq(c7[12]), .der(pixelpersonaje_276_siz), .dir(in_1),
    .sar(pixelpersonaje_244_sar), .siz(pixelpersonaje_244_siz), .sde(c8[12]), .in_7(in_2), .in_5(in_3));  // open: in_8
  PixelPersonaje pixelpersonaje_245 (
    .clk(clk), .abajo(pixelpersonaje_246_sar), .izq(c7[11]), .der(pixelpersonaje_277_siz), .dir(in_1),
    .sar(pixelpersonaje_245_sar), .siz(pixelpersonaje_245_siz), .sde(c8[11]), .in_7(in_2), .in_5(in_3));  // open: in_8
  PixelPersonaje pixelpersonaje_246 (
    .clk(clk), .abajo(pixelpersonaje_247_sar), .izq(c7[10]), .der(pixelpersonaje_278_siz), .dir(in_1),
    .sar(pixelpersonaje_246_sar), .siz(pixelpersonaje_246_siz), .sde(c8[10]), .in_7(in_2), .in_5(in_3));  // open: in_8
  PixelPersonaje pixelpersonaje_247 (
    .clk(clk), .abajo(pixelpersonaje_248_sar), .izq(c7[9]), .der(pixelpersonaje_279_siz), .dir(in_1),
    .sar(pixelpersonaje_247_sar), .siz(pixelpersonaje_247_siz), .sde(c8[9]), .in_7(in_2), .in_5(in_3));  // open: in_8
  PixelPersonaje pixelpersonaje_248 (
    .clk(clk), .abajo(pixelpersonaje_249_sar), .izq(c7[8]), .der(pixelpersonaje_280_siz), .dir(in_1),
    .sar(pixelpersonaje_248_sar), .siz(pixelpersonaje_248_siz), .sde(c8[8]), .in_7(in_2), .in_5(in_3));  // open: in_8
  PixelPersonaje pixelpersonaje_249 (
    .clk(clk), .abajo(pixelpersonaje_250_sar), .izq(c7[7]), .der(pixelpersonaje_281_siz), .dir(in_1),
    .sar(pixelpersonaje_249_sar), .siz(pixelpersonaje_249_siz), .sde(c8[7]), .in_7(in_2), .in_5(in_3));  // open: in_8
  PixelPersonaje pixelpersonaje_250 (
    .clk(clk), .abajo(pixelpersonaje_251_sar), .izq(c7[6]), .der(pixelpersonaje_282_siz), .dir(in_1),
    .sar(pixelpersonaje_250_sar), .siz(pixelpersonaje_250_siz), .sde(c8[6]), .in_7(in_2), .in_5(in_3));  // open: in_8
  PixelPersonaje pixelpersonaje_251 (
    .clk(clk), .abajo(pixelpersonaje_252_sar), .izq(c7[5]), .der(pixelpersonaje_283_siz), .dir(in_1),
    .sar(pixelpersonaje_251_sar), .siz(pixelpersonaje_251_siz), .sde(c8[5]), .in_7(in_2), .in_5(in_3));  // open: in_8
  PixelPersonaje pixelpersonaje_252 (
    .clk(clk), .abajo(pixelpersonaje_253_sar), .izq(c7[4]), .der(pixelpersonaje_284_siz), .dir(in_1),
    .sar(pixelpersonaje_252_sar), .siz(pixelpersonaje_252_siz), .sde(c8[4]), .in_7(in_2), .in_5(in_3));  // open: in_8
  PixelPersonaje pixelpersonaje_253 (
    .clk(clk), .abajo(pixelpersonaje_254_sar), .izq(c7[3]), .der(pixelpersonaje_285_siz), .dir(in_1),
    .sar(pixelpersonaje_253_sar), .siz(pixelpersonaje_253_siz), .sde(c8[3]), .in_7(in_2), .in_5(in_3));  // open: in_8
  PixelPersonaje pixelpersonaje_254 (
    .clk(clk), .abajo(pixelpersonaje_255_sar), .izq(c7[2]), .der(pixelpersonaje_286_siz), .dir(in_1),
    .sar(pixelpersonaje_254_sar), .siz(pixelpersonaje_254_siz), .sde(c8[2]), .in_8(s7os8), .in_7(in_2),
    .in_5(in_3));
  PixelPersonaje pixelpersonaje_255 (
    .clk(clk), .abajo(pixelpersonaje_256_sar), .izq(c7[1]), .der(pixelpersonaje_287_siz), .dir(in_1),
    .sar(pixelpersonaje_255_sar), .siz(pixelpersonaje_255_siz), .sde(c8[1]), .in_8(s7os8), .in_7(in_2),
    .in_5(in_3));
  PixelPersonaje pixelpersonaje_256 (
    .clk(clk), .abajo(c8[31]), .izq(c7[0]), .der(pixelpersonaje_288_siz), .dir(in_1),
    .sar(pixelpersonaje_256_sar), .siz(pixelpersonaje_256_siz), .sde(c8[0]), .in_7(in_2), .in_5(in_3));  // open: in_8
  PixelPersonaje pixelpersonaje_257 (
    .clk(clk), .abajo(pixelpersonaje_258_sar), .izq(c8[31]), .der(pixelpersonaje_289_siz), .dir(in_1),
    .siz(pixelpersonaje_257_siz), .sde(c9[31]), .in_7(in_2), .in_5(in_3));  // open: sar, in_8
  PixelPersonaje pixelpersonaje_258 (
    .clk(clk), .abajo(pixelpersonaje_259_sar), .izq(c8[30]), .der(pixelpersonaje_290_siz), .dir(in_1),
    .sar(pixelpersonaje_258_sar), .siz(pixelpersonaje_258_siz), .sde(c9[30]), .in_7(in_2), .in_5(in_3));  // open: in_8
  PixelPersonaje pixelpersonaje_259 (
    .clk(clk), .abajo(pixelpersonaje_260_sar), .izq(c8[29]), .der(pixelpersonaje_291_siz), .dir(in_1),
    .sar(pixelpersonaje_259_sar), .siz(pixelpersonaje_259_siz), .sde(c9[29]), .in_7(in_2), .in_5(in_3));  // open: in_8
  PixelPersonaje pixelpersonaje_260 (
    .clk(clk), .abajo(pixelpersonaje_261_sar), .izq(c8[28]), .der(pixelpersonaje_292_siz), .dir(in_1),
    .sar(pixelpersonaje_260_sar), .siz(pixelpersonaje_260_siz), .sde(c9[28]), .in_7(in_2), .in_5(in_3));  // open: in_8
  PixelPersonaje pixelpersonaje_261 (
    .clk(clk), .abajo(pixelpersonaje_262_sar), .izq(c8[27]), .der(pixelpersonaje_293_siz), .dir(in_1),
    .sar(pixelpersonaje_261_sar), .siz(pixelpersonaje_261_siz), .sde(c9[27]), .in_7(in_2), .in_5(in_3));  // open: in_8
  PixelPersonaje pixelpersonaje_262 (
    .clk(clk), .abajo(pixelpersonaje_263_sar), .izq(c8[26]), .der(pixelpersonaje_294_siz), .dir(in_1),
    .sar(pixelpersonaje_262_sar), .siz(pixelpersonaje_262_siz), .sde(c9[26]), .in_7(in_2), .in_5(in_3));  // open: in_8
  PixelPersonaje pixelpersonaje_263 (
    .clk(clk), .abajo(pixelpersonaje_264_sar), .izq(c8[25]), .der(pixelpersonaje_295_siz), .dir(in_1),
    .sar(pixelpersonaje_263_sar), .siz(pixelpersonaje_263_siz), .sde(c9[25]), .in_7(in_2), .in_5(in_3));  // open: in_8
  PixelPersonaje pixelpersonaje_264 (
    .clk(clk), .abajo(pixelpersonaje_265_sar), .izq(c8[24]), .der(pixelpersonaje_296_siz), .dir(in_1),
    .sar(pixelpersonaje_264_sar), .siz(pixelpersonaje_264_siz), .sde(c9[24]), .in_7(in_2), .in_5(in_3));  // open: in_8
  PixelPersonaje pixelpersonaje_265 (
    .clk(clk), .abajo(pixelpersonaje_266_sar), .izq(c8[23]), .der(pixelpersonaje_297_siz), .dir(in_1),
    .sar(pixelpersonaje_265_sar), .siz(pixelpersonaje_265_siz), .sde(c9[23]), .in_7(in_2), .in_5(in_3));  // open: in_8
  PixelPersonaje pixelpersonaje_266 (
    .clk(clk), .abajo(pixelpersonaje_267_sar), .izq(c8[22]), .der(pixelpersonaje_298_siz), .dir(in_1),
    .sar(pixelpersonaje_266_sar), .siz(pixelpersonaje_266_siz), .sde(c9[22]), .in_7(in_2), .in_5(in_3));  // open: in_8
  PixelPersonaje pixelpersonaje_267 (
    .clk(clk), .abajo(pixelpersonaje_268_sar), .izq(c8[21]), .der(pixelpersonaje_299_siz), .dir(in_1),
    .sar(pixelpersonaje_267_sar), .siz(pixelpersonaje_267_siz), .sde(c9[21]), .in_7(in_2), .in_5(in_3));  // open: in_8
  PixelPersonaje pixelpersonaje_268 (
    .clk(clk), .abajo(pixelpersonaje_269_sar), .izq(c8[20]), .der(pixelpersonaje_300_siz), .dir(in_1),
    .sar(pixelpersonaje_268_sar), .siz(pixelpersonaje_268_siz), .sde(c9[20]), .in_7(in_2), .in_5(in_3));  // open: in_8
  PixelPersonaje pixelpersonaje_269 (
    .clk(clk), .abajo(pixelpersonaje_270_sar), .izq(c8[19]), .der(pixelpersonaje_301_siz), .dir(in_1),
    .sar(pixelpersonaje_269_sar), .siz(pixelpersonaje_269_siz), .sde(c9[19]), .in_7(in_2), .in_5(in_3));  // open: in_8
  PixelPersonaje pixelpersonaje_270 (
    .clk(clk), .abajo(pixelpersonaje_271_sar), .izq(c8[18]), .der(pixelpersonaje_302_siz), .dir(in_1),
    .sar(pixelpersonaje_270_sar), .siz(pixelpersonaje_270_siz), .sde(c9[18]), .in_7(in_2), .in_5(in_3));  // open: in_8
  PixelPersonaje pixelpersonaje_271 (
    .clk(clk), .abajo(pixelpersonaje_272_sar), .izq(c8[17]), .der(pixelpersonaje_303_siz), .dir(in_1),
    .sar(pixelpersonaje_271_sar), .siz(pixelpersonaje_271_siz), .sde(c9[17]), .in_7(in_2), .in_5(in_3));  // open: in_8
  PixelPersonaje pixelpersonaje_272 (
    .clk(clk), .abajo(pixelpersonaje_273_sar), .izq(c8[16]), .der(pixelpersonaje_304_siz), .dir(in_1),
    .sar(pixelpersonaje_272_sar), .siz(pixelpersonaje_272_siz), .sde(c9[16]), .in_7(in_2), .in_5(in_3));  // open: in_8
  PixelPersonaje pixelpersonaje_273 (
    .clk(clk), .abajo(pixelpersonaje_274_sar), .izq(c8[15]), .der(pixelpersonaje_305_siz), .dir(in_1),
    .sar(pixelpersonaje_273_sar), .siz(pixelpersonaje_273_siz), .sde(c9[15]), .in_7(in_2), .in_5(in_3));  // open: in_8
  PixelPersonaje pixelpersonaje_274 (
    .clk(clk), .abajo(pixelpersonaje_275_sar), .izq(c8[14]), .der(pixelpersonaje_306_siz), .dir(in_1),
    .sar(pixelpersonaje_274_sar), .siz(pixelpersonaje_274_siz), .sde(c9[14]), .in_7(in_2), .in_5(in_3));  // open: in_8
  PixelPersonaje pixelpersonaje_275 (
    .clk(clk), .abajo(pixelpersonaje_276_sar), .izq(c8[13]), .der(pixelpersonaje_307_siz), .dir(in_1),
    .sar(pixelpersonaje_275_sar), .siz(pixelpersonaje_275_siz), .sde(c9[13]), .in_7(in_2), .in_5(in_3));  // open: in_8
  PixelPersonaje pixelpersonaje_276 (
    .clk(clk), .abajo(pixelpersonaje_277_sar), .izq(c8[12]), .der(pixelpersonaje_308_siz), .dir(in_1),
    .sar(pixelpersonaje_276_sar), .siz(pixelpersonaje_276_siz), .sde(c9[12]), .in_7(in_2), .in_5(in_3));  // open: in_8
  PixelPersonaje pixelpersonaje_277 (
    .clk(clk), .abajo(pixelpersonaje_278_sar), .izq(c8[11]), .der(pixelpersonaje_309_siz), .dir(in_1),
    .sar(pixelpersonaje_277_sar), .siz(pixelpersonaje_277_siz), .sde(c9[11]), .in_7(in_2), .in_5(in_3));  // open: in_8
  PixelPersonaje pixelpersonaje_278 (
    .clk(clk), .abajo(pixelpersonaje_279_sar), .izq(c8[10]), .der(pixelpersonaje_310_siz), .dir(in_1),
    .sar(pixelpersonaje_278_sar), .siz(pixelpersonaje_278_siz), .sde(c9[10]), .in_7(in_2), .in_5(in_3));  // open: in_8
  PixelPersonaje pixelpersonaje_279 (
    .clk(clk), .abajo(pixelpersonaje_280_sar), .izq(c8[9]), .der(pixelpersonaje_311_siz), .dir(in_1),
    .sar(pixelpersonaje_279_sar), .siz(pixelpersonaje_279_siz), .sde(c9[9]), .in_7(in_2), .in_5(in_3));  // open: in_8
  PixelPersonaje pixelpersonaje_280 (
    .clk(clk), .abajo(pixelpersonaje_281_sar), .izq(c8[8]), .der(pixelpersonaje_312_siz), .dir(in_1),
    .sar(pixelpersonaje_280_sar), .siz(pixelpersonaje_280_siz), .sde(c9[8]), .in_7(in_2), .in_5(in_3));  // open: in_8
  PixelPersonaje pixelpersonaje_281 (
    .clk(clk), .abajo(pixelpersonaje_282_sar), .izq(c8[7]), .der(pixelpersonaje_313_siz), .dir(in_1),
    .sar(pixelpersonaje_281_sar), .siz(pixelpersonaje_281_siz), .sde(c9[7]), .in_7(in_2), .in_5(in_3));  // open: in_8
  PixelPersonaje pixelpersonaje_282 (
    .clk(clk), .abajo(pixelpersonaje_283_sar), .izq(c8[6]), .der(pixelpersonaje_314_siz), .dir(in_1),
    .sar(pixelpersonaje_282_sar), .siz(pixelpersonaje_282_siz), .sde(c9[6]), .in_7(in_2), .in_5(in_3));  // open: in_8
  PixelPersonaje pixelpersonaje_283 (
    .clk(clk), .abajo(pixelpersonaje_284_sar), .izq(c8[5]), .der(pixelpersonaje_315_siz), .dir(in_1),
    .sar(pixelpersonaje_283_sar), .siz(pixelpersonaje_283_siz), .sde(c9[5]), .in_7(in_2), .in_5(in_3));  // open: in_8
  PixelPersonaje pixelpersonaje_284 (
    .clk(clk), .abajo(pixelpersonaje_285_sar), .izq(c8[4]), .der(pixelpersonaje_316_siz), .dir(in_1),
    .sar(pixelpersonaje_284_sar), .siz(pixelpersonaje_284_siz), .sde(c9[4]), .in_7(in_2), .in_5(in_3));  // open: in_8
  PixelPersonaje pixelpersonaje_285 (
    .clk(clk), .abajo(pixelpersonaje_286_sar), .izq(c8[3]), .der(pixelpersonaje_317_siz), .dir(in_1),
    .sar(pixelpersonaje_285_sar), .siz(pixelpersonaje_285_siz), .sde(c9[3]), .in_7(in_2), .in_5(in_3));  // open: in_8
  PixelPersonaje pixelpersonaje_286 (
    .clk(clk), .abajo(pixelpersonaje_287_sar), .izq(c8[2]), .der(pixelpersonaje_318_siz), .dir(in_1),
    .sar(pixelpersonaje_286_sar), .siz(pixelpersonaje_286_siz), .sde(c9[2]), .in_8(s8os9), .in_7(in_2),
    .in_5(in_3));
  PixelPersonaje pixelpersonaje_287 (
    .clk(clk), .abajo(pixelpersonaje_288_sar), .izq(c8[1]), .der(pixelpersonaje_319_siz), .dir(in_1),
    .sar(pixelpersonaje_287_sar), .siz(pixelpersonaje_287_siz), .sde(c9[1]), .in_8(s8os9), .in_7(in_2),
    .in_5(in_3));
  PixelPersonaje pixelpersonaje_288 (
    .clk(clk), .abajo(c9[31]), .izq(c8[0]), .der(pixelpersonaje_320_siz), .dir(in_1),
    .sar(pixelpersonaje_288_sar), .siz(pixelpersonaje_288_siz), .sde(c9[0]), .in_7(in_2), .in_5(in_3));  // open: in_8
  PixelPersonaje pixelpersonaje_289 (
    .clk(clk), .abajo(pixelpersonaje_290_sar), .izq(c9[31]), .der(pixelpersonaje_321_siz), .dir(in_1),
    .siz(pixelpersonaje_289_siz), .sde(c10[31]), .in_7(in_2), .in_5(in_3));  // open: sar, in_8
  PixelPersonaje pixelpersonaje_290 (
    .clk(clk), .abajo(pixelpersonaje_291_sar), .izq(c9[30]), .der(pixelpersonaje_322_siz), .dir(in_1),
    .sar(pixelpersonaje_290_sar), .siz(pixelpersonaje_290_siz), .sde(c10[30]), .in_7(in_2), .in_5(in_3));  // open: in_8
  PixelPersonaje pixelpersonaje_291 (
    .clk(clk), .abajo(pixelpersonaje_292_sar), .izq(c9[29]), .der(pixelpersonaje_323_siz), .dir(in_1),
    .sar(pixelpersonaje_291_sar), .siz(pixelpersonaje_291_siz), .sde(c10[29]), .in_7(in_2), .in_5(in_3));  // open: in_8
  PixelPersonaje pixelpersonaje_292 (
    .clk(clk), .abajo(pixelpersonaje_293_sar), .izq(c9[28]), .der(pixelpersonaje_324_siz), .dir(in_1),
    .sar(pixelpersonaje_292_sar), .siz(pixelpersonaje_292_siz), .sde(c10[28]), .in_7(in_2), .in_5(in_3));  // open: in_8
  PixelPersonaje pixelpersonaje_293 (
    .clk(clk), .abajo(pixelpersonaje_294_sar), .izq(c9[27]), .der(pixelpersonaje_325_siz), .dir(in_1),
    .sar(pixelpersonaje_293_sar), .siz(pixelpersonaje_293_siz), .sde(c10[27]), .in_7(in_2), .in_5(in_3));  // open: in_8
  PixelPersonaje pixelpersonaje_294 (
    .clk(clk), .abajo(pixelpersonaje_295_sar), .izq(c9[26]), .der(pixelpersonaje_326_siz), .dir(in_1),
    .sar(pixelpersonaje_294_sar), .siz(pixelpersonaje_294_siz), .sde(c10[26]), .in_7(in_2), .in_5(in_3));  // open: in_8
  PixelPersonaje pixelpersonaje_295 (
    .clk(clk), .abajo(pixelpersonaje_296_sar), .izq(c9[25]), .der(pixelpersonaje_327_siz), .dir(in_1),
    .sar(pixelpersonaje_295_sar), .siz(pixelpersonaje_295_siz), .sde(c10[25]), .in_7(in_2), .in_5(in_3));  // open: in_8
  PixelPersonaje pixelpersonaje_296 (
    .clk(clk), .abajo(pixelpersonaje_297_sar), .izq(c9[24]), .der(pixelpersonaje_328_siz), .dir(in_1),
    .sar(pixelpersonaje_296_sar), .siz(pixelpersonaje_296_siz), .sde(c10[24]), .in_7(in_2), .in_5(in_3));  // open: in_8
  PixelPersonaje pixelpersonaje_297 (
    .clk(clk), .abajo(pixelpersonaje_298_sar), .izq(c9[23]), .der(pixelpersonaje_329_siz), .dir(in_1),
    .sar(pixelpersonaje_297_sar), .siz(pixelpersonaje_297_siz), .sde(c10[23]), .in_7(in_2), .in_5(in_3));  // open: in_8
  PixelPersonaje pixelpersonaje_298 (
    .clk(clk), .abajo(pixelpersonaje_299_sar), .izq(c9[22]), .der(pixelpersonaje_330_siz), .dir(in_1),
    .sar(pixelpersonaje_298_sar), .siz(pixelpersonaje_298_siz), .sde(c10[22]), .in_7(in_2), .in_5(in_3));  // open: in_8
  PixelPersonaje pixelpersonaje_299 (
    .clk(clk), .abajo(pixelpersonaje_300_sar), .izq(c9[21]), .der(pixelpersonaje_331_siz), .dir(in_1),
    .sar(pixelpersonaje_299_sar), .siz(pixelpersonaje_299_siz), .sde(c10[21]), .in_7(in_2), .in_5(in_3));  // open: in_8
  PixelPersonaje pixelpersonaje_300 (
    .clk(clk), .abajo(pixelpersonaje_301_sar), .izq(c9[20]), .der(pixelpersonaje_332_siz), .dir(in_1),
    .sar(pixelpersonaje_300_sar), .siz(pixelpersonaje_300_siz), .sde(c10[20]), .in_7(in_2), .in_5(in_3));  // open: in_8
  PixelPersonaje pixelpersonaje_301 (
    .clk(clk), .abajo(pixelpersonaje_302_sar), .izq(c9[19]), .der(pixelpersonaje_333_siz), .dir(in_1),
    .sar(pixelpersonaje_301_sar), .siz(pixelpersonaje_301_siz), .sde(c10[19]), .in_7(in_2), .in_5(in_3));  // open: in_8
  PixelPersonaje pixelpersonaje_302 (
    .clk(clk), .abajo(pixelpersonaje_303_sar), .izq(c9[18]), .der(pixelpersonaje_334_siz), .dir(in_1),
    .sar(pixelpersonaje_302_sar), .siz(pixelpersonaje_302_siz), .sde(c10[18]), .in_7(in_2), .in_5(in_3));  // open: in_8
  PixelPersonaje pixelpersonaje_303 (
    .clk(clk), .abajo(pixelpersonaje_304_sar), .izq(c9[17]), .der(pixelpersonaje_335_siz), .dir(in_1),
    .sar(pixelpersonaje_303_sar), .siz(pixelpersonaje_303_siz), .sde(c10[17]), .in_7(in_2), .in_5(in_3));  // open: in_8
  PixelPersonaje pixelpersonaje_304 (
    .clk(clk), .abajo(pixelpersonaje_305_sar), .izq(c9[16]), .der(pixelpersonaje_336_siz), .dir(in_1),
    .sar(pixelpersonaje_304_sar), .siz(pixelpersonaje_304_siz), .sde(c10[16]), .in_7(in_2), .in_5(in_3));  // open: in_8
  PixelPersonaje pixelpersonaje_305 (
    .clk(clk), .abajo(pixelpersonaje_306_sar), .izq(c9[15]), .der(pixelpersonaje_337_siz), .dir(in_1),
    .sar(pixelpersonaje_305_sar), .siz(pixelpersonaje_305_siz), .sde(c10[15]), .in_7(in_2), .in_5(in_3));  // open: in_8
  PixelPersonaje pixelpersonaje_306 (
    .clk(clk), .abajo(pixelpersonaje_307_sar), .izq(c9[14]), .der(pixelpersonaje_338_siz), .dir(in_1),
    .sar(pixelpersonaje_306_sar), .siz(pixelpersonaje_306_siz), .sde(c10[14]), .in_7(in_2), .in_5(in_3));  // open: in_8
  PixelPersonaje pixelpersonaje_307 (
    .clk(clk), .abajo(pixelpersonaje_308_sar), .izq(c9[13]), .der(pixelpersonaje_339_siz), .dir(in_1),
    .sar(pixelpersonaje_307_sar), .siz(pixelpersonaje_307_siz), .sde(c10[13]), .in_7(in_2), .in_5(in_3));  // open: in_8
  PixelPersonaje pixelpersonaje_308 (
    .clk(clk), .abajo(pixelpersonaje_309_sar), .izq(c9[12]), .der(pixelpersonaje_340_siz), .dir(in_1),
    .sar(pixelpersonaje_308_sar), .siz(pixelpersonaje_308_siz), .sde(c10[12]), .in_7(in_2), .in_5(in_3));  // open: in_8
  PixelPersonaje pixelpersonaje_309 (
    .clk(clk), .abajo(pixelpersonaje_310_sar), .izq(c9[11]), .der(pixelpersonaje_341_siz), .dir(in_1),
    .sar(pixelpersonaje_309_sar), .siz(pixelpersonaje_309_siz), .sde(c10[11]), .in_7(in_2), .in_5(in_3));  // open: in_8
  PixelPersonaje pixelpersonaje_310 (
    .clk(clk), .abajo(pixelpersonaje_311_sar), .izq(c9[10]), .der(pixelpersonaje_342_siz), .dir(in_1),
    .sar(pixelpersonaje_310_sar), .siz(pixelpersonaje_310_siz), .sde(c10[10]), .in_7(in_2), .in_5(in_3));  // open: in_8
  PixelPersonaje pixelpersonaje_311 (
    .clk(clk), .abajo(pixelpersonaje_312_sar), .izq(c9[9]), .der(pixelpersonaje_343_siz), .dir(in_1),
    .sar(pixelpersonaje_311_sar), .siz(pixelpersonaje_311_siz), .sde(c10[9]), .in_7(in_2), .in_5(in_3));  // open: in_8
  PixelPersonaje pixelpersonaje_312 (
    .clk(clk), .abajo(pixelpersonaje_313_sar), .izq(c9[8]), .der(pixelpersonaje_344_siz), .dir(in_1),
    .sar(pixelpersonaje_312_sar), .siz(pixelpersonaje_312_siz), .sde(c10[8]), .in_7(in_2), .in_5(in_3));  // open: in_8
  PixelPersonaje pixelpersonaje_313 (
    .clk(clk), .abajo(pixelpersonaje_314_sar), .izq(c9[7]), .der(pixelpersonaje_345_siz), .dir(in_1),
    .sar(pixelpersonaje_313_sar), .siz(pixelpersonaje_313_siz), .sde(c10[7]), .in_7(in_2), .in_5(in_3));  // open: in_8
  PixelPersonaje pixelpersonaje_314 (
    .clk(clk), .abajo(pixelpersonaje_315_sar), .izq(c9[6]), .der(pixelpersonaje_346_siz), .dir(in_1),
    .sar(pixelpersonaje_314_sar), .siz(pixelpersonaje_314_siz), .sde(c10[6]), .in_7(in_2), .in_5(in_3));  // open: in_8
  PixelPersonaje pixelpersonaje_315 (
    .clk(clk), .abajo(pixelpersonaje_316_sar), .izq(c9[5]), .der(pixelpersonaje_347_siz), .dir(in_1),
    .sar(pixelpersonaje_315_sar), .siz(pixelpersonaje_315_siz), .sde(c10[5]), .in_7(in_2), .in_5(in_3));  // open: in_8
  PixelPersonaje pixelpersonaje_316 (
    .clk(clk), .abajo(pixelpersonaje_317_sar), .izq(c9[4]), .der(pixelpersonaje_348_siz), .dir(in_1),
    .sar(pixelpersonaje_316_sar), .siz(pixelpersonaje_316_siz), .sde(c10[4]), .in_7(in_2), .in_5(in_3));  // open: in_8
  PixelPersonaje pixelpersonaje_317 (
    .clk(clk), .abajo(pixelpersonaje_318_sar), .izq(c9[3]), .der(pixelpersonaje_349_siz), .dir(in_1),
    .sar(pixelpersonaje_317_sar), .siz(pixelpersonaje_317_siz), .sde(c10[3]), .in_7(in_2), .in_5(in_3));  // open: in_8
  PixelPersonaje pixelpersonaje_318 (
    .clk(clk), .abajo(pixelpersonaje_319_sar), .izq(c9[2]), .der(pixelpersonaje_350_siz), .dir(in_1),
    .sar(pixelpersonaje_318_sar), .siz(pixelpersonaje_318_siz), .sde(c10[2]), .in_8(s9os10), .in_7(in_2),
    .in_5(in_3));
  PixelPersonaje pixelpersonaje_319 (
    .clk(clk), .abajo(pixelpersonaje_320_sar), .izq(c9[1]), .der(pixelpersonaje_351_siz), .dir(in_1),
    .sar(pixelpersonaje_319_sar), .siz(pixelpersonaje_319_siz), .sde(c10[1]), .in_8(s9os10), .in_7(in_2),
    .in_5(in_3));
  PixelPersonaje pixelpersonaje_320 (
    .clk(clk), .abajo(c10[31]), .izq(c9[0]), .der(pixelpersonaje_352_siz), .dir(in_1),
    .sar(pixelpersonaje_320_sar), .siz(pixelpersonaje_320_siz), .sde(c10[0]), .in_7(in_2), .in_5(in_3));  // open: in_8
  PixelPersonaje pixelpersonaje_321 (
    .clk(clk), .abajo(pixelpersonaje_322_sar), .izq(c10[31]), .der(pixelpersonaje_353_siz), .dir(in_1),
    .siz(pixelpersonaje_321_siz), .sde(c11[31]), .in_7(in_2), .in_5(in_3));  // open: sar, in_8
  PixelPersonaje pixelpersonaje_322 (
    .clk(clk), .abajo(pixelpersonaje_323_sar), .izq(c10[30]), .der(pixelpersonaje_354_siz), .dir(in_1),
    .sar(pixelpersonaje_322_sar), .siz(pixelpersonaje_322_siz), .sde(c11[30]), .in_7(in_2), .in_5(in_3));  // open: in_8
  PixelPersonaje pixelpersonaje_323 (
    .clk(clk), .abajo(pixelpersonaje_324_sar), .izq(c10[29]), .der(pixelpersonaje_355_siz), .dir(in_1),
    .sar(pixelpersonaje_323_sar), .siz(pixelpersonaje_323_siz), .sde(c11[29]), .in_7(in_2), .in_5(in_3));  // open: in_8
  PixelPersonaje pixelpersonaje_324 (
    .clk(clk), .abajo(pixelpersonaje_325_sar), .izq(c10[28]), .der(pixelpersonaje_356_siz), .dir(in_1),
    .sar(pixelpersonaje_324_sar), .siz(pixelpersonaje_324_siz), .sde(c11[28]), .in_7(in_2), .in_5(in_3));  // open: in_8
  PixelPersonaje pixelpersonaje_325 (
    .clk(clk), .abajo(pixelpersonaje_326_sar), .izq(c10[27]), .der(pixelpersonaje_357_siz), .dir(in_1),
    .sar(pixelpersonaje_325_sar), .siz(pixelpersonaje_325_siz), .sde(c11[27]), .in_7(in_2), .in_5(in_3));  // open: in_8
  PixelPersonaje pixelpersonaje_326 (
    .clk(clk), .abajo(pixelpersonaje_327_sar), .izq(c10[26]), .der(pixelpersonaje_358_siz), .dir(in_1),
    .sar(pixelpersonaje_326_sar), .siz(pixelpersonaje_326_siz), .sde(c11[26]), .in_7(in_2), .in_5(in_3));  // open: in_8
  PixelPersonaje pixelpersonaje_327 (
    .clk(clk), .abajo(pixelpersonaje_328_sar), .izq(c10[25]), .der(pixelpersonaje_359_siz), .dir(in_1),
    .sar(pixelpersonaje_327_sar), .siz(pixelpersonaje_327_siz), .sde(c11[25]), .in_7(in_2), .in_5(in_3));  // open: in_8
  PixelPersonaje pixelpersonaje_328 (
    .clk(clk), .abajo(pixelpersonaje_329_sar), .izq(c10[24]), .der(pixelpersonaje_360_siz), .dir(in_1),
    .sar(pixelpersonaje_328_sar), .siz(pixelpersonaje_328_siz), .sde(c11[24]), .in_7(in_2), .in_5(in_3));  // open: in_8
  PixelPersonaje pixelpersonaje_329 (
    .clk(clk), .abajo(pixelpersonaje_330_sar), .izq(c10[23]), .der(pixelpersonaje_361_siz), .dir(in_1),
    .sar(pixelpersonaje_329_sar), .siz(pixelpersonaje_329_siz), .sde(c11[23]), .in_7(in_2), .in_5(in_3));  // open: in_8
  PixelPersonaje pixelpersonaje_330 (
    .clk(clk), .abajo(pixelpersonaje_331_sar), .izq(c10[22]), .der(pixelpersonaje_362_siz), .dir(in_1),
    .sar(pixelpersonaje_330_sar), .siz(pixelpersonaje_330_siz), .sde(c11[22]), .in_7(in_2), .in_5(in_3));  // open: in_8
  PixelPersonaje pixelpersonaje_331 (
    .clk(clk), .abajo(pixelpersonaje_332_sar), .izq(c10[21]), .der(pixelpersonaje_363_siz), .dir(in_1),
    .sar(pixelpersonaje_331_sar), .siz(pixelpersonaje_331_siz), .sde(c11[21]), .in_7(in_2), .in_5(in_3));  // open: in_8
  PixelPersonaje pixelpersonaje_332 (
    .clk(clk), .abajo(pixelpersonaje_333_sar), .izq(c10[20]), .der(pixelpersonaje_364_siz), .dir(in_1),
    .sar(pixelpersonaje_332_sar), .siz(pixelpersonaje_332_siz), .sde(c11[20]), .in_7(in_2), .in_5(in_3));  // open: in_8
  PixelPersonaje pixelpersonaje_333 (
    .clk(clk), .abajo(pixelpersonaje_334_sar), .izq(c10[19]), .der(pixelpersonaje_365_siz), .dir(in_1),
    .sar(pixelpersonaje_333_sar), .siz(pixelpersonaje_333_siz), .sde(c11[19]), .in_7(in_2), .in_5(in_3));  // open: in_8
  PixelPersonaje pixelpersonaje_334 (
    .clk(clk), .abajo(pixelpersonaje_335_sar), .izq(c10[18]), .der(pixelpersonaje_366_siz), .dir(in_1),
    .sar(pixelpersonaje_334_sar), .siz(pixelpersonaje_334_siz), .sde(c11[18]), .in_7(in_2), .in_5(in_3));  // open: in_8
  PixelPersonaje pixelpersonaje_335 (
    .clk(clk), .abajo(pixelpersonaje_336_sar), .izq(c10[17]), .der(pixelpersonaje_367_siz), .dir(in_1),
    .sar(pixelpersonaje_335_sar), .siz(pixelpersonaje_335_siz), .sde(c11[17]), .in_7(in_2), .in_5(in_3));  // open: in_8
  PixelPersonaje pixelpersonaje_336 (
    .clk(clk), .abajo(pixelpersonaje_337_sar), .izq(c10[16]), .der(pixelpersonaje_368_siz), .dir(in_1),
    .sar(pixelpersonaje_336_sar), .siz(pixelpersonaje_336_siz), .sde(c11[16]), .in_7(in_2), .in_5(in_3));  // open: in_8
  PixelPersonaje pixelpersonaje_337 (
    .clk(clk), .abajo(pixelpersonaje_338_sar), .izq(c10[15]), .der(pixelpersonaje_369_siz), .dir(in_1),
    .sar(pixelpersonaje_337_sar), .siz(pixelpersonaje_337_siz), .sde(c11[15]), .in_7(in_2), .in_5(in_3));  // open: in_8
  PixelPersonaje pixelpersonaje_338 (
    .clk(clk), .abajo(pixelpersonaje_339_sar), .izq(c10[14]), .der(pixelpersonaje_370_siz), .dir(in_1),
    .sar(pixelpersonaje_338_sar), .siz(pixelpersonaje_338_siz), .sde(c11[14]), .in_7(in_2), .in_5(in_3));  // open: in_8
  PixelPersonaje pixelpersonaje_339 (
    .clk(clk), .abajo(pixelpersonaje_340_sar), .izq(c10[13]), .der(pixelpersonaje_371_siz), .dir(in_1),
    .sar(pixelpersonaje_339_sar), .siz(pixelpersonaje_339_siz), .sde(c11[13]), .in_7(in_2), .in_5(in_3));  // open: in_8
  PixelPersonaje pixelpersonaje_340 (
    .clk(clk), .abajo(pixelpersonaje_341_sar), .izq(c10[12]), .der(pixelpersonaje_372_siz), .dir(in_1),
    .sar(pixelpersonaje_340_sar), .siz(pixelpersonaje_340_siz), .sde(c11[12]), .in_7(in_2), .in_5(in_3));  // open: in_8
  PixelPersonaje pixelpersonaje_341 (
    .clk(clk), .abajo(pixelpersonaje_342_sar), .izq(c10[11]), .der(pixelpersonaje_373_siz), .dir(in_1),
    .sar(pixelpersonaje_341_sar), .siz(pixelpersonaje_341_siz), .sde(c11[11]), .in_7(in_2), .in_5(in_3));  // open: in_8
  PixelPersonaje pixelpersonaje_342 (
    .clk(clk), .abajo(pixelpersonaje_343_sar), .izq(c10[10]), .der(pixelpersonaje_374_siz), .dir(in_1),
    .sar(pixelpersonaje_342_sar), .siz(pixelpersonaje_342_siz), .sde(c11[10]), .in_7(in_2), .in_5(in_3));  // open: in_8
  PixelPersonaje pixelpersonaje_343 (
    .clk(clk), .abajo(pixelpersonaje_344_sar), .izq(c10[9]), .der(pixelpersonaje_375_siz), .dir(in_1),
    .sar(pixelpersonaje_343_sar), .siz(pixelpersonaje_343_siz), .sde(c11[9]), .in_7(in_2), .in_5(in_3));  // open: in_8
  PixelPersonaje pixelpersonaje_344 (
    .clk(clk), .abajo(pixelpersonaje_345_sar), .izq(c10[8]), .der(pixelpersonaje_376_siz), .dir(in_1),
    .sar(pixelpersonaje_344_sar), .siz(pixelpersonaje_344_siz), .sde(c11[8]), .in_7(in_2), .in_5(in_3));  // open: in_8
  PixelPersonaje pixelpersonaje_345 (
    .clk(clk), .abajo(pixelpersonaje_346_sar), .izq(c10[7]), .der(pixelpersonaje_377_siz), .dir(in_1),
    .sar(pixelpersonaje_345_sar), .siz(pixelpersonaje_345_siz), .sde(c11[7]), .in_7(in_2), .in_5(in_3));  // open: in_8
  PixelPersonaje pixelpersonaje_346 (
    .clk(clk), .abajo(pixelpersonaje_347_sar), .izq(c10[6]), .der(pixelpersonaje_378_siz), .dir(in_1),
    .sar(pixelpersonaje_346_sar), .siz(pixelpersonaje_346_siz), .sde(c11[6]), .in_7(in_2), .in_5(in_3));  // open: in_8
  PixelPersonaje pixelpersonaje_347 (
    .clk(clk), .abajo(pixelpersonaje_348_sar), .izq(c10[5]), .der(pixelpersonaje_379_siz), .dir(in_1),
    .sar(pixelpersonaje_347_sar), .siz(pixelpersonaje_347_siz), .sde(c11[5]), .in_7(in_2), .in_5(in_3));  // open: in_8
  PixelPersonaje pixelpersonaje_348 (
    .clk(clk), .abajo(pixelpersonaje_349_sar), .izq(c10[4]), .der(pixelpersonaje_380_siz), .dir(in_1),
    .sar(pixelpersonaje_348_sar), .siz(pixelpersonaje_348_siz), .sde(c11[4]), .in_7(in_2), .in_5(in_3));  // open: in_8
  PixelPersonaje pixelpersonaje_349 (
    .clk(clk), .abajo(pixelpersonaje_350_sar), .izq(c10[3]), .der(pixelpersonaje_381_siz), .dir(in_1),
    .sar(pixelpersonaje_349_sar), .siz(pixelpersonaje_349_siz), .sde(c11[3]), .in_7(in_2), .in_5(in_3));  // open: in_8
  PixelPersonaje pixelpersonaje_350 (
    .clk(clk), .abajo(pixelpersonaje_351_sar), .izq(c10[2]), .der(pixelpersonaje_382_siz), .dir(in_1),
    .sar(pixelpersonaje_350_sar), .siz(pixelpersonaje_350_siz), .sde(c11[2]), .in_8(s10os11), .in_7(in_2),
    .in_5(in_3));
  PixelPersonaje pixelpersonaje_351 (
    .clk(clk), .abajo(pixelpersonaje_352_sar), .izq(c10[1]), .der(pixelpersonaje_383_siz), .dir(in_1),
    .sar(pixelpersonaje_351_sar), .siz(pixelpersonaje_351_siz), .sde(c11[1]), .in_8(s10os11), .in_7(in_2),
    .in_5(in_3));
  PixelPersonaje pixelpersonaje_352 (
    .clk(clk), .abajo(c11[31]), .izq(c10[0]), .der(pixelpersonaje_384_siz), .dir(in_1),
    .sar(pixelpersonaje_352_sar), .siz(pixelpersonaje_352_siz), .sde(c11[0]), .in_7(in_2), .in_5(in_3));  // open: in_8
  PixelPersonaje pixelpersonaje_353 (
    .clk(clk), .abajo(pixelpersonaje_354_sar), .izq(c11[31]), .der(pixelpersonaje_385_siz), .dir(in_1),
    .siz(pixelpersonaje_353_siz), .sde(c12[31]), .in_7(in_2), .in_5(in_3));  // open: sar, in_8
  PixelPersonaje pixelpersonaje_354 (
    .clk(clk), .abajo(pixelpersonaje_355_sar), .izq(c11[30]), .der(pixelpersonaje_386_siz), .dir(in_1),
    .sar(pixelpersonaje_354_sar), .siz(pixelpersonaje_354_siz), .sde(c12[30]), .in_7(in_2), .in_5(in_3));  // open: in_8
  PixelPersonaje pixelpersonaje_355 (
    .clk(clk), .abajo(pixelpersonaje_356_sar), .izq(c11[29]), .der(pixelpersonaje_387_siz), .dir(in_1),
    .sar(pixelpersonaje_355_sar), .siz(pixelpersonaje_355_siz), .sde(c12[29]), .in_7(in_2), .in_5(in_3));  // open: in_8
  PixelPersonaje pixelpersonaje_356 (
    .clk(clk), .abajo(pixelpersonaje_357_sar), .izq(c11[28]), .der(pixelpersonaje_388_siz), .dir(in_1),
    .sar(pixelpersonaje_356_sar), .siz(pixelpersonaje_356_siz), .sde(c12[28]), .in_7(in_2), .in_5(in_3));  // open: in_8
  PixelPersonaje pixelpersonaje_357 (
    .clk(clk), .abajo(pixelpersonaje_358_sar), .izq(c11[27]), .der(pixelpersonaje_389_siz), .dir(in_1),
    .sar(pixelpersonaje_357_sar), .siz(pixelpersonaje_357_siz), .sde(c12[27]), .in_7(in_2), .in_5(in_3));  // open: in_8
  PixelPersonaje pixelpersonaje_358 (
    .clk(clk), .abajo(pixelpersonaje_359_sar), .izq(c11[26]), .der(pixelpersonaje_390_siz), .dir(in_1),
    .sar(pixelpersonaje_358_sar), .siz(pixelpersonaje_358_siz), .sde(c12[26]), .in_7(in_2), .in_5(in_3));  // open: in_8
  PixelPersonaje pixelpersonaje_359 (
    .clk(clk), .abajo(pixelpersonaje_360_sar), .izq(c11[25]), .der(pixelpersonaje_391_siz), .dir(in_1),
    .sar(pixelpersonaje_359_sar), .siz(pixelpersonaje_359_siz), .sde(c12[25]), .in_7(in_2), .in_5(in_3));  // open: in_8
  PixelPersonaje pixelpersonaje_360 (
    .clk(clk), .abajo(pixelpersonaje_361_sar), .izq(c11[24]), .der(pixelpersonaje_392_siz), .dir(in_1),
    .sar(pixelpersonaje_360_sar), .siz(pixelpersonaje_360_siz), .sde(c12[24]), .in_7(in_2), .in_5(in_3));  // open: in_8
  PixelPersonaje pixelpersonaje_361 (
    .clk(clk), .abajo(pixelpersonaje_362_sar), .izq(c11[23]), .der(pixelpersonaje_393_siz), .dir(in_1),
    .sar(pixelpersonaje_361_sar), .siz(pixelpersonaje_361_siz), .sde(c12[23]), .in_7(in_2), .in_5(in_3));  // open: in_8
  PixelPersonaje pixelpersonaje_362 (
    .clk(clk), .abajo(pixelpersonaje_363_sar), .izq(c11[22]), .der(pixelpersonaje_394_siz), .dir(in_1),
    .sar(pixelpersonaje_362_sar), .siz(pixelpersonaje_362_siz), .sde(c12[22]), .in_7(in_2), .in_5(in_3));  // open: in_8
  PixelPersonaje pixelpersonaje_363 (
    .clk(clk), .abajo(pixelpersonaje_364_sar), .izq(c11[21]), .der(pixelpersonaje_395_siz), .dir(in_1),
    .sar(pixelpersonaje_363_sar), .siz(pixelpersonaje_363_siz), .sde(c12[21]), .in_7(in_2), .in_5(in_3));  // open: in_8
  PixelPersonaje pixelpersonaje_364 (
    .clk(clk), .abajo(pixelpersonaje_365_sar), .izq(c11[20]), .der(pixelpersonaje_396_siz), .dir(in_1),
    .sar(pixelpersonaje_364_sar), .siz(pixelpersonaje_364_siz), .sde(c12[20]), .in_7(in_2), .in_5(in_3));  // open: in_8
  PixelPersonaje pixelpersonaje_365 (
    .clk(clk), .abajo(pixelpersonaje_366_sar), .izq(c11[19]), .der(pixelpersonaje_397_siz), .dir(in_1),
    .sar(pixelpersonaje_365_sar), .siz(pixelpersonaje_365_siz), .sde(c12[19]), .in_7(in_2), .in_5(in_3));  // open: in_8
  PixelPersonaje pixelpersonaje_366 (
    .clk(clk), .abajo(pixelpersonaje_367_sar), .izq(c11[18]), .der(pixelpersonaje_398_siz), .dir(in_1),
    .sar(pixelpersonaje_366_sar), .siz(pixelpersonaje_366_siz), .sde(c12[18]), .in_7(in_2), .in_5(in_3));  // open: in_8
  PixelPersonaje pixelpersonaje_367 (
    .clk(clk), .abajo(pixelpersonaje_368_sar), .izq(c11[17]), .der(pixelpersonaje_399_siz), .dir(in_1),
    .sar(pixelpersonaje_367_sar), .siz(pixelpersonaje_367_siz), .sde(c12[17]), .in_7(in_2), .in_5(in_3));  // open: in_8
  PixelPersonaje pixelpersonaje_368 (
    .clk(clk), .abajo(pixelpersonaje_369_sar), .izq(c11[16]), .der(pixelpersonaje_400_siz), .dir(in_1),
    .sar(pixelpersonaje_368_sar), .siz(pixelpersonaje_368_siz), .sde(c12[16]), .in_7(in_2), .in_5(in_3));  // open: in_8
  PixelPersonaje pixelpersonaje_369 (
    .clk(clk), .abajo(pixelpersonaje_370_sar), .izq(c11[15]), .der(pixelpersonaje_401_siz), .dir(in_1),
    .sar(pixelpersonaje_369_sar), .siz(pixelpersonaje_369_siz), .sde(c12[15]), .in_7(in_2), .in_5(in_3));  // open: in_8
  PixelPersonaje pixelpersonaje_370 (
    .clk(clk), .abajo(pixelpersonaje_371_sar), .izq(c11[14]), .der(pixelpersonaje_402_siz), .dir(in_1),
    .sar(pixelpersonaje_370_sar), .siz(pixelpersonaje_370_siz), .sde(c12[14]), .in_7(in_2), .in_5(in_3));  // open: in_8
  PixelPersonaje pixelpersonaje_371 (
    .clk(clk), .abajo(pixelpersonaje_372_sar), .izq(c11[13]), .der(pixelpersonaje_403_siz), .dir(in_1),
    .sar(pixelpersonaje_371_sar), .siz(pixelpersonaje_371_siz), .sde(c12[13]), .in_7(in_2), .in_5(in_3));  // open: in_8
  PixelPersonaje pixelpersonaje_372 (
    .clk(clk), .abajo(pixelpersonaje_373_sar), .izq(c11[12]), .der(pixelpersonaje_404_siz), .dir(in_1),
    .sar(pixelpersonaje_372_sar), .siz(pixelpersonaje_372_siz), .sde(c12[12]), .in_7(in_2), .in_5(in_3));  // open: in_8
  PixelPersonaje pixelpersonaje_373 (
    .clk(clk), .abajo(pixelpersonaje_374_sar), .izq(c11[11]), .der(pixelpersonaje_405_siz), .dir(in_1),
    .sar(pixelpersonaje_373_sar), .siz(pixelpersonaje_373_siz), .sde(c12[11]), .in_7(in_2), .in_5(in_3));  // open: in_8
  PixelPersonaje pixelpersonaje_374 (
    .clk(clk), .abajo(pixelpersonaje_375_sar), .izq(c11[10]), .der(pixelpersonaje_406_siz), .dir(in_1),
    .sar(pixelpersonaje_374_sar), .siz(pixelpersonaje_374_siz), .sde(c12[10]), .in_7(in_2), .in_5(in_3));  // open: in_8
  PixelPersonaje pixelpersonaje_375 (
    .clk(clk), .abajo(pixelpersonaje_376_sar), .izq(c11[9]), .der(pixelpersonaje_407_siz), .dir(in_1),
    .sar(pixelpersonaje_375_sar), .siz(pixelpersonaje_375_siz), .sde(c12[9]), .in_7(in_2), .in_5(in_3));  // open: in_8
  PixelPersonaje pixelpersonaje_376 (
    .clk(clk), .abajo(pixelpersonaje_377_sar), .izq(c11[8]), .der(pixelpersonaje_408_siz), .dir(in_1),
    .sar(pixelpersonaje_376_sar), .siz(pixelpersonaje_376_siz), .sde(c12[8]), .in_7(in_2), .in_5(in_3));  // open: in_8
  PixelPersonaje pixelpersonaje_377 (
    .clk(clk), .abajo(pixelpersonaje_378_sar), .izq(c11[7]), .der(pixelpersonaje_409_siz), .dir(in_1),
    .sar(pixelpersonaje_377_sar), .siz(pixelpersonaje_377_siz), .sde(c12[7]), .in_7(in_2), .in_5(in_3));  // open: in_8
  PixelPersonaje pixelpersonaje_378 (
    .clk(clk), .abajo(pixelpersonaje_379_sar), .izq(c11[6]), .der(pixelpersonaje_410_siz), .dir(in_1),
    .sar(pixelpersonaje_378_sar), .siz(pixelpersonaje_378_siz), .sde(c12[6]), .in_7(in_2), .in_5(in_3));  // open: in_8
  PixelPersonaje pixelpersonaje_379 (
    .clk(clk), .abajo(pixelpersonaje_380_sar), .izq(c11[5]), .der(pixelpersonaje_411_siz), .dir(in_1),
    .sar(pixelpersonaje_379_sar), .siz(pixelpersonaje_379_siz), .sde(c12[5]), .in_7(in_2), .in_5(in_3));  // open: in_8
  PixelPersonaje pixelpersonaje_380 (
    .clk(clk), .abajo(pixelpersonaje_381_sar), .izq(c11[4]), .der(pixelpersonaje_412_siz), .dir(in_1),
    .sar(pixelpersonaje_380_sar), .siz(pixelpersonaje_380_siz), .sde(c12[4]), .in_7(in_2), .in_5(in_3));  // open: in_8
  PixelPersonaje pixelpersonaje_381 (
    .clk(clk), .abajo(pixelpersonaje_382_sar), .izq(c11[3]), .der(pixelpersonaje_413_siz), .dir(in_1),
    .sar(pixelpersonaje_381_sar), .siz(pixelpersonaje_381_siz), .sde(c12[3]), .in_7(in_2), .in_5(in_3));  // open: in_8
  PixelPersonaje pixelpersonaje_382 (
    .clk(clk), .abajo(pixelpersonaje_383_sar), .izq(c11[2]), .der(pixelpersonaje_414_siz), .dir(in_1),
    .sar(pixelpersonaje_382_sar), .siz(pixelpersonaje_382_siz), .sde(c12[2]), .in_8(s11os12), .in_7(in_2),
    .in_5(in_3));
  PixelPersonaje pixelpersonaje_383 (
    .clk(clk), .abajo(pixelpersonaje_384_sar), .izq(c11[1]), .der(pixelpersonaje_415_siz), .dir(in_1),
    .sar(pixelpersonaje_383_sar), .siz(pixelpersonaje_383_siz), .sde(c12[1]), .in_8(s11os12), .in_7(in_2),
    .in_5(in_3));
  PixelPersonaje pixelpersonaje_384 (
    .clk(clk), .abajo(c12[31]), .izq(c11[0]), .der(pixelpersonaje_416_siz), .dir(in_1),
    .sar(pixelpersonaje_384_sar), .siz(pixelpersonaje_384_siz), .sde(c12[0]), .in_7(in_2), .in_5(in_3));  // open: in_8
  or or_1 (s1os2, s1, s2);
  or or_2 (s2os3, s2, s3);
  or or_3 (s3os4, s3, s4);
  or or_4 (s4os5, s4, s4);
  or or_5 (s5os6, s4, s6);
  or or_6 (s6os7, s6, s7);
  or or_7 (s7os8, s7, s8);
  or or_8 (s8os9, s8, s9);
  or or_9 (s9os10, s9, s10);
  or or_10 (s10os11, s10, s11);
  or or_11 (s11os12, s11, s12);
  or or_12 (s12os13, s12, s13);
  or or_13 (s13os14, s13, s14);
  or or_14 (s14os15, s14, s15);
  PixelPersonaje pixelpersonaje_385 (
    .clk(clk), .abajo(pixelpersonaje_386_sar), .izq(c12[31]), .der(pixelpersonaje_417_siz), .dir(in_1),
    .siz(pixelpersonaje_385_siz), .sde(c13[31]), .in_7(in_2), .in_5(in_3));  // open: sar, in_8
  PixelPersonaje pixelpersonaje_386 (
    .clk(clk), .abajo(pixelpersonaje_387_sar), .izq(c12[30]), .der(pixelpersonaje_418_siz), .dir(in_1),
    .sar(pixelpersonaje_386_sar), .siz(pixelpersonaje_386_siz), .sde(c13[30]), .in_7(in_2), .in_5(in_3));  // open: in_8
  PixelPersonaje pixelpersonaje_387 (
    .clk(clk), .abajo(pixelpersonaje_388_sar), .izq(c12[29]), .der(pixelpersonaje_419_siz), .dir(in_1),
    .sar(pixelpersonaje_387_sar), .siz(pixelpersonaje_387_siz), .sde(c13[29]), .in_7(in_2), .in_5(in_3));  // open: in_8
  PixelPersonaje pixelpersonaje_388 (
    .clk(clk), .abajo(pixelpersonaje_389_sar), .izq(c12[28]), .der(pixelpersonaje_420_siz), .dir(in_1),
    .sar(pixelpersonaje_388_sar), .siz(pixelpersonaje_388_siz), .sde(c13[28]), .in_7(in_2), .in_5(in_3));  // open: in_8
  PixelPersonaje pixelpersonaje_389 (
    .clk(clk), .abajo(pixelpersonaje_390_sar), .izq(c12[27]), .der(pixelpersonaje_421_siz), .dir(in_1),
    .sar(pixelpersonaje_389_sar), .siz(pixelpersonaje_389_siz), .sde(c13[27]), .in_7(in_2), .in_5(in_3));  // open: in_8
  PixelPersonaje pixelpersonaje_390 (
    .clk(clk), .abajo(pixelpersonaje_391_sar), .izq(c12[26]), .der(pixelpersonaje_422_siz), .dir(in_1),
    .sar(pixelpersonaje_390_sar), .siz(pixelpersonaje_390_siz), .sde(c13[26]), .in_7(in_2), .in_5(in_3));  // open: in_8
  PixelPersonaje pixelpersonaje_391 (
    .clk(clk), .abajo(pixelpersonaje_392_sar), .izq(c12[25]), .der(pixelpersonaje_423_siz), .dir(in_1),
    .sar(pixelpersonaje_391_sar), .siz(pixelpersonaje_391_siz), .sde(c13[25]), .in_7(in_2), .in_5(in_3));  // open: in_8
  PixelPersonaje pixelpersonaje_392 (
    .clk(clk), .abajo(pixelpersonaje_393_sar), .izq(c12[24]), .der(pixelpersonaje_424_siz), .dir(in_1),
    .sar(pixelpersonaje_392_sar), .siz(pixelpersonaje_392_siz), .sde(c13[24]), .in_7(in_2), .in_5(in_3));  // open: in_8
  PixelPersonaje pixelpersonaje_393 (
    .clk(clk), .abajo(pixelpersonaje_394_sar), .izq(c12[23]), .der(pixelpersonaje_425_siz), .dir(in_1),
    .sar(pixelpersonaje_393_sar), .siz(pixelpersonaje_393_siz), .sde(c13[23]), .in_7(in_2), .in_5(in_3));  // open: in_8
  PixelPersonaje pixelpersonaje_394 (
    .clk(clk), .abajo(pixelpersonaje_395_sar), .izq(c12[22]), .der(pixelpersonaje_426_siz), .dir(in_1),
    .sar(pixelpersonaje_394_sar), .siz(pixelpersonaje_394_siz), .sde(c13[22]), .in_7(in_2), .in_5(in_3));  // open: in_8
  PixelPersonaje pixelpersonaje_395 (
    .clk(clk), .abajo(pixelpersonaje_396_sar), .izq(c12[21]), .der(pixelpersonaje_427_siz), .dir(in_1),
    .sar(pixelpersonaje_395_sar), .siz(pixelpersonaje_395_siz), .sde(c13[21]), .in_7(in_2), .in_5(in_3));  // open: in_8
  PixelPersonaje pixelpersonaje_396 (
    .clk(clk), .abajo(pixelpersonaje_397_sar), .izq(c12[20]), .der(pixelpersonaje_428_siz), .dir(in_1),
    .sar(pixelpersonaje_396_sar), .siz(pixelpersonaje_396_siz), .sde(c13[20]), .in_7(in_2), .in_5(in_3));  // open: in_8
  PixelPersonaje pixelpersonaje_397 (
    .clk(clk), .abajo(pixelpersonaje_398_sar), .izq(c12[19]), .der(pixelpersonaje_429_siz), .dir(in_1),
    .sar(pixelpersonaje_397_sar), .siz(pixelpersonaje_397_siz), .sde(c13[19]), .in_7(in_2), .in_5(in_3));  // open: in_8
  PixelPersonaje pixelpersonaje_398 (
    .clk(clk), .abajo(pixelpersonaje_399_sar), .izq(c12[18]), .der(pixelpersonaje_430_siz), .dir(in_1),
    .sar(pixelpersonaje_398_sar), .siz(pixelpersonaje_398_siz), .sde(c13[18]), .in_7(in_2), .in_5(in_3));  // open: in_8
  PixelPersonaje pixelpersonaje_399 (
    .clk(clk), .abajo(pixelpersonaje_400_sar), .izq(c12[17]), .der(pixelpersonaje_431_siz), .dir(in_1),
    .sar(pixelpersonaje_399_sar), .siz(pixelpersonaje_399_siz), .sde(c13[17]), .in_7(in_2), .in_5(in_3));  // open: in_8
  PixelPersonaje pixelpersonaje_400 (
    .clk(clk), .abajo(pixelpersonaje_401_sar), .izq(c12[16]), .der(pixelpersonaje_432_siz), .dir(in_1),
    .sar(pixelpersonaje_400_sar), .siz(pixelpersonaje_400_siz), .sde(c13[16]), .in_7(in_2), .in_5(in_3));  // open: in_8
  PixelPersonaje pixelpersonaje_401 (
    .clk(clk), .abajo(pixelpersonaje_402_sar), .izq(c12[15]), .der(pixelpersonaje_433_siz), .dir(in_1),
    .sar(pixelpersonaje_401_sar), .siz(pixelpersonaje_401_siz), .sde(c13[15]), .in_7(in_2), .in_5(in_3));  // open: in_8
  PixelPersonaje pixelpersonaje_402 (
    .clk(clk), .abajo(pixelpersonaje_403_sar), .izq(c12[14]), .der(pixelpersonaje_434_siz), .dir(in_1),
    .sar(pixelpersonaje_402_sar), .siz(pixelpersonaje_402_siz), .sde(c13[14]), .in_7(in_2), .in_5(in_3));  // open: in_8
  PixelPersonaje pixelpersonaje_403 (
    .clk(clk), .abajo(pixelpersonaje_404_sar), .izq(c12[13]), .der(pixelpersonaje_435_siz), .dir(in_1),
    .sar(pixelpersonaje_403_sar), .siz(pixelpersonaje_403_siz), .sde(c13[13]), .in_7(in_2), .in_5(in_3));  // open: in_8
  PixelPersonaje pixelpersonaje_404 (
    .clk(clk), .abajo(pixelpersonaje_405_sar), .izq(c12[12]), .der(pixelpersonaje_436_siz), .dir(in_1),
    .sar(pixelpersonaje_404_sar), .siz(pixelpersonaje_404_siz), .sde(c13[12]), .in_7(in_2), .in_5(in_3));  // open: in_8
  PixelPersonaje pixelpersonaje_405 (
    .clk(clk), .abajo(pixelpersonaje_406_sar), .izq(c12[11]), .der(pixelpersonaje_437_siz), .dir(in_1),
    .sar(pixelpersonaje_405_sar), .siz(pixelpersonaje_405_siz), .sde(c13[11]), .in_7(in_2), .in_5(in_3));  // open: in_8
  PixelPersonaje pixelpersonaje_406 (
    .clk(clk), .abajo(pixelpersonaje_407_sar), .izq(c12[10]), .der(pixelpersonaje_438_siz), .dir(in_1),
    .sar(pixelpersonaje_406_sar), .siz(pixelpersonaje_406_siz), .sde(c13[10]), .in_7(in_2), .in_5(in_3));  // open: in_8
  PixelPersonaje pixelpersonaje_407 (
    .clk(clk), .abajo(pixelpersonaje_408_sar), .izq(c12[9]), .der(pixelpersonaje_439_siz), .dir(in_1),
    .sar(pixelpersonaje_407_sar), .siz(pixelpersonaje_407_siz), .sde(c13[9]), .in_7(in_2), .in_5(in_3));  // open: in_8
  PixelPersonaje pixelpersonaje_408 (
    .clk(clk), .abajo(pixelpersonaje_409_sar), .izq(c12[8]), .der(pixelpersonaje_440_siz), .dir(in_1),
    .sar(pixelpersonaje_408_sar), .siz(pixelpersonaje_408_siz), .sde(c13[8]), .in_7(in_2), .in_5(in_3));  // open: in_8
  PixelPersonaje pixelpersonaje_409 (
    .clk(clk), .abajo(pixelpersonaje_410_sar), .izq(c12[7]), .der(pixelpersonaje_441_siz), .dir(in_1),
    .sar(pixelpersonaje_409_sar), .siz(pixelpersonaje_409_siz), .sde(c13[7]), .in_7(in_2), .in_5(in_3));  // open: in_8
  PixelPersonaje pixelpersonaje_410 (
    .clk(clk), .abajo(pixelpersonaje_411_sar), .izq(c12[6]), .der(pixelpersonaje_442_siz), .dir(in_1),
    .sar(pixelpersonaje_410_sar), .siz(pixelpersonaje_410_siz), .sde(c13[6]), .in_7(in_2), .in_5(in_3));  // open: in_8
  PixelPersonaje pixelpersonaje_411 (
    .clk(clk), .abajo(pixelpersonaje_412_sar), .izq(c12[5]), .der(pixelpersonaje_443_siz), .dir(in_1),
    .sar(pixelpersonaje_411_sar), .siz(pixelpersonaje_411_siz), .sde(c13[5]), .in_7(in_2), .in_5(in_3));  // open: in_8
  PixelPersonaje pixelpersonaje_412 (
    .clk(clk), .abajo(pixelpersonaje_413_sar), .izq(c12[4]), .der(pixelpersonaje_444_siz), .dir(in_1),
    .sar(pixelpersonaje_412_sar), .siz(pixelpersonaje_412_siz), .sde(c13[4]), .in_7(in_2), .in_5(in_3));  // open: in_8
  PixelPersonaje pixelpersonaje_413 (
    .clk(clk), .abajo(pixelpersonaje_414_sar), .izq(c12[3]), .der(pixelpersonaje_445_siz), .dir(in_1),
    .sar(pixelpersonaje_413_sar), .siz(pixelpersonaje_413_siz), .sde(c13[3]), .in_7(in_2), .in_5(in_3));  // open: in_8
  PixelPersonaje pixelpersonaje_414 (
    .clk(clk), .abajo(pixelpersonaje_415_sar), .izq(c12[2]), .der(pixelpersonaje_446_siz), .dir(in_1),
    .sar(pixelpersonaje_414_sar), .siz(pixelpersonaje_414_siz), .sde(c13[2]), .in_8(s12os13), .in_7(in_2),
    .in_5(in_3));
  PixelPersonaje pixelpersonaje_415 (
    .clk(clk), .abajo(pixelpersonaje_416_sar), .izq(c12[1]), .der(pixelpersonaje_447_siz), .dir(in_1),
    .sar(pixelpersonaje_415_sar), .siz(pixelpersonaje_415_siz), .sde(c13[1]), .in_8(s12os13), .in_7(in_2),
    .in_5(in_3));
  PixelPersonaje pixelpersonaje_416 (
    .clk(clk), .abajo(c13[31]), .izq(c12[0]), .der(pixelpersonaje_448_siz), .dir(in_1),
    .sar(pixelpersonaje_416_sar), .siz(pixelpersonaje_416_siz), .sde(c13[0]), .in_7(in_2), .in_5(in_3));  // open: in_8
  PixelPersonaje pixelpersonaje_417 (
    .clk(clk), .abajo(pixelpersonaje_418_sar), .izq(c13[31]), .der(pixelpersonaje_449_siz), .dir(in_1),
    .siz(pixelpersonaje_417_siz), .sde(c14[31]), .in_7(in_2), .in_5(in_3));  // open: sar, in_8
  PixelPersonaje pixelpersonaje_418 (
    .clk(clk), .abajo(pixelpersonaje_419_sar), .izq(c13[30]), .der(pixelpersonaje_450_siz), .dir(in_1),
    .sar(pixelpersonaje_418_sar), .siz(pixelpersonaje_418_siz), .sde(c14[30]), .in_7(in_2), .in_5(in_3));  // open: in_8
  PixelPersonaje pixelpersonaje_419 (
    .clk(clk), .abajo(pixelpersonaje_420_sar), .izq(c13[29]), .der(pixelpersonaje_451_siz), .dir(in_1),
    .sar(pixelpersonaje_419_sar), .siz(pixelpersonaje_419_siz), .sde(c14[29]), .in_7(in_2), .in_5(in_3));  // open: in_8
  PixelPersonaje pixelpersonaje_420 (
    .clk(clk), .abajo(pixelpersonaje_421_sar), .izq(c13[28]), .der(pixelpersonaje_452_siz), .dir(in_1),
    .sar(pixelpersonaje_420_sar), .siz(pixelpersonaje_420_siz), .sde(c14[28]), .in_7(in_2), .in_5(in_3));  // open: in_8
  PixelPersonaje pixelpersonaje_421 (
    .clk(clk), .abajo(pixelpersonaje_422_sar), .izq(c13[27]), .der(pixelpersonaje_453_siz), .dir(in_1),
    .sar(pixelpersonaje_421_sar), .siz(pixelpersonaje_421_siz), .sde(c14[27]), .in_7(in_2), .in_5(in_3));  // open: in_8
  PixelPersonaje pixelpersonaje_422 (
    .clk(clk), .abajo(pixelpersonaje_423_sar), .izq(c13[26]), .der(pixelpersonaje_454_siz), .dir(in_1),
    .sar(pixelpersonaje_422_sar), .siz(pixelpersonaje_422_siz), .sde(c14[26]), .in_7(in_2), .in_5(in_3));  // open: in_8
  PixelPersonaje pixelpersonaje_423 (
    .clk(clk), .abajo(pixelpersonaje_424_sar), .izq(c13[25]), .der(pixelpersonaje_455_siz), .dir(in_1),
    .sar(pixelpersonaje_423_sar), .siz(pixelpersonaje_423_siz), .sde(c14[25]), .in_7(in_2), .in_5(in_3));  // open: in_8
  PixelPersonaje pixelpersonaje_424 (
    .clk(clk), .abajo(pixelpersonaje_425_sar), .izq(c13[24]), .der(pixelpersonaje_456_siz), .dir(in_1),
    .sar(pixelpersonaje_424_sar), .siz(pixelpersonaje_424_siz), .sde(c14[24]), .in_7(in_2), .in_5(in_3));  // open: in_8
  PixelPersonaje pixelpersonaje_425 (
    .clk(clk), .abajo(pixelpersonaje_426_sar), .izq(c13[23]), .der(pixelpersonaje_457_siz), .dir(in_1),
    .sar(pixelpersonaje_425_sar), .siz(pixelpersonaje_425_siz), .sde(c14[23]), .in_7(in_2), .in_5(in_3));  // open: in_8
  PixelPersonaje pixelpersonaje_426 (
    .clk(clk), .abajo(pixelpersonaje_427_sar), .izq(c13[22]), .der(pixelpersonaje_458_siz), .dir(in_1),
    .sar(pixelpersonaje_426_sar), .siz(pixelpersonaje_426_siz), .sde(c14[22]), .in_7(in_2), .in_5(in_3));  // open: in_8
  PixelPersonaje pixelpersonaje_427 (
    .clk(clk), .abajo(pixelpersonaje_428_sar), .izq(c13[21]), .der(pixelpersonaje_459_siz), .dir(in_1),
    .sar(pixelpersonaje_427_sar), .siz(pixelpersonaje_427_siz), .sde(c14[21]), .in_7(in_2), .in_5(in_3));  // open: in_8
  PixelPersonaje pixelpersonaje_428 (
    .clk(clk), .abajo(pixelpersonaje_429_sar), .izq(c13[20]), .der(pixelpersonaje_460_siz), .dir(in_1),
    .sar(pixelpersonaje_428_sar), .siz(pixelpersonaje_428_siz), .sde(c14[20]), .in_7(in_2), .in_5(in_3));  // open: in_8
  PixelPersonaje pixelpersonaje_429 (
    .clk(clk), .abajo(pixelpersonaje_430_sar), .izq(c13[19]), .der(pixelpersonaje_461_siz), .dir(in_1),
    .sar(pixelpersonaje_429_sar), .siz(pixelpersonaje_429_siz), .sde(c14[19]), .in_7(in_2), .in_5(in_3));  // open: in_8
  PixelPersonaje pixelpersonaje_430 (
    .clk(clk), .abajo(pixelpersonaje_431_sar), .izq(c13[18]), .der(pixelpersonaje_462_siz), .dir(in_1),
    .sar(pixelpersonaje_430_sar), .siz(pixelpersonaje_430_siz), .sde(c14[18]), .in_7(in_2), .in_5(in_3));  // open: in_8
  PixelPersonaje pixelpersonaje_431 (
    .clk(clk), .abajo(pixelpersonaje_432_sar), .izq(c13[17]), .der(pixelpersonaje_463_siz), .dir(in_1),
    .sar(pixelpersonaje_431_sar), .siz(pixelpersonaje_431_siz), .sde(c14[17]), .in_7(in_2), .in_5(in_3));  // open: in_8
  PixelPersonaje pixelpersonaje_432 (
    .clk(clk), .abajo(pixelpersonaje_433_sar), .izq(c13[16]), .der(pixelpersonaje_464_siz), .dir(in_1),
    .sar(pixelpersonaje_432_sar), .siz(pixelpersonaje_432_siz), .sde(c14[16]), .in_7(in_2), .in_5(in_3));  // open: in_8
  PixelPersonaje pixelpersonaje_433 (
    .clk(clk), .abajo(pixelpersonaje_434_sar), .izq(c13[15]), .der(pixelpersonaje_465_siz), .dir(in_1),
    .sar(pixelpersonaje_433_sar), .siz(pixelpersonaje_433_siz), .sde(c14[15]), .in_7(in_2), .in_5(in_3));  // open: in_8
  PixelPersonaje pixelpersonaje_434 (
    .clk(clk), .abajo(pixelpersonaje_435_sar), .izq(c13[14]), .der(pixelpersonaje_466_siz), .dir(in_1),
    .sar(pixelpersonaje_434_sar), .siz(pixelpersonaje_434_siz), .sde(c14[14]), .in_7(in_2), .in_5(in_3));  // open: in_8
  PixelPersonaje pixelpersonaje_435 (
    .clk(clk), .abajo(pixelpersonaje_436_sar), .izq(c13[13]), .der(pixelpersonaje_467_siz), .dir(in_1),
    .sar(pixelpersonaje_435_sar), .siz(pixelpersonaje_435_siz), .sde(c14[13]), .in_7(in_2), .in_5(in_3));  // open: in_8
  PixelPersonaje pixelpersonaje_436 (
    .clk(clk), .abajo(pixelpersonaje_437_sar), .izq(c13[12]), .der(pixelpersonaje_468_siz), .dir(in_1),
    .sar(pixelpersonaje_436_sar), .siz(pixelpersonaje_436_siz), .sde(c14[12]), .in_7(in_2), .in_5(in_3));  // open: in_8
  PixelPersonaje pixelpersonaje_437 (
    .clk(clk), .abajo(pixelpersonaje_438_sar), .izq(c13[11]), .der(pixelpersonaje_469_siz), .dir(in_1),
    .sar(pixelpersonaje_437_sar), .siz(pixelpersonaje_437_siz), .sde(c14[11]), .in_7(in_2), .in_5(in_3));  // open: in_8
  PixelPersonaje pixelpersonaje_438 (
    .clk(clk), .abajo(pixelpersonaje_439_sar), .izq(c13[10]), .der(pixelpersonaje_470_siz), .dir(in_1),
    .sar(pixelpersonaje_438_sar), .siz(pixelpersonaje_438_siz), .sde(c14[10]), .in_7(in_2), .in_5(in_3));  // open: in_8
  PixelPersonaje pixelpersonaje_439 (
    .clk(clk), .abajo(pixelpersonaje_440_sar), .izq(c13[9]), .der(pixelpersonaje_471_siz), .dir(in_1),
    .sar(pixelpersonaje_439_sar), .siz(pixelpersonaje_439_siz), .sde(c14[9]), .in_7(in_2), .in_5(in_3));  // open: in_8
  PixelPersonaje pixelpersonaje_440 (
    .clk(clk), .abajo(pixelpersonaje_441_sar), .izq(c13[8]), .der(pixelpersonaje_472_siz), .dir(in_1),
    .sar(pixelpersonaje_440_sar), .siz(pixelpersonaje_440_siz), .sde(c14[8]), .in_7(in_2), .in_5(in_3));  // open: in_8
  PixelPersonaje pixelpersonaje_441 (
    .clk(clk), .abajo(pixelpersonaje_442_sar), .izq(c13[7]), .der(pixelpersonaje_473_siz), .dir(in_1),
    .sar(pixelpersonaje_441_sar), .siz(pixelpersonaje_441_siz), .sde(c14[7]), .in_7(in_2), .in_5(in_3));  // open: in_8
  PixelPersonaje pixelpersonaje_442 (
    .clk(clk), .abajo(pixelpersonaje_443_sar), .izq(c13[6]), .der(pixelpersonaje_474_siz), .dir(in_1),
    .sar(pixelpersonaje_442_sar), .siz(pixelpersonaje_442_siz), .sde(c14[6]), .in_7(in_2), .in_5(in_3));  // open: in_8
  PixelPersonaje pixelpersonaje_443 (
    .clk(clk), .abajo(pixelpersonaje_444_sar), .izq(c13[5]), .der(pixelpersonaje_475_siz), .dir(in_1),
    .sar(pixelpersonaje_443_sar), .siz(pixelpersonaje_443_siz), .sde(c14[5]), .in_7(in_2), .in_5(in_3));  // open: in_8
  PixelPersonaje pixelpersonaje_444 (
    .clk(clk), .abajo(pixelpersonaje_445_sar), .izq(c13[4]), .der(pixelpersonaje_476_siz), .dir(in_1),
    .sar(pixelpersonaje_444_sar), .siz(pixelpersonaje_444_siz), .sde(c14[4]), .in_7(in_2), .in_5(in_3));  // open: in_8
  PixelPersonaje pixelpersonaje_445 (
    .clk(clk), .abajo(pixelpersonaje_446_sar), .izq(c13[3]), .der(pixelpersonaje_477_siz), .dir(in_1),
    .sar(pixelpersonaje_445_sar), .siz(pixelpersonaje_445_siz), .sde(c14[3]), .in_7(in_2), .in_5(in_3));  // open: in_8
  PixelPersonaje pixelpersonaje_446 (
    .clk(clk), .abajo(pixelpersonaje_447_sar), .izq(c13[2]), .der(pixelpersonaje_478_siz), .dir(in_1),
    .sar(pixelpersonaje_446_sar), .siz(pixelpersonaje_446_siz), .sde(c14[2]), .in_8(s13os14), .in_7(in_2),
    .in_5(in_3));
  PixelPersonaje pixelpersonaje_447 (
    .clk(clk), .abajo(pixelpersonaje_448_sar), .izq(c13[1]), .der(pixelpersonaje_479_siz), .dir(in_1),
    .sar(pixelpersonaje_447_sar), .siz(pixelpersonaje_447_siz), .sde(c14[1]), .in_8(s13os14), .in_7(in_2),
    .in_5(in_3));
  PixelPersonaje pixelpersonaje_448 (
    .clk(clk), .abajo(c14[31]), .izq(c13[0]), .der(pixelpersonaje_480_siz), .dir(in_1),
    .sar(pixelpersonaje_448_sar), .siz(pixelpersonaje_448_siz), .sde(c14[0]), .in_7(in_2), .in_5(in_3));  // open: in_8
  PixelPersonaje pixelpersonaje_449 (
    .clk(clk), .abajo(pixelpersonaje_450_sar), .izq(c14[31]), .der(pixelpersonaje_481_siz), .dir(in_1),
    .siz(pixelpersonaje_449_siz), .sde(c15[31]), .in_7(in_2), .in_5(in_3));  // open: sar, in_8
  PixelPersonaje pixelpersonaje_450 (
    .clk(clk), .abajo(pixelpersonaje_451_sar), .izq(c14[30]), .der(pixelpersonaje_482_siz), .dir(in_1),
    .sar(pixelpersonaje_450_sar), .siz(pixelpersonaje_450_siz), .sde(c15[30]), .in_7(in_2), .in_5(in_3));  // open: in_8
  PixelPersonaje pixelpersonaje_451 (
    .clk(clk), .abajo(pixelpersonaje_452_sar), .izq(c14[29]), .der(pixelpersonaje_483_siz), .dir(in_1),
    .sar(pixelpersonaje_451_sar), .siz(pixelpersonaje_451_siz), .sde(c15[29]), .in_7(in_2), .in_5(in_3));  // open: in_8
  PixelPersonaje pixelpersonaje_452 (
    .clk(clk), .abajo(pixelpersonaje_453_sar), .izq(c14[28]), .der(pixelpersonaje_484_siz), .dir(in_1),
    .sar(pixelpersonaje_452_sar), .siz(pixelpersonaje_452_siz), .sde(c15[28]), .in_7(in_2), .in_5(in_3));  // open: in_8
  PixelPersonaje pixelpersonaje_453 (
    .clk(clk), .abajo(pixelpersonaje_454_sar), .izq(c14[27]), .der(pixelpersonaje_485_siz), .dir(in_1),
    .sar(pixelpersonaje_453_sar), .siz(pixelpersonaje_453_siz), .sde(c15[27]), .in_7(in_2), .in_5(in_3));  // open: in_8
  PixelPersonaje pixelpersonaje_454 (
    .clk(clk), .abajo(pixelpersonaje_455_sar), .izq(c14[26]), .der(pixelpersonaje_486_siz), .dir(in_1),
    .sar(pixelpersonaje_454_sar), .siz(pixelpersonaje_454_siz), .sde(c15[26]), .in_7(in_2), .in_5(in_3));  // open: in_8
  PixelPersonaje pixelpersonaje_455 (
    .clk(clk), .abajo(pixelpersonaje_456_sar), .izq(c14[25]), .der(pixelpersonaje_487_siz), .dir(in_1),
    .sar(pixelpersonaje_455_sar), .siz(pixelpersonaje_455_siz), .sde(c15[25]), .in_7(in_2), .in_5(in_3));  // open: in_8
  PixelPersonaje pixelpersonaje_456 (
    .clk(clk), .abajo(pixelpersonaje_457_sar), .izq(c14[24]), .der(pixelpersonaje_488_siz), .dir(in_1),
    .sar(pixelpersonaje_456_sar), .siz(pixelpersonaje_456_siz), .sde(c15[24]), .in_7(in_2), .in_5(in_3));  // open: in_8
  PixelPersonaje pixelpersonaje_457 (
    .clk(clk), .abajo(pixelpersonaje_458_sar), .izq(c14[23]), .der(pixelpersonaje_489_siz), .dir(in_1),
    .sar(pixelpersonaje_457_sar), .siz(pixelpersonaje_457_siz), .sde(c15[23]), .in_7(in_2), .in_5(in_3));  // open: in_8
  PixelPersonaje pixelpersonaje_458 (
    .clk(clk), .abajo(pixelpersonaje_459_sar), .izq(c14[22]), .der(pixelpersonaje_490_siz), .dir(in_1),
    .sar(pixelpersonaje_458_sar), .siz(pixelpersonaje_458_siz), .sde(c15[22]), .in_7(in_2), .in_5(in_3));  // open: in_8
  PixelPersonaje pixelpersonaje_459 (
    .clk(clk), .abajo(pixelpersonaje_460_sar), .izq(c14[21]), .der(pixelpersonaje_491_siz), .dir(in_1),
    .sar(pixelpersonaje_459_sar), .siz(pixelpersonaje_459_siz), .sde(c15[21]), .in_7(in_2), .in_5(in_3));  // open: in_8
  PixelPersonaje pixelpersonaje_460 (
    .clk(clk), .abajo(pixelpersonaje_461_sar), .izq(c14[20]), .der(pixelpersonaje_492_siz), .dir(in_1),
    .sar(pixelpersonaje_460_sar), .siz(pixelpersonaje_460_siz), .sde(c15[20]), .in_7(in_2), .in_5(in_3));  // open: in_8
  PixelPersonaje pixelpersonaje_461 (
    .clk(clk), .abajo(pixelpersonaje_462_sar), .izq(c14[19]), .der(pixelpersonaje_493_siz), .dir(in_1),
    .sar(pixelpersonaje_461_sar), .siz(pixelpersonaje_461_siz), .sde(c15[19]), .in_7(in_2), .in_5(in_3));  // open: in_8
  PixelPersonaje pixelpersonaje_462 (
    .clk(clk), .abajo(pixelpersonaje_463_sar), .izq(c14[18]), .der(pixelpersonaje_494_siz), .dir(in_1),
    .sar(pixelpersonaje_462_sar), .siz(pixelpersonaje_462_siz), .sde(c15[18]), .in_7(in_2), .in_5(in_3));  // open: in_8
  PixelPersonaje pixelpersonaje_463 (
    .clk(clk), .abajo(pixelpersonaje_464_sar), .izq(c14[17]), .der(pixelpersonaje_495_siz), .dir(in_1),
    .sar(pixelpersonaje_463_sar), .siz(pixelpersonaje_463_siz), .sde(c15[17]), .in_7(in_2), .in_5(in_3));  // open: in_8
  PixelPersonaje pixelpersonaje_464 (
    .clk(clk), .abajo(pixelpersonaje_465_sar), .izq(c14[16]), .der(pixelpersonaje_496_siz), .dir(in_1),
    .sar(pixelpersonaje_464_sar), .siz(pixelpersonaje_464_siz), .sde(c15[16]), .in_7(in_2), .in_5(in_3));  // open: in_8
  PixelPersonaje pixelpersonaje_465 (
    .clk(clk), .abajo(pixelpersonaje_466_sar), .izq(c14[15]), .der(pixelpersonaje_497_siz), .dir(in_1),
    .sar(pixelpersonaje_465_sar), .siz(pixelpersonaje_465_siz), .sde(c15[15]), .in_7(in_2), .in_5(in_3));  // open: in_8
  PixelPersonaje pixelpersonaje_466 (
    .clk(clk), .abajo(pixelpersonaje_467_sar), .izq(c14[14]), .der(pixelpersonaje_498_siz), .dir(in_1),
    .sar(pixelpersonaje_466_sar), .siz(pixelpersonaje_466_siz), .sde(c15[14]), .in_7(in_2), .in_5(in_3));  // open: in_8
  PixelPersonaje pixelpersonaje_467 (
    .clk(clk), .abajo(pixelpersonaje_468_sar), .izq(c14[13]), .der(pixelpersonaje_499_siz), .dir(in_1),
    .sar(pixelpersonaje_467_sar), .siz(pixelpersonaje_467_siz), .sde(c15[13]), .in_7(in_2), .in_5(in_3));  // open: in_8
  PixelPersonaje pixelpersonaje_468 (
    .clk(clk), .abajo(pixelpersonaje_469_sar), .izq(c14[12]), .der(pixelpersonaje_500_siz), .dir(in_1),
    .sar(pixelpersonaje_468_sar), .siz(pixelpersonaje_468_siz), .sde(c15[12]), .in_7(in_2), .in_5(in_3));  // open: in_8
  PixelPersonaje pixelpersonaje_469 (
    .clk(clk), .abajo(pixelpersonaje_470_sar), .izq(c14[11]), .der(pixelpersonaje_501_siz), .dir(in_1),
    .sar(pixelpersonaje_469_sar), .siz(pixelpersonaje_469_siz), .sde(c15[11]), .in_7(in_2), .in_5(in_3));  // open: in_8
  PixelPersonaje pixelpersonaje_470 (
    .clk(clk), .abajo(pixelpersonaje_471_sar), .izq(c14[10]), .der(pixelpersonaje_502_siz), .dir(in_1),
    .sar(pixelpersonaje_470_sar), .siz(pixelpersonaje_470_siz), .sde(c15[10]), .in_7(in_2), .in_5(in_3));  // open: in_8
  PixelPersonaje pixelpersonaje_471 (
    .clk(clk), .abajo(pixelpersonaje_472_sar), .izq(c14[9]), .der(pixelpersonaje_503_siz), .dir(in_1),
    .sar(pixelpersonaje_471_sar), .siz(pixelpersonaje_471_siz), .sde(c15[9]), .in_7(in_2), .in_5(in_3));  // open: in_8
  PixelPersonaje pixelpersonaje_472 (
    .clk(clk), .abajo(pixelpersonaje_473_sar), .izq(c14[8]), .der(pixelpersonaje_504_siz), .dir(in_1),
    .sar(pixelpersonaje_472_sar), .siz(pixelpersonaje_472_siz), .sde(c15[8]), .in_7(in_2), .in_5(in_3));  // open: in_8
  PixelPersonaje pixelpersonaje_473 (
    .clk(clk), .abajo(pixelpersonaje_474_sar), .izq(c14[7]), .der(pixelpersonaje_505_siz), .dir(in_1),
    .sar(pixelpersonaje_473_sar), .siz(pixelpersonaje_473_siz), .sde(c15[7]), .in_7(in_2), .in_5(in_3));  // open: in_8
  PixelPersonaje pixelpersonaje_474 (
    .clk(clk), .abajo(pixelpersonaje_475_sar), .izq(c14[6]), .der(pixelpersonaje_506_siz), .dir(in_1),
    .sar(pixelpersonaje_474_sar), .siz(pixelpersonaje_474_siz), .sde(c15[6]), .in_7(in_2), .in_5(in_3));  // open: in_8
  PixelPersonaje pixelpersonaje_475 (
    .clk(clk), .abajo(pixelpersonaje_476_sar), .izq(c14[5]), .der(pixelpersonaje_507_siz), .dir(in_1),
    .sar(pixelpersonaje_475_sar), .siz(pixelpersonaje_475_siz), .sde(c15[5]), .in_7(in_2), .in_5(in_3));  // open: in_8
  PixelPersonaje pixelpersonaje_476 (
    .clk(clk), .abajo(pixelpersonaje_477_sar), .izq(c14[4]), .der(pixelpersonaje_508_siz), .dir(in_1),
    .sar(pixelpersonaje_476_sar), .siz(pixelpersonaje_476_siz), .sde(c15[4]), .in_7(in_2), .in_5(in_3));  // open: in_8
  PixelPersonaje pixelpersonaje_477 (
    .clk(clk), .abajo(pixelpersonaje_478_sar), .izq(c14[3]), .der(pixelpersonaje_509_siz), .dir(in_1),
    .sar(pixelpersonaje_477_sar), .siz(pixelpersonaje_477_siz), .sde(c15[3]), .in_7(in_2), .in_5(in_3));  // open: in_8
  PixelPersonaje pixelpersonaje_478 (
    .clk(clk), .abajo(pixelpersonaje_479_sar), .izq(c14[2]), .der(pixelpersonaje_510_siz), .dir(in_1),
    .sar(pixelpersonaje_478_sar), .siz(pixelpersonaje_478_siz), .sde(c15[2]), .in_8(s14os15), .in_7(in_2),
    .in_5(in_3));
  PixelPersonaje pixelpersonaje_479 (
    .clk(clk), .abajo(pixelpersonaje_480_sar), .izq(c14[1]), .der(pixelpersonaje_511_siz), .dir(in_1),
    .sar(pixelpersonaje_479_sar), .siz(pixelpersonaje_479_siz), .sde(c15[1]), .in_8(s14os15), .in_7(in_2),
    .in_5(in_3));
  PixelPersonaje pixelpersonaje_480 (
    .clk(clk), .abajo(c15[31]), .izq(c14[0]), .der(pixelpersonaje_512_siz), .dir(in_1),
    .sar(pixelpersonaje_480_sar), .siz(pixelpersonaje_480_siz), .sde(c15[0]), .in_7(in_2), .in_5(in_3));  // open: in_8
  PixelPersonaje pixelpersonaje_481 (
    .clk(clk), .abajo(pixelpersonaje_482_sar), .izq(c15[31]), .der(c1[31]), .dir(in_1),
    .siz(pixelpersonaje_481_siz), .sde(c16[31]), .in_7(in_2), .in_5(in_3));  // open: sar, in_8
  PixelPersonaje pixelpersonaje_482 (
    .clk(clk), .abajo(pixelpersonaje_483_sar), .izq(c15[30]), .der(c1[30]), .dir(in_1),
    .sar(pixelpersonaje_482_sar), .siz(pixelpersonaje_482_siz), .sde(c16[30]), .in_7(in_2), .in_5(in_3));  // open: in_8
  PixelPersonaje pixelpersonaje_483 (
    .clk(clk), .abajo(pixelpersonaje_484_sar), .izq(c15[29]), .der(c1[29]), .dir(in_1),
    .sar(pixelpersonaje_483_sar), .siz(pixelpersonaje_483_siz), .sde(c16[29]), .in_7(in_2), .in_5(in_3));  // open: in_8
  PixelPersonaje pixelpersonaje_484 (
    .clk(clk), .abajo(pixelpersonaje_485_sar), .izq(c15[28]), .der(c1[28]), .dir(in_1),
    .sar(pixelpersonaje_484_sar), .siz(pixelpersonaje_484_siz), .sde(c16[28]), .in_7(in_2), .in_5(in_3));  // open: in_8
  PixelPersonaje pixelpersonaje_485 (
    .clk(clk), .abajo(pixelpersonaje_486_sar), .izq(c15[27]), .der(c1[27]), .dir(in_1),
    .sar(pixelpersonaje_485_sar), .siz(pixelpersonaje_485_siz), .sde(c16[27]), .in_7(in_2), .in_5(in_3));  // open: in_8
  PixelPersonaje pixelpersonaje_486 (
    .clk(clk), .abajo(pixelpersonaje_487_sar), .izq(c15[26]), .der(c1[26]), .dir(in_1),
    .sar(pixelpersonaje_486_sar), .siz(pixelpersonaje_486_siz), .sde(c16[26]), .in_7(in_2), .in_5(in_3));  // open: in_8
  PixelPersonaje pixelpersonaje_487 (
    .clk(clk), .abajo(pixelpersonaje_488_sar), .izq(c15[25]), .der(c1[25]), .dir(in_1),
    .sar(pixelpersonaje_487_sar), .siz(pixelpersonaje_487_siz), .sde(c16[25]), .in_7(in_2), .in_5(in_3));  // open: in_8
  PixelPersonaje pixelpersonaje_488 (
    .clk(clk), .abajo(pixelpersonaje_489_sar), .izq(c15[24]), .der(c1[24]), .dir(in_1),
    .sar(pixelpersonaje_488_sar), .siz(pixelpersonaje_488_siz), .sde(c16[24]), .in_7(in_2), .in_5(in_3));  // open: in_8
  PixelPersonaje pixelpersonaje_489 (
    .clk(clk), .abajo(pixelpersonaje_490_sar), .izq(c15[23]), .der(c1[23]), .dir(in_1),
    .sar(pixelpersonaje_489_sar), .siz(pixelpersonaje_489_siz), .sde(c16[23]), .in_7(in_2), .in_5(in_3));  // open: in_8
  PixelPersonaje pixelpersonaje_490 (
    .clk(clk), .abajo(pixelpersonaje_491_sar), .izq(c15[22]), .der(c1[22]), .dir(in_1),
    .sar(pixelpersonaje_490_sar), .siz(pixelpersonaje_490_siz), .sde(c16[22]), .in_7(in_2), .in_5(in_3));  // open: in_8
  PixelPersonaje pixelpersonaje_491 (
    .clk(clk), .abajo(pixelpersonaje_492_sar), .izq(c15[21]), .der(c1[21]), .dir(in_1),
    .sar(pixelpersonaje_491_sar), .siz(pixelpersonaje_491_siz), .sde(c16[21]), .in_7(in_2), .in_5(in_3));  // open: in_8
  PixelPersonaje pixelpersonaje_492 (
    .clk(clk), .abajo(pixelpersonaje_493_sar), .izq(c15[20]), .der(c1[20]), .dir(in_1),
    .sar(pixelpersonaje_492_sar), .siz(pixelpersonaje_492_siz), .sde(c16[20]), .in_7(in_2), .in_5(in_3));  // open: in_8
  PixelPersonaje pixelpersonaje_493 (
    .clk(clk), .abajo(pixelpersonaje_494_sar), .izq(c15[19]), .der(c1[19]), .dir(in_1),
    .sar(pixelpersonaje_493_sar), .siz(pixelpersonaje_493_siz), .sde(c16[19]), .in_7(in_2), .in_5(in_3));  // open: in_8
  PixelPersonaje pixelpersonaje_494 (
    .clk(clk), .abajo(pixelpersonaje_495_sar), .izq(c15[18]), .der(c1[18]), .dir(in_1),
    .sar(pixelpersonaje_494_sar), .siz(pixelpersonaje_494_siz), .sde(c16[18]), .in_7(in_2), .in_5(in_3));  // open: in_8
  PixelPersonaje pixelpersonaje_495 (
    .clk(clk), .abajo(pixelpersonaje_496_sar), .izq(c15[17]), .der(c1[17]), .dir(in_1),
    .sar(pixelpersonaje_495_sar), .siz(pixelpersonaje_495_siz), .sde(c16[17]), .in_7(in_2), .in_5(in_3));  // open: in_8
  PixelPersonaje pixelpersonaje_496 (
    .clk(clk), .abajo(pixelpersonaje_497_sar), .izq(c15[16]), .der(c1[16]), .dir(in_1),
    .sar(pixelpersonaje_496_sar), .siz(pixelpersonaje_496_siz), .sde(c16[16]), .in_7(in_2), .in_5(in_3));  // open: in_8
  PixelPersonaje pixelpersonaje_497 (
    .clk(clk), .abajo(pixelpersonaje_498_sar), .izq(c15[15]), .der(c1[15]), .dir(in_1),
    .sar(pixelpersonaje_497_sar), .siz(pixelpersonaje_497_siz), .sde(c16[15]), .in_7(in_2), .in_5(in_3));  // open: in_8
  PixelPersonaje pixelpersonaje_498 (
    .clk(clk), .abajo(pixelpersonaje_499_sar), .izq(c15[14]), .der(c1[14]), .dir(in_1),
    .sar(pixelpersonaje_498_sar), .siz(pixelpersonaje_498_siz), .sde(c16[14]), .in_7(in_2), .in_5(in_3));  // open: in_8
  PixelPersonaje pixelpersonaje_499 (
    .clk(clk), .abajo(pixelpersonaje_500_sar), .izq(c15[13]), .der(c1[13]), .dir(in_1),
    .sar(pixelpersonaje_499_sar), .siz(pixelpersonaje_499_siz), .sde(c16[13]), .in_7(in_2), .in_5(in_3));  // open: in_8
  PixelPersonaje pixelpersonaje_500 (
    .clk(clk), .abajo(pixelpersonaje_501_sar), .izq(c15[12]), .der(c1[12]), .dir(in_1),
    .sar(pixelpersonaje_500_sar), .siz(pixelpersonaje_500_siz), .sde(c16[12]), .in_7(in_2), .in_5(in_3));  // open: in_8
  PixelPersonaje pixelpersonaje_501 (
    .clk(clk), .abajo(pixelpersonaje_502_sar), .izq(c15[11]), .der(c1[11]), .dir(in_1),
    .sar(pixelpersonaje_501_sar), .siz(pixelpersonaje_501_siz), .sde(c16[11]), .in_7(in_2), .in_5(in_3));  // open: in_8
  PixelPersonaje pixelpersonaje_502 (
    .clk(clk), .abajo(pixelpersonaje_503_sar), .izq(c15[10]), .der(c1[10]), .dir(in_1),
    .sar(pixelpersonaje_502_sar), .siz(pixelpersonaje_502_siz), .sde(c16[10]), .in_7(in_2), .in_5(in_3));  // open: in_8
  PixelPersonaje pixelpersonaje_503 (
    .clk(clk), .abajo(pixelpersonaje_504_sar), .izq(c15[9]), .der(c1[9]), .dir(in_1),
    .sar(pixelpersonaje_503_sar), .siz(pixelpersonaje_503_siz), .sde(c16[9]), .in_7(in_2), .in_5(in_3));  // open: in_8
  PixelPersonaje pixelpersonaje_504 (
    .clk(clk), .abajo(pixelpersonaje_505_sar), .izq(c15[8]), .der(c1[8]), .dir(in_1),
    .sar(pixelpersonaje_504_sar), .siz(pixelpersonaje_504_siz), .sde(c16[8]), .in_7(in_2), .in_5(in_3));  // open: in_8
  PixelPersonaje pixelpersonaje_505 (
    .clk(clk), .abajo(pixelpersonaje_506_sar), .izq(c15[7]), .der(c1[7]), .dir(in_1),
    .sar(pixelpersonaje_505_sar), .siz(pixelpersonaje_505_siz), .sde(c16[7]), .in_7(in_2), .in_5(in_3));  // open: in_8
  PixelPersonaje pixelpersonaje_506 (
    .clk(clk), .abajo(pixelpersonaje_507_sar), .izq(c15[6]), .der(c1[6]), .dir(in_1),
    .sar(pixelpersonaje_506_sar), .siz(pixelpersonaje_506_siz), .sde(c16[6]), .in_7(in_2), .in_5(in_3));  // open: in_8
  PixelPersonaje pixelpersonaje_507 (
    .clk(clk), .abajo(pixelpersonaje_508_sar), .izq(c15[5]), .der(c1[5]), .dir(in_1),
    .sar(pixelpersonaje_507_sar), .siz(pixelpersonaje_507_siz), .sde(c16[5]), .in_7(in_2), .in_5(in_3));  // open: in_8
  PixelPersonaje pixelpersonaje_508 (
    .clk(clk), .abajo(pixelpersonaje_509_sar), .izq(c15[4]), .der(c1[4]), .dir(in_1),
    .sar(pixelpersonaje_508_sar), .siz(pixelpersonaje_508_siz), .sde(c16[4]), .in_7(in_2), .in_5(in_3));  // open: in_8
  PixelPersonaje pixelpersonaje_509 (
    .clk(clk), .abajo(pixelpersonaje_510_sar), .izq(c15[3]), .der(c1[3]), .dir(in_1),
    .sar(pixelpersonaje_509_sar), .siz(pixelpersonaje_509_siz), .sde(c16[3]), .in_7(in_2), .in_5(in_3));  // open: in_8
  PixelPersonaje pixelpersonaje_510 (
    .clk(clk), .abajo(pixelpersonaje_511_sar), .izq(c15[2]), .der(c1[2]), .dir(in_1),
    .sar(pixelpersonaje_510_sar), .siz(pixelpersonaje_510_siz), .sde(c16[2]), .in_8(s15), .in_7(in_2),
    .in_5(in_3));
  PixelPersonaje pixelpersonaje_511 (
    .clk(clk), .abajo(pixelpersonaje_512_sar), .izq(c15[1]), .der(c1[1]), .dir(in_1),
    .sar(pixelpersonaje_511_sar), .siz(pixelpersonaje_511_siz), .sde(c16[1]), .in_8(s15), .in_7(in_2),
    .in_5(in_3));
  PixelPersonaje pixelpersonaje_512 (
    .clk(clk), .abajo(c16[31]), .izq(c15[0]), .der(c1[0]), .dir(in_1), .sar(pixelpersonaje_512_sar),
    .siz(pixelpersonaje_512_siz), .sde(c16[0]), .in_7(in_2), .in_5(in_3));  // open: in_8
  Clock clock_2 (.out(clk));

  // Other names for the same wires on the sheet: _497 = c1[0]; _481 = c1[1]; _465 = c1[2]; _449 = c1[3]; _433 = c1[4];
  //   _417 = c1[5]; _401 = c1[6]; _385 = c1[7]; _369 = c1[8]; _353 = c1[9]; _337 = c1[10]; _321 = c1[11];
  //   _305 = c1[12]; _289 = c1[13]; _273 = c1[14]; _257 = c1[15]; _241 = c1[16]; _225 = c1[17]; _209 = c1[18];
  //   _193 = c1[19]; _177 = c1[20]; _161 = c1[21]; _145 = c1[22]; _129 = c1[23]; _113 = c1[24]; _97 = c1[25];
  //   _81 = c1[26]; _65 = c1[27]; _49 = c1[28]; _33 = c1[29]; _17 = c1[30]; _1 = c1[31]; _498 = c2[0]; _482 = c2[1];
  //   _466 = c2[2]; _450 = c2[3]; _434 = c2[4]; _418 = c2[5]; _402 = c2[6]; _386 = c2[7]; _370 = c2[8]; _354 = c2[9];
  //   _338 = c2[10]; _322 = c2[11]; _306 = c2[12]; _290 = c2[13]; _274 = c2[14]; _258 = c2[15]; _242 = c2[16];
  //   _226 = c2[17]; _210 = c2[18]; _194 = c2[19]; _178 = c2[20]; _162 = c2[21]; _146 = c2[22]; _130 = c2[23];
  //   _114 = c2[24]; _98 = c2[25]; _82 = c2[26]; _66 = c2[27]; _50 = c2[28]; _34 = c2[29]; _18 = c2[30]; _2 = c2[31];
  //   _499 = c3[0]; _483 = c3[1]; _467 = c3[2]; _451 = c3[3]; _435 = c3[4]; _419 = c3[5]; _403 = c3[6]; _387 = c3[7];
  //   _371 = c3[8]; _355 = c3[9]; _339 = c3[10]; _323 = c3[11]; _307 = c3[12]; _291 = c3[13]; _275 = c3[14];
  //   _259 = c3[15]; _243 = c3[16]; _227 = c3[17]; _211 = c3[18]; _195 = c3[19]; _179 = c3[20]; _163 = c3[21];
  //   _147 = c3[22]; _131 = c3[23]; _115 = c3[24]; _99 = c3[25]; _83 = c3[26]; _67 = c3[27]; _51 = c3[28];
  //   _35 = c3[29]; _19 = c3[30]; _3 = c3[31]; _500 = c4[0]; _484 = c4[1]; _468 = c4[2]; _452 = c4[3]; _436 = c4[4];
  //   _420 = c4[5]; _404 = c4[6]; _388 = c4[7]; _372 = c4[8]; _356 = c4[9]; _340 = c4[10]; _324 = c4[11];
  //   _308 = c4[12]; _292 = c4[13]; _276 = c4[14]; _260 = c4[15]; _244 = c4[16]; _228 = c4[17]; _212 = c4[18];
  //   _196 = c4[19]; _180 = c4[20]; _164 = c4[21]; _148 = c4[22]; _132 = c4[23]; _116 = c4[24]; _100 = c4[25];
  //   _84 = c4[26]; _68 = c4[27]; _52 = c4[28]; _36 = c4[29]; _20 = c4[30]; _4 = c4[31]; _501 = c5[0]; _485 = c5[1];
  //   _469 = c5[2]; _453 = c5[3]; _437 = c5[4]; _421 = c5[5]; _405 = c5[6]; _389 = c5[7]; _373 = c5[8]; _357 = c5[9];
  //   _341 = c5[10]; _325 = c5[11]; _309 = c5[12]; _293 = c5[13]; _277 = c5[14]; _261 = c5[15]; _245 = c5[16];
  //   _229 = c5[17]; _213 = c5[18]; _197 = c5[19]; _181 = c5[20]; _165 = c5[21]; _149 = c5[22]; _133 = c5[23];
  //   _117 = c5[24]; _101 = c5[25]; _85 = c5[26]; _69 = c5[27]; _53 = c5[28]; _37 = c5[29]; _21 = c5[30]; _5 = c5[31];
  //   _502 = c6[0]; _486 = c6[1]; _470 = c6[2]; _454 = c6[3]; _438 = c6[4]; _422 = c6[5]; _406 = c6[6]; _390 = c6[7];
  //   _374 = c6[8]; _358 = c6[9]; _342 = c6[10]; _326 = c6[11]; _310 = c6[12]; _294 = c6[13]; _278 = c6[14];
  //   _262 = c6[15]; _246 = c6[16]; _230 = c6[17]; _214 = c6[18]; _198 = c6[19]; _182 = c6[20]; _166 = c6[21];
  //   _150 = c6[22]; _134 = c6[23]; _118 = c6[24]; _102 = c6[25]; _86 = c6[26]; _70 = c6[27]; _54 = c6[28];
  //   _38 = c6[29]; _22 = c6[30]; _6 = c6[31]; _503 = c7[0]; _487 = c7[1]; _471 = c7[2]; _455 = c7[3]; _439 = c7[4];
  //   _423 = c7[5]; _407 = c7[6]; _391 = c7[7]; _375 = c7[8]; _359 = c7[9]; _343 = c7[10]; _327 = c7[11];
  //   _311 = c7[12]; _295 = c7[13]; _279 = c7[14]; _263 = c7[15]; _247 = c7[16]; _231 = c7[17]; _215 = c7[18];
  //   _199 = c7[19]; _183 = c7[20]; _167 = c7[21]; _151 = c7[22]; _135 = c7[23]; _119 = c7[24]; _103 = c7[25];
  //   _87 = c7[26]; _71 = c7[27]; _55 = c7[28]; _39 = c7[29]; _23 = c7[30]; _7 = c7[31]; _504 = c8[0]; _488 = c8[1];
  //   _472 = c8[2]; _456 = c8[3]; _440 = c8[4]; _424 = c8[5]; _408 = c8[6]; _392 = c8[7]; _376 = c8[8]; _360 = c8[9];
  //   _344 = c8[10]; _328 = c8[11]; _312 = c8[12]; _296 = c8[13]; _280 = c8[14]; _264 = c8[15]; _248 = c8[16];
  //   _232 = c8[17]; _216 = c8[18]; _200 = c8[19]; _184 = c8[20]; _168 = c8[21]; _152 = c8[22]; _136 = c8[23];
  //   _120 = c8[24]; _104 = c8[25]; _88 = c8[26]; _72 = c8[27]; _56 = c8[28]; _40 = c8[29]; _24 = c8[30]; _8 = c8[31];
  //   _505 = c9[0]; _489 = c9[1]; _473 = c9[2]; _457 = c9[3]; _441 = c9[4]; _425 = c9[5]; _409 = c9[6]; _393 = c9[7];
  //   _377 = c9[8]; _361 = c9[9]; _345 = c9[10]; _329 = c9[11]; _313 = c9[12]; _297 = c9[13]; _281 = c9[14];
  //   _265 = c9[15]; _249 = c9[16]; _233 = c9[17]; _217 = c9[18]; _201 = c9[19]; _185 = c9[20]; _169 = c9[21];
  //   _153 = c9[22]; _137 = c9[23]; _121 = c9[24]; _105 = c9[25]; _89 = c9[26]; _73 = c9[27]; _57 = c9[28];
  //   _41 = c9[29]; _25 = c9[30]; _9 = c9[31]; _506 = c10[0]; _490 = c10[1]; _474 = c10[2]; _458 = c10[3];
  //   _442 = c10[4]; _426 = c10[5]; _410 = c10[6]; _394 = c10[7]; _378 = c10[8]; _362 = c10[9]; _346 = c10[10];
  //   _330 = c10[11]; _314 = c10[12]; _298 = c10[13]; _282 = c10[14]; _266 = c10[15]; _250 = c10[16]; _234 = c10[17];
  //   _218 = c10[18]; _202 = c10[19]; _186 = c10[20]; _170 = c10[21]; _154 = c10[22]; _138 = c10[23]; _122 = c10[24];
  //   _106 = c10[25]; _90 = c10[26]; _74 = c10[27]; _58 = c10[28]; _42 = c10[29]; _26 = c10[30]; _10 = c10[31];
  //   _507 = c11[0]; _491 = c11[1]; _475 = c11[2]; _459 = c11[3]; _443 = c11[4]; _427 = c11[5]; _411 = c11[6];
  //   _395 = c11[7]; _379 = c11[8]; _363 = c11[9]; _347 = c11[10]; _331 = c11[11]; _315 = c11[12]; _299 = c11[13];
  //   _283 = c11[14]; _267 = c11[15]; _251 = c11[16]; _235 = c11[17]; _219 = c11[18]; _203 = c11[19]; _187 = c11[20];
  //   _171 = c11[21]; _155 = c11[22]; _139 = c11[23]; _123 = c11[24]; _107 = c11[25]; _91 = c11[26]; _75 = c11[27];
  //   _59 = c11[28]; _43 = c11[29]; _27 = c11[30]; _11 = c11[31]; _508 = c12[0]; _492 = c12[1]; _476 = c12[2];
  //   _460 = c12[3]; _444 = c12[4]; _428 = c12[5]; _412 = c12[6]; _396 = c12[7]; _380 = c12[8]; _364 = c12[9];
  //   _348 = c12[10]; _332 = c12[11]; _316 = c12[12]; _300 = c12[13]; _284 = c12[14]; _268 = c12[15]; _252 = c12[16];
  //   _236 = c12[17]; _220 = c12[18]; _204 = c12[19]; _188 = c12[20]; _172 = c12[21]; _156 = c12[22]; _140 = c12[23];
  //   _124 = c12[24]; _108 = c12[25]; _92 = c12[26]; _76 = c12[27]; _60 = c12[28]; _44 = c12[29]; _28 = c12[30];
  //   _12 = c12[31]; _509 = c13[0]; _493 = c13[1]; _477 = c13[2]; _461 = c13[3]; _445 = c13[4]; _429 = c13[5];
  //   _413 = c13[6]; _397 = c13[7]; _381 = c13[8]; _365 = c13[9]; _349 = c13[10]; _333 = c13[11]; _317 = c13[12];
  //   _301 = c13[13]; _285 = c13[14]; _269 = c13[15]; _253 = c13[16]; _237 = c13[17]; _221 = c13[18]; _205 = c13[19];
  //   _189 = c13[20]; _173 = c13[21]; _157 = c13[22]; _141 = c13[23]; _125 = c13[24]; _109 = c13[25]; _93 = c13[26];
  //   _77 = c13[27]; _61 = c13[28]; _45 = c13[29]; _29 = c13[30]; _13 = c13[31]; _510 = c14[0]; _494 = c14[1];
  //   _478 = c14[2]; _462 = c14[3]; _446 = c14[4]; _430 = c14[5]; _414 = c14[6]; _398 = c14[7]; _382 = c14[8];
  //   _366 = c14[9]; _350 = c14[10]; _334 = c14[11]; _318 = c14[12]; _302 = c14[13]; _286 = c14[14]; _270 = c14[15];
  //   _254 = c14[16]; _238 = c14[17]; _222 = c14[18]; _206 = c14[19]; _190 = c14[20]; _174 = c14[21]; _158 = c14[22];
  //   _142 = c14[23]; _126 = c14[24]; _110 = c14[25]; _94 = c14[26]; _78 = c14[27]; _62 = c14[28]; _46 = c14[29];
  //   _30 = c14[30]; _14 = c14[31]; _511 = c15[0]; _495 = c15[1]; _479 = c15[2]; _463 = c15[3]; _447 = c15[4];
  //   _431 = c15[5]; _415 = c15[6]; _399 = c15[7]; _383 = c15[8]; _367 = c15[9]; _351 = c15[10]; _335 = c15[11];
  //   _319 = c15[12]; _303 = c15[13]; _287 = c15[14]; _271 = c15[15]; _255 = c15[16]; _239 = c15[17]; _223 = c15[18];
  //   _207 = c15[19]; _191 = c15[20]; _175 = c15[21]; _159 = c15[22]; _143 = c15[23]; _127 = c15[24]; _111 = c15[25];
  //   _95 = c15[26]; _79 = c15[27]; _63 = c15[28]; _47 = c15[29]; _31 = c15[30]; _15 = c15[31]; _512 = c16[0];
  //   _496 = c16[1]; _480 = c16[2]; _464 = c16[3]; _448 = c16[4]; _432 = c16[5]; _416 = c16[6]; _400 = c16[7];
  //   _384 = c16[8]; _368 = c16[9]; _352 = c16[10]; _336 = c16[11]; _320 = c16[12]; _304 = c16[13]; _288 = c16[14];
  //   _272 = c16[15]; _256 = c16[16]; _240 = c16[17]; _224 = c16[18]; _208 = c16[19]; _192 = c16[20]; _176 = c16[21];
  //   _160 = c16[22]; _144 = c16[23]; _128 = c16[24]; _112 = c16[25]; _96 = c16[26]; _80 = c16[27]; _64 = c16[28];
  //   _48 = c16[29]; _32 = c16[30]; _16 = c16[31]; dir[1:0] = in_1; off = in_3; reset = in_2; s5 = s4; start16 = s15
endmodule

// pix
module PixelPersonaje (
  input  clk,
  input  abajo,
  input  izq,
  input  der,
  input  in_5,
  input  [1:0] dir,
  input  in_7,
  input  in_8,
  output sar,
  output siz,
  output sde
);

  wire multiplexer_1_out;

  Multiplexer #(.select(2)) multiplexer_1 (
    .in0(sar), .in1(abajo), .in2(izq), .in3(der), .out(multiplexer_1_out), .sel(dir));  // open: en
  D_Flip_Flop d_ff_1 (.clk(clk), .D(multiplexer_1_out), .Q(sar), .preset(in_8), .en(in_7), .reset(in_5));  // open: Qn

  assign sde = sar;
  assign siz = sar;
endmodule

// ale
module Random (
  input  generar,
  input  reset,
  output [31:0] c1,
  output [31:0] c2,
  output [31:0] c3,
  output [31:0] c4,
  output [31:0] c5,
  output [31:0] c6,
  output [31:0] c7,
  output [31:0] c8,
  output [31:0] c9,
  output [31:0] c10,
  output [31:0] c11,
  output [31:0] c12,
  output [31:0] c13,
  output [31:0] c14,
  output [31:0] c15,
  output [31:0] c16
);

  wire comparator_1_lt, or_1_out;
  wire [3:0] columna_out, divider_1_rem;
  wire [4:0] adder_1_out, adder_2_out, anterior_q, randombarrera_1_out_5;
  wire [31:0] demultiplexer_1_out1, demultiplexer_1_out2, demultiplexer_1_out3, demultiplexer_1_out4,
       demultiplexer_1_out5, demultiplexer_1_out6, demultiplexer_1_out7, demultiplexer_1_out8,
       demultiplexer_1_out9, demultiplexer_1_out10, demultiplexer_1_out11, demultiplexer_1_out12,
       demultiplexer_1_out13, demultiplexer_1_out14, demultiplexer_1_out15;
  wire [31:6] decoder_1_out25;

  or or_1 (or_1_out, reset, comparator_1_lt);
  Random_part #(.width(4), .seed(-200)) columna (.clk(generar), .next(or_1_out), .out(columna_out));  // open: clr
  Register #(.width(5)) anterior (
    .D(randombarrera_1_out_5), .en(or_1_out), .Q(anterior_q), .clk(generar));  // open: clr
  Adder #(.width(5)) adder_1 (.a(5'b00101), .b(anterior_q), .out(adder_1_out));  // open: cin, cout
  Adder #(.width(5)) adder_2 (.a(anterior_q), .b(5'b00011), .out(adder_2_out));  // open: cin, cout
  // Probe on anterior_q
  // Probe on 5'b11000
  Decoder #(.select(5), .enable("false")) decoder_1 (
    .out0(decoder_1_out25[31]), .out1(decoder_1_out25[30]), .out2(decoder_1_out25[29]),
    .out3(decoder_1_out25[28]), .out4(decoder_1_out25[27]), .out5(decoder_1_out25[26]),
    .out6(decoder_1_out25[25]), .out7(decoder_1_out25[24]), .out8(decoder_1_out25[23]),
    .out9(decoder_1_out25[22]), .out10(decoder_1_out25[21]), .out11(decoder_1_out25[20]),
    .out12(decoder_1_out25[19]), .out13(decoder_1_out25[18]), .out14(decoder_1_out25[17]),
    .out15(decoder_1_out25[16]), .out16(decoder_1_out25[15]), .out17(decoder_1_out25[14]),
    .out18(decoder_1_out25[13]), .out19(decoder_1_out25[12]), .out20(decoder_1_out25[11]),
    .out21(decoder_1_out25[10]), .out22(decoder_1_out25[9]), .out23(decoder_1_out25[8]),
    .out24(decoder_1_out25[7]), .out25(decoder_1_out25[6]), .sel(randombarrera_1_out_5));  // open: out26, out27, out28, out29, out30, out31
  randomBarrera randombarrera_1 (
    .sup(adder_1_out), .inf(adder_2_out), .click(generar), .activo(or_1_out), .out_5(randombarrera_1_out_5));
  Comparator #(.width(5), .mode("unsigned")) comparator_1 (
    .a(anterior_q), .b(5'b11000), .lt(comparator_1_lt));  // open: gt, eq
  Divider #(.width(4)) divider_1 (.a(columna_out), .b(4'b1011), .rem(divider_1_rem));  // open: out, upper
  Demultiplexer #(.select(4), .width(32), .disabled(0), .enable("false")) demultiplexer_1 (
    .out0(c1), .out1(demultiplexer_1_out1), .out2(demultiplexer_1_out2), .out3(demultiplexer_1_out3),
    .out4(demultiplexer_1_out4), .out5(demultiplexer_1_out5), .out6(demultiplexer_1_out6),
    .out7(demultiplexer_1_out7), .out8(demultiplexer_1_out8), .out9(demultiplexer_1_out9),
    .out10(demultiplexer_1_out10), .out11(demultiplexer_1_out11), .out12(demultiplexer_1_out12),
    .out13(demultiplexer_1_out13), .out14(demultiplexer_1_out14), .out15(demultiplexer_1_out15),
    .in({decoder_1_out25, {6{1'b0}}}), .sel(divider_1_rem));
  assign c16 = demultiplexer_1_out10 | demultiplexer_1_out11 | demultiplexer_1_out12 | demultiplexer_1_out13 | demultiplexer_1_out14 | demultiplexer_1_out15;  // OR_Gate or_2, 32 bits wide
  assign c2 = c1 | demultiplexer_1_out1;  // OR_Gate or_3, 32 bits wide
  assign c3 = c1 | demultiplexer_1_out1 | demultiplexer_1_out2;  // OR_Gate or_4, 32 bits wide
  assign c4 = c1 | demultiplexer_1_out1 | demultiplexer_1_out2 | demultiplexer_1_out3;  // OR_Gate or_5, 32 bits wide
  assign c5 = c1 | demultiplexer_1_out1 | demultiplexer_1_out2 | demultiplexer_1_out3 | demultiplexer_1_out4;  // OR_Gate or_6, 32 bits wide
  assign c6 = c1 | demultiplexer_1_out1 | demultiplexer_1_out2 | demultiplexer_1_out3 | demultiplexer_1_out4 | demultiplexer_1_out5;  // OR_Gate or_7, 32 bits wide
  assign c7 = demultiplexer_1_out1 | demultiplexer_1_out2 | demultiplexer_1_out3 | demultiplexer_1_out4 | demultiplexer_1_out5 | demultiplexer_1_out6;  // OR_Gate or_8, 32 bits wide
  assign c8 = demultiplexer_1_out2 | demultiplexer_1_out3 | demultiplexer_1_out4 | demultiplexer_1_out5 | demultiplexer_1_out6 | demultiplexer_1_out7;  // OR_Gate or_9, 32 bits wide
  assign c9 = demultiplexer_1_out3 | demultiplexer_1_out4 | demultiplexer_1_out5 | demultiplexer_1_out6 | demultiplexer_1_out7 | demultiplexer_1_out8;  // OR_Gate or_10, 32 bits wide
  assign c10 = demultiplexer_1_out4 | demultiplexer_1_out5 | demultiplexer_1_out6 | demultiplexer_1_out7 | demultiplexer_1_out8 | demultiplexer_1_out9;  // OR_Gate or_11, 32 bits wide
  assign c11 = demultiplexer_1_out5 | demultiplexer_1_out6 | demultiplexer_1_out7 | demultiplexer_1_out8 | demultiplexer_1_out9 | demultiplexer_1_out10;  // OR_Gate or_12, 32 bits wide
  assign c12 = demultiplexer_1_out6 | demultiplexer_1_out7 | demultiplexer_1_out8 | demultiplexer_1_out9 | demultiplexer_1_out10 | demultiplexer_1_out11;  // OR_Gate or_13, 32 bits wide
  assign c13 = demultiplexer_1_out7 | demultiplexer_1_out8 | demultiplexer_1_out9 | demultiplexer_1_out10 | demultiplexer_1_out11 | demultiplexer_1_out12;  // OR_Gate or_14, 32 bits wide
  assign c14 = demultiplexer_1_out8 | demultiplexer_1_out9 | demultiplexer_1_out10 | demultiplexer_1_out11 | demultiplexer_1_out12 | demultiplexer_1_out13;  // OR_Gate or_15, 32 bits wide
  assign c15 = demultiplexer_1_out9 | demultiplexer_1_out10 | demultiplexer_1_out11 | demultiplexer_1_out12 | demultiplexer_1_out13 | demultiplexer_1_out14;  // OR_Gate or_16, 32 bits wide
endmodule

// personaje
module main (
);

  wire and_1_out, button_1_out, cl1, cl2, cl3, cl4, cl5, cl6, cl7, cl8, cl9, cl10, cl11, cl12, cl13, cl14,
       cl15, cl16, clock_1_out, clock_2_out, clock_3_out, clock_4_out, clock_5_out, crst1, crst2, crst3,
       crst4, crst5, crst6, crst7, crst8, crst9, crst10, crst11, crst12, crst13, crst14, crst15, crst16,
       d_ff_1_q, d_ff_2_q, d_ff_3_q, d_ff_4_q, endgame, endrow, in, not_1_out, or_13_out, or_16_out, p1, p2,
       p3, p4, p5, p6, p7, p8, p9, p10, p11, p12, p13, p14, p15, p16, pointo, register_1_q, roff, starto, win;
  wire [1:0] dir;
  wire [3:0] contador_1_decenas, contador_1_unidades;
  wire [6:0] keyboard_1_data;
  wire [31:0] c1, c2, c3, c4, c5, c6, c7, c8, c9, c10, c11, c12, c13, c14, c15, c16, danger, or_1_out,
       or_2_out, or_5_out, or_6_out, or_7_out, or_9_out, or_11_out, or_12_out, or_15_out, or_17_out,
       or_18_out, or_19_out, or_20_out, or_21_out, or_22_out, or_23_out, or_24_out, r1, r2, r3, r4, r5, r6,
       r7, r8, r9, r10, r11, r12, r13, r14, r15, r16, random_1_out;

  Clock clock_1 (.out(clock_1_out));
  assign or_1_out = c1 | r1;  // OR_Gate or_1, 32 bits wide
  colisiones colisiones_1 (.out_5(crst1), .columna(r1), .personaje(c1), .colision(cl1), .peligro(danger), .destroy(p1));
  Keyboard #(.buflen(2)) keyboard_1 (.clk(clock_1_out), .data(keyboard_1_data));  // open: re, clr, avail
  // Probe on starto
  assign or_2_out = c2 | r2;  // OR_Gate or_2, 32 bits wide
  not not_1 (not_1_out, register_1_q);
  or or_3 (pointo, cl1, cl2, cl3, cl4, cl5, cl6, cl7, cl8, cl9, cl10, cl11, cl12, cl13, cl14, cl15, cl16);
  or or_4 (starto, keyboard_1_data[6], keyboard_1_data[5], keyboard_1_data[4], keyboard_1_data[3], keyboard_1_data[2], keyboard_1_data[1], keyboard_1_data[0]);
  assign or_5_out = c3 | r3;  // OR_Gate or_5, 32 bits wide
  colisiones colisiones_2 (.out_5(crst2), .columna(r2), .personaje(c2), .colision(cl2), .peligro(danger), .destroy(p2));
  colisiones colisiones_3 (.out_5(crst3), .columna(r3), .personaje(c3), .colision(cl3), .peligro(danger), .destroy(p3));
  // Probe on not_1_out
  // Probe on keyboard_1_data
  assign or_6_out = c4 | r4;  // OR_Gate or_6, 32 bits wide
  colisiones colisiones_4 (.out_5(crst4), .columna(r4), .personaje(c4), .colision(cl4), .peligro(danger), .destroy(p4));
  teclado teclado_1 (
    .e6(keyboard_1_data[6]), .e5(keyboard_1_data[5]), .e4(keyboard_1_data[4]), .e3(keyboard_1_data[3]),
    .e2(keyboard_1_data[2]), .e1(keyboard_1_data[1]), .e0(keyboard_1_data[0]), .s1(dir[1]), .s0(dir[0]));
  Clock clock_2 (.out(clock_2_out));
  assign or_7_out = c5 | r5;  // OR_Gate or_7, 32 bits wide
  MallaPersonaje mallapersonaje_1 (
    .in_1(dir), .in_2(not_1_out), .in_3(roff), .in_4(in), .in_5(in), .c1(c1), .c2(c2), .c3(c3), .c4(c4),
    .c5(c5), .c6(c6), .c7(c7), .c8(c8), .c9(c9), .c10(c10), .c11(c11), .c12(c12), .c13(c13), .c14(c14),
    .c15(c15), .c16(c16));  // open: out_22
  and and_1 (and_1_out, pointo, ~starto);  // AND_Gate
  LED led_1 (.in(win));
  LED led_2 (.in(win));
  or or_8 (in, d_ff_1_q, button_1_out);
  Button button_1 (.out(button_1_out));
  D_Flip_Flop #(.trigger("falling")) d_ff_1 (.clk(clock_2_out), .D(roff), .Q(d_ff_1_q));  // open: Qn, preset, en, reset
  assign or_9_out = c6 | r6;  // OR_Gate or_9, 32 bits wide
  colisiones colisiones_5 (.out_5(crst5), .columna(r5), .personaje(c5), .colision(cl5), .peligro(danger), .destroy(p5));
  D_Flip_Flop d_ff_2 (.clk(clock_3_out), .D(endrow), .Q(d_ff_2_q));  // open: Qn, preset, en, reset
  Clock clock_3 (.out(clock_3_out));
  Register #(.width(1), .trigger("high")) register_1 (
    .D(and_1_out), .Q(register_1_q), .clk(clock_4_out));  // open: en, clr
  LED led_3 (.in(win));
  LED led_4 (.in(win));
  LED led_5 (.in(win));
  LED led_6 (.in(win));
  LED led_7 (.in(win));
  LED led_8 (.in(win));
  DotMatrix #(.matrixcols(16), .matrixrows(32)) dotmatrix_1 (
    .col0(or_1_out), .col1(or_2_out), .col2(or_5_out), .col3(or_6_out), .col4(or_7_out), .col5(or_9_out),
    .col6(or_11_out), .col7(or_12_out), .col8(or_15_out), .col9(or_17_out), .col10(or_18_out),
    .col11(or_20_out), .col12(or_21_out), .col13(or_22_out), .col14(or_23_out), .col15(or_24_out));
  colisiones colisiones_6 (.out_5(crst6), .columna(r6), .personaje(c6), .colision(cl6), .peligro(danger), .destroy(p6));
  or or_10 (roff, d_ff_2_q, endgame);
  LED led_9 (.in(win));
  LED led_10 (.in(win));
  LED led_11 (.in(win));
  LED led_12 (.in(win));
  LED led_13 (.in(win));
  assign or_11_out = c7 | r7;  // OR_Gate or_11, 32 bits wide
  colisiones colisiones_7 (.out_5(crst7), .columna(r7), .personaje(c7), .colision(cl7), .peligro(danger), .destroy(p7));
  memoria memoria_1 (
    .in_1(clock_4_out), .in_2(or_13_out), .out_3(r1), .out_4(r2), .out_5(r3), .out_6(r4), .out_7(r5),
    .out_8(r6), .out_9(r7), .out_10(r8), .out_11(r9), .out_12(r10), .out_13(r11), .out_14(r12), .out_15(r13),
    .out_16(r14), .out_17(r15), .out_18(r16));
  Clock clock_4 (.out(clock_4_out));
  LED led_14 (.in(win));
  LED led_15 (.in(win));
  LED led_16 (.in(win));
  LED led_17 (.in(win));
  LED led_18 (.in(win));
  LED led_19 (.in(win));
  LED led_20 (.in(win));
  LED led_21 (.in(win));
  DotMatrix #(.matrixcols(1), .matrixrows(32)) dotmatrix_2 (.col0(danger));
  assign or_12_out = c8 | r8;  // OR_Gate or_12, 32 bits wide
  colisiones colisiones_8 (.out_5(crst8), .columna(r8), .personaje(c8), .colision(cl8), .peligro(danger), .destroy(p8));
  or or_13 (or_13_out, endrow, endgame);
  or or_14 (endrow, crst1, crst2, crst3, crst4, crst5, crst6, crst7, crst8, crst9, crst10, crst11, crst12, crst13, crst14, crst15, crst16);
  LED led_22 (.in(win));
  LED led_23 (.in(win));
  LED led_24 (.in(win));
  LED led_25 (.in(win));
  Hex_Digit_Display hex_digit_display_1 (.value(contador_1_decenas));  // open: dp
  assign or_15_out = c9 | r9;  // OR_Gate or_15, 32 bits wide
  colisiones colisiones_9 (.out_5(crst9), .columna(r9), .personaje(c9), .colision(cl9), .peligro(danger), .destroy(p9));
  Hex_Digit_Display hex_digit_display_2 (.value(contador_1_unidades));  // open: dp
  contador contador_1 (
    .diez_en_diez(endrow), .decenas(contador_1_decenas), .unidades(contador_1_unidades), .in_3(win),
    .generar(or_16_out));
  or or_16 (or_16_out, d_ff_3_q, d_ff_4_q);
  assign or_17_out = c10 | r10;  // OR_Gate or_17, 32 bits wide
  Clock clock_5 (.out(clock_5_out));
  colisiones colisiones_10 (
    .out_5(crst10), .columna(r10), .personaje(c10), .colision(cl10), .peligro(danger), .destroy(p10));
  D_Flip_Flop d_ff_3 (.clk(clock_5_out), .D(pointo), .Q(d_ff_3_q));  // open: Qn, preset, en, reset
  D_Flip_Flop d_ff_4 (.clk(clock_5_out), .D(endrow), .Q(d_ff_4_q));  // open: Qn, preset, en, reset
  assign or_18_out = c11 | r11;  // OR_Gate or_18, 32 bits wide
  colisiones colisiones_11 (
    .out_5(crst11), .columna(r11), .personaje(c11), .colision(cl11), .peligro(danger), .destroy(p11));
  assign or_19_out = r1 | r2 | r3 | r4 | r5 | r6 | r7 | r8 | r9 | r10 | r11 | r12 | r13 | r14 | r15 | r16;  // OR_Gate or_19, 32 bits wide
  assign or_20_out = c12 | r12;  // OR_Gate or_20, 32 bits wide
  colisiones colisiones_12 (
    .out_5(crst12), .columna(r12), .personaje(c12), .colision(cl12), .peligro(danger), .destroy(p12));
  assign or_21_out = c13 | r13;  // OR_Gate or_21, 32 bits wide
  colisiones colisiones_13 (
    .out_5(crst13), .columna(r13), .personaje(c13), .colision(cl13), .peligro(danger), .destroy(p13));
  assign or_22_out = c14 | r14;  // OR_Gate or_22, 32 bits wide
  assign danger = or_19_out & random_1_out;  // AND_Gate and_2, 32 bits wide
  Random_part #(.width(32), .trigger("falling")) random_1 (.clk(endrow), .out(random_1_out));  // open: next, clr
  colisiones colisiones_14 (
    .out_5(crst14), .columna(r14), .personaje(c14), .colision(cl14), .peligro(danger), .destroy(p14));
  assign or_23_out = c15 | r15;  // OR_Gate or_23, 32 bits wide
  colisiones colisiones_15 (
    .out_5(crst15), .columna(r15), .personaje(c15), .colision(cl15), .peligro(danger), .destroy(p15));
  assign or_24_out = c16 | r16;  // OR_Gate or_24, 32 bits wide
  colisiones colisiones_16 (
    .out_5(crst16), .columna(r16), .personaje(c16), .colision(cl16), .peligro(danger), .destroy(p16));
  or or_25 (endgame, p1, p2, p3, p4, p5, p6, p7, p8, p9, p10, p11, p12, p13, p14, p15, p16);

  // Other names for the same wires on the sheet: resetpj = endrow
endmodule

module teclado (
  input  e6,
  input  e5,
  input  e4,
  input  e3,
  input  e2,
  input  e1,
  input  e0,
  output s1,
  output s0
);

  wire and_1_out, and_2_out, not_1_out, not_2_out, not_3_out, not_4_out, not_5_out, not_6_out, not_7_out,
       not_8_out, not_9_out, not_10_out, not_11_out;

  not not_1 (not_1_out, e4);
  not not_2 (not_2_out, e3);
  not not_3 (not_3_out, e2);
  not not_4 (not_4_out, e1);
  not not_5 (not_5_out, e4);
  not not_6 (not_6_out, e3);
  not not_7 (not_7_out, e1);
  not not_8 (not_8_out, e0);
  not not_9 (not_9_out, e6);
  not not_10 (not_10_out, e5);
  not not_11 (not_11_out, e2);
  and and_1 (and_1_out, e6, e5, not_1_out, not_2_out, not_3_out, not_4_out, e0);
  and and_2 (and_2_out, e6, e5, not_5_out, not_6_out, e2, not_7_out, not_8_out);
  or or_1 (s0, not_9_out, not_10_out, not_11_out, e0, e1, e3, e4);
  or or_2 (s1, and_1_out, and_2_out);
endmodule

module columna (
  input  [31:0] \input ,
  input  CLK,
  input  reset,
  output [31:0] \output 
);

  pixel pixel_1 (.CLK(CLK), .ENTRADA(\input [31]), .reset(reset), .SALIDA(\output [31]));
  pixel pixel_2 (.CLK(CLK), .ENTRADA(\input [30]), .reset(reset), .SALIDA(\output [30]));
  pixel pixel_3 (.CLK(CLK), .ENTRADA(\input [29]), .reset(reset), .SALIDA(\output [29]));
  pixel pixel_4 (.CLK(CLK), .ENTRADA(\input [28]), .reset(reset), .SALIDA(\output [28]));
  pixel pixel_5 (.CLK(CLK), .ENTRADA(\input [27]), .reset(reset), .SALIDA(\output [27]));
  pixel pixel_6 (.CLK(CLK), .ENTRADA(\input [26]), .reset(reset), .SALIDA(\output [26]));
  pixel pixel_7 (.CLK(CLK), .ENTRADA(\input [25]), .reset(reset), .SALIDA(\output [25]));
  pixel pixel_8 (.CLK(CLK), .ENTRADA(\input [24]), .reset(reset), .SALIDA(\output [24]));
  pixel pixel_9 (.CLK(CLK), .ENTRADA(\input [23]), .reset(reset), .SALIDA(\output [23]));
  pixel pixel_10 (.CLK(CLK), .ENTRADA(\input [22]), .reset(reset), .SALIDA(\output [22]));
  pixel pixel_11 (.CLK(CLK), .ENTRADA(\input [21]), .reset(reset), .SALIDA(\output [21]));
  pixel pixel_12 (.CLK(CLK), .ENTRADA(\input [20]), .reset(reset), .SALIDA(\output [20]));
  pixel pixel_13 (.CLK(CLK), .ENTRADA(\input [19]), .reset(reset), .SALIDA(\output [19]));
  pixel pixel_14 (.CLK(CLK), .ENTRADA(\input [18]), .reset(reset), .SALIDA(\output [18]));
  pixel pixel_15 (.CLK(CLK), .ENTRADA(\input [17]), .reset(reset), .SALIDA(\output [17]));
  pixel pixel_16 (.CLK(CLK), .ENTRADA(\input [16]), .reset(reset), .SALIDA(\output [16]));
  pixel pixel_17 (.CLK(CLK), .ENTRADA(\input [15]), .reset(reset), .SALIDA(\output [15]));
  pixel pixel_18 (.CLK(CLK), .ENTRADA(\input [14]), .reset(reset), .SALIDA(\output [14]));
  pixel pixel_19 (.CLK(CLK), .ENTRADA(\input [13]), .reset(reset), .SALIDA(\output [13]));
  pixel pixel_20 (.CLK(CLK), .ENTRADA(\input [12]), .reset(reset), .SALIDA(\output [12]));
  pixel pixel_21 (.CLK(CLK), .ENTRADA(\input [11]), .reset(reset), .SALIDA(\output [11]));
  pixel pixel_22 (.CLK(CLK), .ENTRADA(\input [10]), .reset(reset), .SALIDA(\output [10]));
  pixel pixel_23 (.CLK(CLK), .ENTRADA(\input [9]), .reset(reset), .SALIDA(\output [9]));
  pixel pixel_24 (.CLK(CLK), .ENTRADA(\input [8]), .reset(reset), .SALIDA(\output [8]));
  pixel pixel_25 (.CLK(CLK), .ENTRADA(\input [7]), .reset(reset), .SALIDA(\output [7]));
  pixel pixel_26 (.CLK(CLK), .ENTRADA(\input [6]), .reset(reset), .SALIDA(\output [6]));
  pixel pixel_27 (.CLK(CLK), .ENTRADA(\input [5]), .reset(reset), .SALIDA(\output [5]));
  pixel pixel_28 (.CLK(CLK), .ENTRADA(\input [4]), .reset(reset), .SALIDA(\output [4]));
  pixel pixel_29 (.CLK(CLK), .ENTRADA(\input [3]), .reset(reset), .SALIDA(\output [3]));
  pixel pixel_30 (.CLK(CLK), .ENTRADA(\input [2]), .reset(reset), .SALIDA(\output [2]));
  pixel pixel_31 (.CLK(CLK), .ENTRADA(\input [1]), .reset(reset), .SALIDA(\output [1]));
  pixel pixel_32 (.CLK(CLK), .ENTRADA(\input [0]), .reset(reset), .SALIDA(\output [0]));
endmodule

// pix
module pixel (
  input  CLK,
  input  ENTRADA,
  input  reset,
  output SALIDA
);

  wire or_1_out;

  or or_1 (or_1_out, SALIDA, ENTRADA);
  D_Flip_Flop d_ff_1 (.clk(CLK), .D(or_1_out), .Q(SALIDA), .reset(reset));  // open: Qn, preset, en
endmodule

module memoria (
  input  in_1,
  input  in_2,
  output [31:0] out_3,
  output [31:0] out_4,
  output [31:0] out_5,
  output [31:0] out_6,
  output [31:0] out_7,
  output [31:0] out_8,
  output [31:0] out_9,
  output [31:0] out_10,
  output [31:0] out_11,
  output [31:0] out_12,
  output [31:0] out_13,
  output [31:0] out_14,
  output [31:0] out_15,
  output [31:0] out_16,
  output [31:0] out_17,
  output [31:0] out_18
);

  wire [31:0] random_1_c1, random_1_c2, random_1_c3, random_1_c4, random_1_c5, random_1_c6, random_1_c7,
       random_1_c8, random_1_c9, random_1_c10, random_1_c11, random_1_c12, random_1_c13, random_1_c14,
       random_1_c15, random_1_c16;

  Random random_1 (
    .generar(in_1), .reset(in_2), .c1(random_1_c1), .c2(random_1_c2), .c3(random_1_c3), .c4(random_1_c4),
    .c5(random_1_c5), .c6(random_1_c6), .c7(random_1_c7), .c8(random_1_c8), .c9(random_1_c9),
    .c10(random_1_c10), .c11(random_1_c11), .c12(random_1_c12), .c13(random_1_c13), .c14(random_1_c14),
    .c15(random_1_c15), .c16(random_1_c16));
  columna columna_1 (.\input (random_1_c1), .CLK(in_1), .reset(in_2), .\output (out_3));
  columna columna_2 (.\input (random_1_c2), .CLK(in_1), .reset(in_2), .\output (out_4));
  columna columna_3 (.\input (random_1_c3), .CLK(in_1), .reset(in_2), .\output (out_5));
  columna columna_4 (.\input (random_1_c4), .CLK(in_1), .reset(in_2), .\output (out_6));
  columna columna_5 (.\input (random_1_c5), .CLK(in_1), .reset(in_2), .\output (out_7));
  columna columna_6 (.\input (random_1_c6), .CLK(in_1), .reset(in_2), .\output (out_8));
  columna columna_7 (.\input (random_1_c7), .CLK(in_1), .reset(in_2), .\output (out_9));
  columna columna_8 (.\input (random_1_c8), .CLK(in_1), .reset(in_2), .\output (out_10));
  columna columna_9 (.\input (random_1_c9), .CLK(in_1), .reset(in_2), .\output (out_11));
  columna columna_10 (.\input (random_1_c10), .CLK(in_1), .reset(in_2), .\output (out_12));
  columna columna_11 (.\input (random_1_c11), .CLK(in_1), .reset(in_2), .\output (out_13));
  columna columna_12 (.\input (random_1_c12), .CLK(in_1), .reset(in_2), .\output (out_14));
  columna columna_13 (.\input (random_1_c13), .CLK(in_1), .reset(in_2), .\output (out_15));
  columna columna_14 (.\input (random_1_c14), .CLK(in_1), .reset(in_2), .\output (out_16));
  columna columna_15 (.\input (random_1_c15), .CLK(in_1), .reset(in_2), .\output (out_17));
  columna columna_16 (.\input (random_1_c16), .CLK(in_1), .reset(in_2), .\output (out_18));
endmodule

module randomBarrera (
  input  [4:0] sup,
  input  [4:0] inf,
  input  click,
  input  activo,
  output [4:0] out_5
);

  wire [4:0] adder_1_out, divider_1_rem, random_1_out, subtractor_1_out;

  Random_part #(.width(5)) random_1 (.clk(click), .next(activo), .out(random_1_out));  // open: clr
  Adder #(.width(5)) adder_1 (.a(5'b00001), .b(subtractor_1_out), .out(adder_1_out));  // open: cin, cout
  Subtractor #(.width(5)) subtractor_1 (.a(sup), .b(inf), .out(subtractor_1_out));  // open: bin, bout
  Divider #(.width(5)) divider_1 (.a(random_1_out), .b(adder_1_out), .rem(divider_1_rem));  // open: out, upper
  Adder #(.width(5)) adder_2 (.a(divider_1_rem), .b(inf), .out(out_5));  // open: cin, cout
endmodule

module colisiones (
  input  [31:0] columna,
  input  [31:0] personaje,
  input  [31:0] peligro,
  output colision,
  output out_5,
  output destroy
);

  wire colision0, colision1, colision2, colision3, colision4, colision5, colision6, colision7, colision8,
       colision9, colision10, colision11, colision12, colision13, colision14, colision15, colision16,
       colision17, colision18, colision19, colision20, colision21, colision22, colision23, colision24,
       colision25, colision26, colision27, colision28, colision29, destroy0, destroy1, destroy2, destroy3,
       destroy4, destroy5, destroy6, destroy7, destroy8, destroy9, destroy10, destroy11, destroy12,
       destroy13, destroy14, destroy15, destroy16, destroy17, destroy18, destroy19, destroy20, destroy21,
       destroy22, destroy23, destroy24, destroy25, destroy26, destroy27, destroy28, destroy29, or_2_out;

  and and_1 (colision0, personaje[0], personaje[1], columna[2]);
  and and_2 (colision1, personaje[1], personaje[2], columna[3]);
  and and_3 (colision2, personaje[2], personaje[3], columna[4]);
  and and_4 (colision3, personaje[3], personaje[4], columna[5]);
  and and_5 (colision4, personaje[4], personaje[5], columna[6]);
  and and_6 (colision5, personaje[5], personaje[6], columna[7]);
  and and_7 (colision6, personaje[6], personaje[7], columna[8]);
  and and_8 (colision7, personaje[7], personaje[8], columna[9]);
  and and_9 (destroy0, personaje[0], personaje[1], peligro[2]);
  and and_10 (destroy1, personaje[1], personaje[2], peligro[3]);
  and and_11 (destroy2, personaje[2], personaje[3], peligro[4]);
  and and_12 (destroy3, personaje[3], personaje[4], peligro[5]);
  and and_13 (destroy4, personaje[4], personaje[5], peligro[6]);
  and and_14 (destroy5, personaje[5], personaje[6], peligro[7]);
  and and_15 (destroy6, personaje[6], personaje[7], peligro[8]);
  and and_16 (destroy7, personaje[7], personaje[8], peligro[9]);
  and and_17 (colision8, personaje[8], personaje[9], columna[10]);
  and and_18 (colision9, personaje[9], personaje[10], columna[11]);
  and and_19 (colision10, personaje[10], personaje[11], columna[12]);
  and and_20 (colision11, personaje[11], personaje[12], columna[13]);
  and and_21 (colision12, personaje[12], personaje[13], columna[14]);
  and and_22 (colision13, personaje[13], personaje[14], columna[15]);
  and and_23 (colision14, personaje[14], personaje[15], columna[16]);
  and and_24 (colision15, personaje[15], personaje[16], columna[17]);
  and and_25 (destroy8, personaje[8], personaje[9], peligro[10]);
  and and_26 (destroy9, personaje[9], personaje[10], peligro[11]);
  and and_27 (destroy10, personaje[10], personaje[11], peligro[12]);
  and and_28 (destroy11, personaje[11], personaje[12], peligro[13]);
  and and_29 (destroy12, personaje[12], personaje[13], peligro[14]);
  and and_30 (destroy13, personaje[13], personaje[14], peligro[15]);
  and and_31 (destroy14, personaje[14], personaje[15], peligro[16]);
  and and_32 (destroy15, personaje[15], personaje[16], peligro[17]);
  and and_33 (colision16, personaje[16], personaje[17], columna[18]);
  and and_34 (colision17, personaje[17], personaje[18], columna[19]);
  and and_35 (colision18, personaje[18], personaje[19], columna[20]);
  and and_36 (colision19, personaje[19], personaje[20], columna[21]);
  and and_37 (colision20, personaje[20], personaje[21], columna[22]);
  and and_38 (colision21, personaje[21], personaje[22], columna[23]);
  and and_39 (colision22, personaje[22], personaje[23], columna[24]);
  and and_40 (colision23, personaje[23], personaje[24], columna[25]);
  and and_41 (destroy16, personaje[16], personaje[17], peligro[18]);
  and and_42 (destroy17, personaje[17], personaje[18], peligro[19]);
  and and_43 (destroy18, personaje[18], personaje[19], peligro[20]);
  and and_44 (destroy19, personaje[19], personaje[20], peligro[21]);
  and and_45 (destroy20, personaje[20], personaje[21], peligro[22]);
  and and_46 (destroy21, personaje[21], personaje[22], peligro[23]);
  and and_47 (destroy22, personaje[22], personaje[23], peligro[24]);
  and and_48 (destroy23, personaje[23], personaje[24], peligro[25]);
  and and_49 (colision24, personaje[24], personaje[25], columna[26]);
  and and_50 (colision25, personaje[25], personaje[26], columna[27]);
  and and_51 (colision26, personaje[26], personaje[27], columna[28]);
  and and_52 (colision27, personaje[27], personaje[28], columna[29]);
  and and_53 (colision28, personaje[28], personaje[29], columna[30]);
  and and_54 (colision29, personaje[29], personaje[30], columna[31]);
  and and_55 (destroy24, personaje[24], personaje[25], peligro[26]);
  and and_56 (destroy25, personaje[25], personaje[26], peligro[27]);
  and and_57 (destroy26, personaje[26], personaje[27], peligro[28]);
  and and_58 (destroy27, personaje[27], personaje[28], peligro[29]);
  and and_59 (destroy28, personaje[28], personaje[29], peligro[30]);
  and and_60 (destroy29, personaje[29], personaje[30], peligro[31]);
  or or_1 (colision, colision0, colision8, colision1, colision9, colision2, colision10, colision3, colision11, colision4, colision12, colision5, colision13, colision6, colision14, colision7, colision15, colision16, colision24, colision17, colision25, colision18, colision26, colision19, colision27, colision20, colision28, colision21, colision29, colision22, colision23);
  or or_2 (or_2_out, destroy0, destroy8, destroy1, destroy9, destroy2, destroy10, destroy3, destroy11, destroy4, destroy12, destroy5, destroy13, destroy6, destroy14, destroy7, destroy15, destroy16, destroy24, destroy17, destroy25, destroy18, destroy26, destroy19, destroy27, destroy20, destroy28, destroy21, destroy29, destroy22, destroy23);
  and and_61 (destroy, or_2_out, colision);

  assign out_5 = personaje[31];

  // Other names for the same wires on the sheet: r0 = columna[0]; r1 = columna[1]; r2 = columna[2]; r3 = columna[3];
  //   r4 = columna[4]; r5 = columna[5]; r6 = columna[6]; r7 = columna[7]; r8 = columna[8]; r9 = columna[9];
  //   r10 = columna[10]; r11 = columna[11]; r12 = columna[12]; r13 = columna[13]; r14 = columna[14];
  //   r15 = columna[15]; r16 = columna[16]; r17 = columna[17]; r18 = columna[18]; r19 = columna[19];
  //   r20 = columna[20]; r21 = columna[21]; r22 = columna[22]; r23 = columna[23]; r24 = columna[24];
  //   r25 = columna[25]; r26 = columna[26]; r27 = columna[27]; r28 = columna[28]; r29 = columna[29];
  //   r30 = columna[30]; r31 = columna[31]; p0 = peligro[0]; p1 = peligro[1]; p2 = peligro[2]; p3 = peligro[3];
  //   p4 = peligro[4]; p5 = peligro[5]; p6 = peligro[6]; p7 = peligro[7]; p8 = peligro[8]; p9 = peligro[9];
  //   p10 = peligro[10]; p11 = peligro[11]; p12 = peligro[12]; p13 = peligro[13]; p14 = peligro[14];
  //   p15 = peligro[15]; p16 = peligro[16]; p17 = peligro[17]; p18 = peligro[18]; p19 = peligro[19];
  //   p20 = peligro[20]; p21 = peligro[21]; p22 = peligro[22]; p23 = peligro[23]; p24 = peligro[24];
  //   p25 = peligro[25]; p26 = peligro[26]; p27 = peligro[27]; p28 = peligro[28]; p29 = peligro[29];
  //   p30 = peligro[30]; p31 = peligro[31]; c0 = personaje[0]; c1 = personaje[1]; c2 = personaje[2];
  //   c3 = personaje[3]; c4 = personaje[4]; c5 = personaje[5]; c6 = personaje[6]; c7 = personaje[7];
  //   c8 = personaje[8]; c9 = personaje[9]; c10 = personaje[10]; c11 = personaje[11]; c12 = personaje[12];
  //   c13 = personaje[13]; c14 = personaje[14]; c15 = personaje[15]; c16 = personaje[16]; c17 = personaje[17];
  //   c18 = personaje[18]; c19 = personaje[19]; c20 = personaje[20]; c21 = personaje[21]; c22 = personaje[22];
  //   c23 = personaje[23]; c24 = personaje[24]; c25 = personaje[25]; c26 = personaje[26]; c27 = personaje[27];
  //   c28 = personaje[28]; c29 = personaje[29]; c30 = personaje[30]; c31 = personaje[31]
endmodule

module contador (
  input  diez_en_diez,
  input  generar,
  input  in_3,
  output [3:0] decenas,
  output [3:0] unidades
);

  wire comparator_2_eq, comparator_3_eq;
  wire [7:0] adder_1_out, adder_2_out, multiplexer_1_out, register_1_q;
  wire [7:4] divider_1_out, divider_1_rem;

  Adder adder_1 (.a(register_1_q), .b(8'h1), .out(adder_1_out));  // open: cin, cout
  Adder adder_2 (.a(8'ha), .b(register_1_q), .out(adder_2_out));  // open: cin, cout
  Multiplexer #(.width(8)) multiplexer_1 (
    .in0(adder_1_out), .in1(adder_2_out), .out(multiplexer_1_out), .sel(diez_en_diez), .en(1'b1));
  Register register_1 (.D(multiplexer_1_out), .Q(register_1_q), .clk(generar));  // open: en, clr
  Divider divider_1 (
    .a(register_1_q), .b(8'ha), .out({divider_1_out, decenas}), .rem({divider_1_rem, unidades}));  // open: upper
  Comparator comparator_1 (.a(register_1_q), .b(8'h63));  // open: gt, eq, lt
  Comparator #(.width(4)) comparator_2 (.a(unidades), .b(4'b1001), .eq(comparator_2_eq));  // open: gt, lt
  Comparator #(.width(4)) comparator_3 (.a(decenas), .b(4'b1001), .eq(comparator_3_eq));  // open: gt, lt
  and and_1 (in_3, comparator_2_eq, comparator_3_eq);
endmodule
// barerasmalas
module barrera_peligrosa (
  input  [31:0] in_1,
  input  [31:0] in_2,
  output out_3
);

  wire a1, a2, a3, a4, a5, a6, a7, a8, a9, a10, a11, a12, a13, a14, a15, a16, a17, a18, a19, a20, a21, a22,
       a23, a24, a25, a26, a27, a28, a29, a30, a31, a32;

  and and_1 (a1, in_1[0], in_2[0]);
  and and_2 (a2, in_1[1], in_2[1]);
  and and_3 (a3, in_1[2], in_2[2]);
  and and_4 (a4, in_1[3], in_2[3]);
  and and_5 (a5, in_1[4], in_2[4]);
  and and_6 (a6, in_1[5], in_2[5]);
  and and_7 (a7, in_1[6], in_2[6]);
  and and_8 (a8, in_1[7], in_2[7]);
  and and_9 (a9, in_1[8], in_2[8]);
  and and_10 (a10, in_1[9], in_2[9]);
  and and_11 (a11, in_1[10], in_2[10]);
  and and_12 (a12, in_1[11], in_2[11]);
  and and_13 (a13, in_1[12], in_2[12]);
  and and_14 (a14, in_1[13], in_2[13]);
  and and_15 (a15, in_1[14], in_2[14]);
  and and_16 (a16, in_1[15], in_2[15]);
  and and_17 (a17, in_1[16], in_2[16]);
  and and_18 (a18, in_1[17], in_2[17]);
  and and_19 (a19, in_1[18], in_2[18]);
  and and_20 (a20, in_1[19], in_2[19]);
  and and_21 (a21, in_1[20], in_2[20]);
  and and_22 (a22, in_1[21], in_2[21]);
  and and_23 (a23, in_1[22], in_2[22]);
  and and_24 (a24, in_1[23], in_2[23]);
  and and_25 (a25, in_1[24], in_2[24]);
  and and_26 (a26, in_1[25], in_2[25]);
  and and_27 (a27, in_1[26], in_2[26]);
  and and_28 (a28, in_1[27], in_2[27]);
  and and_29 (a29, in_1[28], in_2[28]);
  and and_30 (a32, in_1[31], in_2[31]);
  and and_31 (a31, in_1[30], in_2[30]);
  and and_32 (a30, in_1[29], in_2[29]);
  or or_1 (out_3, a1, a2, a3, a4, a5, a6, a7, a8, a9, a10, a11, a12, a13, a14, a15, a16, a17, a18, a19, a20, a21, a22, a23, a24, a25, a26, a27, a28, a29, a30, a31, a32);

  // Other names for the same wires on the sheet: _01 = in_1[0]; _02 = in_1[1]; _03 = in_1[2]; _04 = in_1[3];
  //   _05 = in_1[4]; _06 = in_1[5]; _07 = in_1[6]; _08 = in_1[7]; _09 = in_1[8]; _010 = in_1[9]; _011 = in_1[10];
  //   _012 = in_1[11]; _013 = in_1[12]; _014 = in_1[13]; _015 = in_1[14]; _016 = in_1[15]; _017 = in_1[16];
  //   _018 = in_1[17]; _019 = in_1[18]; _020 = in_1[19]; _021 = in_1[20]; _022 = in_1[21]; _023 = in_1[22];
  //   _024 = in_1[23]; _025 = in_1[24]; _026 = in_1[25]; _027 = in_1[26]; _028 = in_1[27]; _029 = in_1[28];
  //   _030 = in_1[29]; _031 = in_1[30]; _032 = in_1[31]; _1 = in_2[0]; _2 = in_2[1]; _3 = in_2[2]; _4 = in_2[3];
  //   _5 = in_2[4]; _6 = in_2[5]; _7 = in_2[6]; _8 = in_2[7]; _9 = in_2[8]; _10 = in_2[9]; _11 = in_2[10];
  //   _12 = in_2[11]; _13 = in_2[12]; _14 = in_2[13]; _15 = in_2[14]; _16 = in_2[15]; _17 = in_2[16]; _18 = in_2[17];
  //   _19 = in_2[18]; _20 = in_2[19]; _21 = in_2[20]; _22 = in_2[21]; _23 = in_2[22]; _24 = in_2[23]; _25 = in_2[24];
  //   _26 = in_2[25]; _27 = in_2[26]; _28 = in_2[27]; _29 = in_2[28]; _30 = in_2[29]; _31 = in_2[30]; _32 = in_2[31]
endmodule
